// Logisim project DISPLAY.circ as structural Verilog: 3 circuits, main circuit main
module main (
  input  CLK,
  input  CLR,
  input  WRITE_BUFFER,
  input  FLUSH_BUFFER,
  input  [4:0] in_5,
  input  [15:0] in_6,
  input  in_7
);

  wire CLK_t;
  wire [15:0] n32_x_16b_buffer_1_r0_3, n32_x_16b_buffer_1_r0_4, n32_x_16b_buffer_1_r1_3,
       n32_x_16b_buffer_1_r1_4, n32_x_16b_buffer_1_r2_3, n32_x_16b_buffer_1_r2_4, n32_x_16b_buffer_1_r3_3,
       n32_x_16b_buffer_1_r3_4, n32_x_16b_buffer_1_r4_3, n32_x_16b_buffer_1_r4_4, n32_x_16b_buffer_1_r5_3,
       n32_x_16b_buffer_1_r5_4, n32_x_16b_buffer_1_r6_3, n32_x_16b_buffer_1_r6_4, n32_x_16b_buffer_1_r7_3,
       n32_x_16b_buffer_1_r7_4, n32_x_16b_buffer_1_r8_3, n32_x_16b_buffer_1_r8_4, n32_x_16b_buffer_1_r9_3,
       n32_x_16b_buffer_1_r9_4, n32_x_16b_buffer_1_r10_3, n32_x_16b_buffer_1_r10_4, n32_x_16b_buffer_1_r11_3,
       n32_x_16b_buffer_1_r11_4, n32_x_16b_buffer_1_r12_3, n32_x_16b_buffer_1_r12_4,
       n32_x_16b_buffer_1_r13_3, n32_x_16b_buffer_1_r13_4, n32_x_16b_buffer_1_r14_3,
       n32_x_16b_buffer_1_r14_4, n32_x_16b_buffer_1_r15_3, n32_x_16b_buffer_1_r15_4, n32_x_16b_register_1_r0,
       n32_x_16b_register_1_r0_2, n32_x_16b_register_1_r1, n32_x_16b_register_1_r1_2,
       n32_x_16b_register_1_r2, n32_x_16b_register_1_r2_2, n32_x_16b_register_1_r3,
       n32_x_16b_register_1_r3_2, n32_x_16b_register_1_r4, n32_x_16b_register_1_r4_2,
       n32_x_16b_register_1_r5, n32_x_16b_register_1_r5_2, n32_x_16b_register_1_r6,
       n32_x_16b_register_1_r6_2, n32_x_16b_register_1_r7, n32_x_16b_register_1_r7_2,
       n32_x_16b_register_1_r8, n32_x_16b_register_1_r8_2, n32_x_16b_register_1_r9,
       n32_x_16b_register_1_r9_2, n32_x_16b_register_1_r10, n32_x_16b_register_1_r10_2,
       n32_x_16b_register_1_r11, n32_x_16b_register_1_r11_2, n32_x_16b_register_1_r12,
       n32_x_16b_register_1_r12_2, n32_x_16b_register_1_r13, n32_x_16b_register_1_r13_2,
       n32_x_16b_register_1_r14, n32_x_16b_register_1_r14_2, n32_x_16b_register_1_r15,
       n32_x_16b_register_1_r15_2;

  Clock clock_1 (.out(CLK_t));
  _32_x_16b_REGISTER u_32_x_16b_register_1 (
    .CLK(CLK_t), .CLR(CLR), .FLUSH(in_7), .R0(n32_x_16b_register_1_r0), .R1(n32_x_16b_register_1_r1),
    .R2(n32_x_16b_register_1_r2), .R3(n32_x_16b_register_1_r3), .R4(n32_x_16b_register_1_r4),
    .R5(n32_x_16b_register_1_r5), .R6(n32_x_16b_register_1_r6), .R7(n32_x_16b_register_1_r7),
    .R8(n32_x_16b_register_1_r8), .R9(n32_x_16b_register_1_r9), .R10(n32_x_16b_register_1_r10),
    .R11(n32_x_16b_register_1_r11), .R12(n32_x_16b_register_1_r12), .R13(n32_x_16b_register_1_r13),
    .R14(n32_x_16b_register_1_r14), .R15(n32_x_16b_register_1_r15), .R0_2(n32_x_16b_register_1_r0_2),
    .R1_2(n32_x_16b_register_1_r1_2), .R2_2(n32_x_16b_register_1_r2_2), .R3_2(n32_x_16b_register_1_r3_2),
    .R4_2(n32_x_16b_register_1_r4_2), .R5_2(n32_x_16b_register_1_r5_2), .R6_2(n32_x_16b_register_1_r6_2),
    .R7_2(n32_x_16b_register_1_r7_2), .R8_2(n32_x_16b_register_1_r8_2), .R9_2(n32_x_16b_register_1_r9_2),
    .R10_2(n32_x_16b_register_1_r10_2), .R11_2(n32_x_16b_register_1_r11_2),
    .R12_2(n32_x_16b_register_1_r12_2), .R13_2(n32_x_16b_register_1_r13_2),
    .R14_2(n32_x_16b_register_1_r14_2), .R15_2(n32_x_16b_register_1_r15_2), .ADDR(in_5), .WRITE_DATA(in_6));
  DotMatrix #(.matrixcols(32), .matrixrows(16)) dotmatrix_1 (
    .col0(n32_x_16b_buffer_1_r0_3), .col1(n32_x_16b_buffer_1_r1_3), .col2(n32_x_16b_buffer_1_r2_3),
    .col3(n32_x_16b_buffer_1_r3_3), .col4(n32_x_16b_buffer_1_r4_3), .col5(n32_x_16b_buffer_1_r5_3),
    .col6(n32_x_16b_buffer_1_r6_3), .col7(n32_x_16b_buffer_1_r7_3), .col8(n32_x_16b_buffer_1_r8_3),
    .col9(n32_x_16b_buffer_1_r9_3), .col10(n32_x_16b_buffer_1_r10_3), .col11(n32_x_16b_buffer_1_r11_3),
    .col12(n32_x_16b_buffer_1_r12_3), .col13(n32_x_16b_buffer_1_r13_3), .col14(n32_x_16b_buffer_1_r14_3),
    .col15(n32_x_16b_buffer_1_r15_3), .col16(n32_x_16b_buffer_1_r0_4), .col17(n32_x_16b_buffer_1_r1_4),
    .col18(n32_x_16b_buffer_1_r2_4), .col19(n32_x_16b_buffer_1_r3_4), .col20(n32_x_16b_buffer_1_r4_4),
    .col21(n32_x_16b_buffer_1_r5_4), .col22(n32_x_16b_buffer_1_r6_4), .col23(n32_x_16b_buffer_1_r7_4),
    .col24(n32_x_16b_buffer_1_r8_4), .col25(n32_x_16b_buffer_1_r9_4), .col26(n32_x_16b_buffer_1_r10_4),
    .col27(n32_x_16b_buffer_1_r11_4), .col28(n32_x_16b_buffer_1_r12_4), .col29(n32_x_16b_buffer_1_r13_4),
    .col30(n32_x_16b_buffer_1_r14_4), .col31(n32_x_16b_buffer_1_r15_4));
  _32_x_16b_BUFFER u_32_x_16b_buffer_1 (
    .CLK(CLK_t), .CLR(CLR), .FLUSH(FLUSH_BUFFER), .R0(n32_x_16b_register_1_r0), .R1(n32_x_16b_register_1_r1),
    .R2(n32_x_16b_register_1_r2), .R3(n32_x_16b_register_1_r3), .R4(n32_x_16b_register_1_r4),
    .R5(n32_x_16b_register_1_r5), .R6(n32_x_16b_register_1_r6), .R7(n32_x_16b_register_1_r7),
    .R8(n32_x_16b_register_1_r8), .R9(n32_x_16b_register_1_r9), .R10(n32_x_16b_register_1_r10),
    .R11(n32_x_16b_register_1_r11), .R12(n32_x_16b_register_1_r12), .R13(n32_x_16b_register_1_r13),
    .R14(n32_x_16b_register_1_r14), .R15(n32_x_16b_register_1_r15), .R0_2(n32_x_16b_register_1_r0_2),
    .R1_2(n32_x_16b_register_1_r1_2), .R2_2(n32_x_16b_register_1_r2_2), .R3_2(n32_x_16b_register_1_r3_2),
    .R4_2(n32_x_16b_register_1_r4_2), .R5_2(n32_x_16b_register_1_r5_2), .R6_2(n32_x_16b_register_1_r6_2),
    .R7_2(n32_x_16b_register_1_r7_2), .R8_2(n32_x_16b_register_1_r8_2), .R9_2(n32_x_16b_register_1_r9_2),
    .R10_2(n32_x_16b_register_1_r10_2), .R11_2(n32_x_16b_register_1_r11_2),
    .R12_2(n32_x_16b_register_1_r12_2), .R13_2(n32_x_16b_register_1_r13_2),
    .R14_2(n32_x_16b_register_1_r14_2), .R15_2(n32_x_16b_register_1_r15_2), .R0_3(n32_x_16b_buffer_1_r0_3),
    .R1_3(n32_x_16b_buffer_1_r1_3), .R2_3(n32_x_16b_buffer_1_r2_3), .R3_3(n32_x_16b_buffer_1_r3_3),
    .R4_3(n32_x_16b_buffer_1_r4_3), .R5_3(n32_x_16b_buffer_1_r5_3), .R6_3(n32_x_16b_buffer_1_r6_3),
    .R7_3(n32_x_16b_buffer_1_r7_3), .R8_3(n32_x_16b_buffer_1_r8_3), .R9_3(n32_x_16b_buffer_1_r9_3),
    .R10_3(n32_x_16b_buffer_1_r10_3), .R11_3(n32_x_16b_buffer_1_r11_3), .R12_3(n32_x_16b_buffer_1_r12_3),
    .R13_3(n32_x_16b_buffer_1_r13_3), .R14_3(n32_x_16b_buffer_1_r14_3), .R15_3(n32_x_16b_buffer_1_r15_3),
    .R0_4(n32_x_16b_buffer_1_r0_4), .R1_4(n32_x_16b_buffer_1_r1_4), .R2_4(n32_x_16b_buffer_1_r2_4),
    .R3_4(n32_x_16b_buffer_1_r3_4), .R4_4(n32_x_16b_buffer_1_r4_4), .R5_4(n32_x_16b_buffer_1_r5_4),
    .R6_4(n32_x_16b_buffer_1_r6_4), .R7_4(n32_x_16b_buffer_1_r7_4), .R8_4(n32_x_16b_buffer_1_r8_4),
    .R9_4(n32_x_16b_buffer_1_r9_4), .R10_4(n32_x_16b_buffer_1_r10_4), .R11_4(n32_x_16b_buffer_1_r11_4),
    .R12_4(n32_x_16b_buffer_1_r12_4), .R13_4(n32_x_16b_buffer_1_r13_4), .R14_4(n32_x_16b_buffer_1_r14_4),
    .R15_4(n32_x_16b_buffer_1_r15_4));
endmodule

module _32_x_16b_REGISTER (
  input  CLK,
  input  CLR,
  input  FLUSH,
  input  [4:0] ADDR,
  input  [15:0] WRITE_DATA,
  output [15:0] R0,
  output [15:0] R1,
  output [15:0] R2,
  output [15:0] R3,
  output [15:0] R4,
  output [15:0] R5,
  output [15:0] R6,
  output [15:0] R7,
  output [15:0] R8,
  output [15:0] R9,
  output [15:0] R10,
  output [15:0] R11,
  output [15:0] R12,
  output [15:0] R13,
  output [15:0] R14,
  output [15:0] R15,
  output [15:0] R0_2,
  output [15:0] R1_2,
  output [15:0] R2_2,
  output [15:0] R3_2,
  output [15:0] R4_2,
  output [15:0] R5_2,
  output [15:0] R6_2,
  output [15:0] R7_2,
  output [15:0] R8_2,
  output [15:0] R9_2,
  output [15:0] R10_2,
  output [15:0] R11_2,
  output [15:0] R12_2,
  output [15:0] R13_2,
  output [15:0] R14_2,
  output [15:0] R15_2
);

  wire demultiplexer_1_out0, demultiplexer_1_out1, demultiplexer_1_out2, demultiplexer_1_out3,
       demultiplexer_1_out4, demultiplexer_1_out5, demultiplexer_1_out6, demultiplexer_1_out7,
       demultiplexer_1_out8, demultiplexer_1_out9, demultiplexer_1_out10, demultiplexer_1_out11,
       demultiplexer_1_out12, demultiplexer_1_out13, demultiplexer_1_out14, demultiplexer_1_out15,
       demultiplexer_1_out16, demultiplexer_1_out17, demultiplexer_1_out18, demultiplexer_1_out19,
       demultiplexer_1_out20, demultiplexer_1_out21, demultiplexer_1_out22, demultiplexer_1_out23,
       demultiplexer_1_out24, demultiplexer_1_out25, demultiplexer_1_out26, demultiplexer_1_out27,
       demultiplexer_1_out28, demultiplexer_1_out29, demultiplexer_1_out30, demultiplexer_1_out31;

  Demultiplexer #(.select(5), .enable("false")) demultiplexer_1 (
    .out0(demultiplexer_1_out0), .out1(demultiplexer_1_out1), .out2(demultiplexer_1_out2),
    .out3(demultiplexer_1_out3), .out4(demultiplexer_1_out4), .out5(demultiplexer_1_out5),
    .out6(demultiplexer_1_out6), .out7(demultiplexer_1_out7), .out8(demultiplexer_1_out8),
    .out9(demultiplexer_1_out9), .out10(demultiplexer_1_out10), .out11(demultiplexer_1_out11),
    .out12(demultiplexer_1_out12), .out13(demultiplexer_1_out13), .out14(demultiplexer_1_out14),
    .out15(demultiplexer_1_out15), .out16(demultiplexer_1_out16), .out17(demultiplexer_1_out17),
    .out18(demultiplexer_1_out18), .out19(demultiplexer_1_out19), .out20(demultiplexer_1_out20),
    .out21(demultiplexer_1_out21), .out22(demultiplexer_1_out22), .out23(demultiplexer_1_out23),
    .out24(demultiplexer_1_out24), .out25(demultiplexer_1_out25), .out26(demultiplexer_1_out26),
    .out27(demultiplexer_1_out27), .out28(demultiplexer_1_out28), .out29(demultiplexer_1_out29),
    .out30(demultiplexer_1_out30), .out31(demultiplexer_1_out31), .in(FLUSH), .sel(ADDR));
  Register #(.width(16)) register_1 (.D(WRITE_DATA), .en(demultiplexer_1_out1), .Q(R1), .clk(CLK), .clr(CLR));
  Register #(.width(16)) register_2 (.D(WRITE_DATA), .en(demultiplexer_1_out3), .Q(R3), .clk(CLK), .clr(CLR));
  Register #(.width(16)) register_3 (.D(WRITE_DATA), .en(demultiplexer_1_out5), .Q(R5), .clk(CLK), .clr(CLR));
  Register #(.width(16)) register_4 (.D(WRITE_DATA), .en(demultiplexer_1_out7), .Q(R7), .clk(CLK), .clr(CLR));
  Register #(.width(16)) register_5 (.D(WRITE_DATA), .en(demultiplexer_1_out9), .Q(R9), .clk(CLK), .clr(CLR));
  Register #(.width(16)) register_6 (.D(WRITE_DATA), .en(demultiplexer_1_out11), .Q(R11), .clk(CLK), .clr(CLR));
  Register #(.width(16)) register_7 (.D(WRITE_DATA), .en(demultiplexer_1_out13), .Q(R13), .clk(CLK), .clr(CLR));
  Register #(.width(16)) register_8 (.D(WRITE_DATA), .en(demultiplexer_1_out15), .Q(R15), .clk(CLK), .clr(CLR));
  Register #(.width(16)) register_9 (.D(WRITE_DATA), .en(demultiplexer_1_out17), .Q(R1_2), .clk(CLK), .clr(CLR));
  Register #(.width(16)) register_10 (.D(WRITE_DATA), .en(demultiplexer_1_out19), .Q(R3_2), .clk(CLK), .clr(CLR));
  Register #(.width(16)) register_11 (.D(WRITE_DATA), .en(demultiplexer_1_out21), .Q(R5_2), .clk(CLK), .clr(CLR));
  Register #(.width(16)) register_12 (.D(WRITE_DATA), .en(demultiplexer_1_out23), .Q(R7_2), .clk(CLK), .clr(CLR));
  Register #(.width(16)) register_13 (.D(WRITE_DATA), .en(demultiplexer_1_out25), .Q(R9_2), .clk(CLK), .clr(CLR));
  Register #(.width(16)) register_14 (.D(WRITE_DATA), .en(demultiplexer_1_out27), .Q(R11_2), .clk(CLK), .clr(CLR));
  Register #(.width(16)) register_15 (.D(WRITE_DATA), .en(demultiplexer_1_out29), .Q(R13_2), .clk(CLK), .clr(CLR));
  Register #(.width(16)) register_16 (.D(WRITE_DATA), .en(demultiplexer_1_out31), .Q(R15_2), .clk(CLK), .clr(CLR));
  Register #(.width(16)) register_17 (.D(WRITE_DATA), .en(demultiplexer_1_out0), .Q(R0), .clk(CLK), .clr(CLR));
  Register #(.width(16)) register_18 (.D(WRITE_DATA), .en(demultiplexer_1_out2), .Q(R2), .clk(CLK), .clr(CLR));
  Register #(.width(16)) register_19 (.D(WRITE_DATA), .en(demultiplexer_1_out4), .Q(R4), .clk(CLK), .clr(CLR));
  Register #(.width(16)) register_20 (.D(WRITE_DATA), .en(demultiplexer_1_out6), .Q(R6), .clk(CLK), .clr(CLR));
  Register #(.width(16)) register_21 (.D(WRITE_DATA), .en(demultiplexer_1_out8), .Q(R8), .clk(CLK), .clr(CLR));
  Register #(.width(16)) register_22 (.D(WRITE_DATA), .en(demultiplexer_1_out10), .Q(R10), .clk(CLK), .clr(CLR));
  Register #(.width(16)) register_23 (.D(WRITE_DATA), .en(demultiplexer_1_out12), .Q(R12), .clk(CLK), .clr(CLR));
  Register #(.width(16)) register_24 (.D(WRITE_DATA), .en(demultiplexer_1_out14), .Q(R14), .clk(CLK), .clr(CLR));
  Register #(.width(16)) register_25 (.D(WRITE_DATA), .en(demultiplexer_1_out16), .Q(R0_2), .clk(CLK), .clr(CLR));
  Register #(.width(16)) register_26 (.D(WRITE_DATA), .en(demultiplexer_1_out18), .Q(R2_2), .clk(CLK), .clr(CLR));
  Register #(.width(16)) register_27 (.D(WRITE_DATA), .en(demultiplexer_1_out20), .Q(R4_2), .clk(CLK), .clr(CLR));
  Register #(.width(16)) register_28 (.D(WRITE_DATA), .en(demultiplexer_1_out22), .Q(R6_2), .clk(CLK), .clr(CLR));
  Register #(.width(16)) register_29 (.D(WRITE_DATA), .en(demultiplexer_1_out24), .Q(R8_2), .clk(CLK), .clr(CLR));
  Register #(.width(16)) register_30 (.D(WRITE_DATA), .en(demultiplexer_1_out26), .Q(R10_2), .clk(CLK), .clr(CLR));
  Register #(.width(16)) register_31 (.D(WRITE_DATA), .en(demultiplexer_1_out28), .Q(R12_2), .clk(CLK), .clr(CLR));
  Register #(.width(16)) register_32 (.D(WRITE_DATA), .en(demultiplexer_1_out30), .Q(R14_2), .clk(CLK), .clr(CLR));

  // Other names for the same wires on the sheet: WD[15:0] = WRITE_DATA; WRITE = FLUSH
endmodule

module _32_x_16b_BUFFER (
  input  CLK,
  input  CLR,
  input  FLUSH,
  input  [15:0] R0,
  input  [15:0] R1,
  input  [15:0] R2,
  input  [15:0] R3,
  input  [15:0] R4,
  input  [15:0] R5,
  input  [15:0] R6,
  input  [15:0] R7,
  input  [15:0] R8,
  input  [15:0] R9,
  input  [15:0] R10,
  input  [15:0] R11,
  input  [15:0] R12,
  input  [15:0] R13,
  input  [15:0] R14,
  input  [15:0] R15,
  input  [15:0] R0_2,
  input  [15:0] R1_2,
  input  [15:0] R2_2,
  input  [15:0] R3_2,
  input  [15:0] R4_2,
  input  [15:0] R5_2,
  input  [15:0] R6_2,
  input  [15:0] R7_2,
  input  [15:0] R8_2,
  input  [15:0] R9_2,
  input  [15:0] R10_2,
  input  [15:0] R11_2,
  input  [15:0] R12_2,
  input  [15:0] R13_2,
  input  [15:0] R14_2,
  input  [15:0] R15_2,
  output [15:0] R0_3,
  output [15:0] R1_3,
  output [15:0] R2_3,
  output [15:0] R3_3,
  output [15:0] R4_3,
  output [15:0] R5_3,
  output [15:0] R6_3,
  output [15:0] R7_3,
  output [15:0] R8_3,
  output [15:0] R9_3,
  output [15:0] R10_3,
  output [15:0] R11_3,
  output [15:0] R12_3,
  output [15:0] R13_3,
  output [15:0] R14_3,
  output [15:0] R15_3,
  output [15:0] R0_4,
  output [15:0] R1_4,
  output [15:0] R2_4,
  output [15:0] R3_4,
  output [15:0] R4_4,
  output [15:0] R5_4,
  output [15:0] R6_4,
  output [15:0] R7_4,
  output [15:0] R8_4,
  output [15:0] R9_4,
  output [15:0] R10_4,
  output [15:0] R11_4,
  output [15:0] R12_4,
  output [15:0] R13_4,
  output [15:0] R14_4,
  output [15:0] R15_4
);

  Register #(.width(16)) register_1 (.D(R1), .en(FLUSH), .Q(R1_3), .clk(CLK), .clr(CLR));
  Register #(.width(16)) register_2 (.D(R3), .en(FLUSH), .Q(R3_3), .clk(CLK), .clr(CLR));
  Register #(.width(16)) register_3 (.D(R5), .en(FLUSH), .Q(R5_3), .clk(CLK), .clr(CLR));
  Register #(.width(16)) register_4 (.D(R7), .en(FLUSH), .Q(R7_3), .clk(CLK), .clr(CLR));
  Register #(.width(16)) register_5 (.D(R9), .en(FLUSH), .Q(R9_3), .clk(CLK), .clr(CLR));
  Register #(.width(16)) register_6 (.D(R11), .en(FLUSH), .Q(R11_3), .clk(CLK), .clr(CLR));
  Register #(.width(16)) register_7 (.D(R13), .en(FLUSH), .Q(R13_3), .clk(CLK), .clr(CLR));
  Register #(.width(16)) register_8 (.D(R15), .en(FLUSH), .Q(R15_3), .clk(CLK), .clr(CLR));
  Register #(.width(16)) register_9 (.D(R1_2), .en(FLUSH), .Q(R1_4), .clk(CLK), .clr(CLR));
  Register #(.width(16)) register_10 (.D(R3_2), .en(FLUSH), .Q(R3_4), .clk(CLK), .clr(CLR));
  Register #(.width(16)) register_11 (.D(R5_2), .en(FLUSH), .Q(R5_4), .clk(CLK), .clr(CLR));
  Register #(.width(16)) register_12 (.D(R7_2), .en(FLUSH), .Q(R7_4), .clk(CLK), .clr(CLR));
  Register #(.width(16)) register_13 (.D(R9_2), .en(FLUSH), .Q(R9_4), .clk(CLK), .clr(CLR));
  Register #(.width(16)) register_14 (.D(R11_2), .en(FLUSH), .Q(R11_4), .clk(CLK), .clr(CLR));
  Register #(.width(16)) register_15 (.D(R13_2), .en(FLUSH), .Q(R13_4), .clk(CLK), .clr(CLR));
  Register #(.width(16)) register_16 (.D(R15_2), .en(FLUSH), .Q(R15_4), .clk(CLK), .clr(CLR));
  Register #(.width(16)) register_17 (.D(R0), .en(FLUSH), .Q(R0_3), .clk(CLK), .clr(CLR));
  Register #(.width(16)) register_18 (.D(R2), .en(FLUSH), .Q(R2_3), .clk(CLK), .clr(CLR));
  Register #(.width(16)) register_19 (.D(R4), .en(FLUSH), .Q(R4_3), .clk(CLK), .clr(CLR));
  Register #(.width(16)) register_20 (.D(R6), .en(FLUSH), .Q(R6_3), .clk(CLK), .clr(CLR));
  Register #(.width(16)) register_21 (.D(R8), .en(FLUSH), .Q(R8_3), .clk(CLK), .clr(CLR));
  Register #(.width(16)) register_22 (.D(R10), .en(FLUSH), .Q(R10_3), .clk(CLK), .clr(CLR));
  Register #(.width(16)) register_23 (.D(R12), .en(FLUSH), .Q(R12_3), .clk(CLK), .clr(CLR));
  Register #(.width(16)) register_24 (.D(R14), .en(FLUSH), .Q(R14_3), .clk(CLK), .clr(CLR));
  Register #(.width(16)) register_25 (.D(R0_2), .en(FLUSH), .Q(R0_4), .clk(CLK), .clr(CLR));
  Register #(.width(16)) register_26 (.D(R2_2), .en(FLUSH), .Q(R2_4), .clk(CLK), .clr(CLR));
  Register #(.width(16)) register_27 (.D(R4_2), .en(FLUSH), .Q(R4_4), .clk(CLK), .clr(CLR));
  Register #(.width(16)) register_28 (.D(R6_2), .en(FLUSH), .Q(R6_4), .clk(CLK), .clr(CLR));
  Register #(.width(16)) register_29 (.D(R8_2), .en(FLUSH), .Q(R8_4), .clk(CLK), .clr(CLR));
  Register #(.width(16)) register_30 (.D(R10_2), .en(FLUSH), .Q(R10_4), .clk(CLK), .clr(CLR));
  Register #(.width(16)) register_31 (.D(R12_2), .en(FLUSH), .Q(R12_4), .clk(CLK), .clr(CLR));
  Register #(.width(16)) register_32 (.D(R14_2), .en(FLUSH), .Q(R14_4), .clk(CLK), .clr(CLR));

  // Other names for the same wires on the sheet: WRITE = FLUSH
endmodule
