// Logisim project MIPS.circ as structural Verilog: 22 circuits, main circuit main
module main (
  input  RESET
);

  wire alu_8_by_art_1_p4, alu_8_by_art_1_p6, ALU_SRC, Branch_PC_Src, CLK, cntrl_1_alusrc, cntrl_1_beq,
       cntrl_1_bneq, cntrl_1_memread, cntrl_1_memtoreg, cntrl_1_memwrite, cntrl_1_regdst, cntrl_1_regwrite,
       ex_mem_1_beq_2, ex_mem_1_bneq_2, ex_mem_1_mem_to_reg_2, ex_mem_1_zero_2, EX_MEM_REG_WRITE, Hazard,
       id_ex_1_beq_2, id_ex_1_bneq_2, id_ex_1_jump_2, id_ex_1_mem_to_reg_2, id_ex_1_mem_write_2,
       id_ex_1_reg_write_2, ID_EX_MEM_READ, JUMP_PC_Src, MEM_READ, MEM_TO_REG, MEM_WB_REG_WRITE, MEM_WRITE,
       REG_DEST;
  wire [1:0] forwarding_unit_1_forward_a, forwarding_unit_1_forward_b;
  wire [2:0] ALU_OP, cntrl_1_aluop;
  wire [3:0] ex_mem_1_write_reg_2, id_1_dest, id_1_opcode, id_1_src_1, id_1_src_2, id_ex_1_dest_reg_2,
       id_ex_1_src_1_2, id_ex_1_src_2_2, mem_wb_1_write_reg_2, multiplexer_6_out;
  wire [7:0] adder_1_out, alu_8_by_art_1_p2, alu_8_by_art_1_p5, Branch_PC, ex_mem_1_reg_data_2_2,
       EX_MEM_RegData, id_1_addr___immd, id_ex_1_pc_2, id_ex_1_reg_data_1_2, id_ex_1_reg_data_2_2, ID_EX_IMM,
       if_1_pc___1, if_1_pc_read, if_id_1_pc_2, Jump_Address, mem_1_data_read, mem_wb_1_alu_result_2,
       mem_wb_1_reg_data_2_2, MEM_WB_RegData, multiplexer_1_out, multiplexer_2_out, multiplexer_3_out,
       multiplexer_4_out, reg_file_1_readdata1, reg_file_1_readdata2;
  wire [19:0] if_1_instruction, if_id_1_instruction_2;
  wire [23:0] R10S, R432;

  Clock u_CLK (.out(CLK));
  Multiplexer #(.width(8), .enable("false")) multiplexer_1 (
    .in0(multiplexer_2_out), .in1(Jump_Address), .out(multiplexer_1_out), .sel(JUMP_PC_Src));
  Multiplexer #(.width(8), .enable("false")) multiplexer_2 (
    .in0(if_1_pc___1), .in1(Branch_PC), .out(multiplexer_2_out), .sel(Branch_PC_Src));
  IF if_1 (
    .PC_Write(multiplexer_1_out), .CLK(CLK), .RESET(RESET), .PC_Read(if_1_pc_read),
    .Instruction(if_1_instruction), .PC___1(if_1_pc___1), .Stall(Hazard));
  // Probe on R10S[15:8]
  // Probe on R10S[23:16]
  // Probe on R432[7:0]
  // Probe on R432[15:8]
  // Probe on R432[23:16]
  // Probe on R10S[7:0]
  // Probe on if_1_pc_read
  IF_ID if_id_1 (
    .Instruction(if_1_instruction), .Instruction_2(if_id_1_instruction_2), .PC(if_1_pc___1),
    .PC_2(if_id_1_pc_2), .CLK(CLK), .CLR(RESET), .Stall(Hazard));
  ID id_1 (
    .Instruction(if_id_1_instruction_2), .Opcode(id_1_opcode), .Src_1(id_1_src_1), .Src_2(id_1_src_2),
    .Dest(id_1_dest), .Addr___Immd(id_1_addr___immd), .Jump_Addr(Jump_Address));
  CNTRL cntrl_1 (
    .OP_Code(id_1_opcode), .RegDst(cntrl_1_regdst), .ALUSrc(cntrl_1_alusrc), .MemToReg(cntrl_1_memtoreg),
    .RegWrite(cntrl_1_regwrite), .MemRead(cntrl_1_memread), .MemWrite(cntrl_1_memwrite), .beq(cntrl_1_beq),
    .bneq(cntrl_1_bneq), .Jump(JUMP_PC_Src), .ALUOp(cntrl_1_aluop), .NOP(Hazard));
  REG_FILE reg_file_1 (
    .Src_1(id_1_src_1), .Src_2(id_1_src_2), .WriteData(MEM_WB_RegData), .CLK(CLK), .CLR(RESET),
    .t4__t3__t2(R432), .t1__t0__sp(R10S), .ReadData1(reg_file_1_readdata1), .ReadData2(reg_file_1_readdata2),
    .Dest_1(mem_wb_1_write_reg_2), .RegWrite(MEM_WB_REG_WRITE));
  HAZARD_DETECTION hazard_detection_1 (
    .ID_EX_MemRead(ID_EX_MEM_READ), .ID_EX_RegisterRt(id_ex_1_dest_reg_2), .IF_ID_RegisterRs(id_1_src_1),
    .IF_ID_RegisterRt(id_1_src_2), .Hazard(Hazard));
  ID_EX id_ex_1 (
    .Reg_Data_1(reg_file_1_readdata1), .Reg_Data_2(reg_file_1_readdata2), .IMM(id_1_addr___immd),
    .DEST_REG(id_1_src_2), .CLK(CLK), .CLR(RESET), .Reg_Data_1_2(id_ex_1_reg_data_1_2),
    .Reg_Data_2_2(id_ex_1_reg_data_2_2), .IMM_2(ID_EX_IMM), .DEST_REG_2(id_ex_1_dest_reg_2),
    .SRC_2(id_1_dest), .SRC_2_2(id_ex_1_src_2_2), .PC(if_id_1_pc_2), .PC_2(id_ex_1_pc_2), .SRC_1(id_1_src_1),
    .SRC_1_2(id_ex_1_src_1_2), .MEM_READ(cntrl_1_memread), .MEM_READ_2(ID_EX_MEM_READ),
    .MEM_WRITE(cntrl_1_memwrite), .MEM_WRITE_2(id_ex_1_mem_write_2), .BNEQ(cntrl_1_bneq),
    .BNEQ_2(id_ex_1_bneq_2), .BEQ(cntrl_1_beq), .BEQ_2(id_ex_1_beq_2), .JUMP(JUMP_PC_Src),
    .JUMP_2(id_ex_1_jump_2), .MEM_TO_REG(cntrl_1_memtoreg), .MEM_TO_REG_2(id_ex_1_mem_to_reg_2),
    .REG_WRITE(cntrl_1_regwrite), .REG_WRITE_2(id_ex_1_reg_write_2), .out_20(ALU_OP), .in_1(cntrl_1_aluop),
    .in_2(cntrl_1_alusrc), .out_21(ALU_SRC), .in_3(cntrl_1_regdst), .out_22(REG_DEST));
  Multiplexer #(.select(2), .width(8), .enable("false")) multiplexer_3 (
    .in0(id_ex_1_reg_data_1_2), .in1(MEM_WB_RegData), .in2(EX_MEM_RegData), .out(multiplexer_3_out),
    .sel(forwarding_unit_1_forward_a));  // open: in3
  Multiplexer #(.select(2), .width(8), .enable("false")) multiplexer_4 (
    .in0(id_ex_1_reg_data_2_2), .in1(MEM_WB_RegData), .in2(EX_MEM_RegData), .out(multiplexer_4_out),
    .sel(forwarding_unit_1_forward_b));  // open: in3
  FORWARDING_UNIT forwarding_unit_1 (
    .ID_EX_RegisterRs(id_ex_1_src_1_2), .ID_EX_RegisterRt(id_ex_1_dest_reg_2),
    .EX_MEM_RegisterRd(ex_mem_1_write_reg_2), .EX_MEM_RegWrite(EX_MEM_REG_WRITE),
    .MEM_WB_RegisterRd(mem_wb_1_write_reg_2), .MEM_WB_RegWrite(MEM_WB_REG_WRITE),
    .Forward_A(forwarding_unit_1_forward_a), .Forward_B(forwarding_unit_1_forward_b));
  // ALU_8_by_ART alu_8_by_art_1: pin names not known; wires that end beside it: multiplexer_3_out, alu_8_by_art_1_p2, ALU_OP, alu_8_by_art_1_p4, alu_8_by_art_1_p5, alu_8_by_art_1_p6
  Multiplexer #(.width(8), .enable("false")) multiplexer_5 (
    .in0(multiplexer_4_out), .in1(ID_EX_IMM), .out(alu_8_by_art_1_p2), .sel(ALU_SRC));
  Adder adder_1 (.a(id_ex_1_pc_2), .b(ID_EX_IMM), .out(adder_1_out));  // open: cin, cout
  Multiplexer #(.width(4), .enable("false")) multiplexer_6 (
    .in0(id_ex_1_dest_reg_2), .in1(id_ex_1_src_2_2), .out(multiplexer_6_out), .sel(REG_DEST));
  EX_MEM ex_mem_1 (
    .REG_WRITE(id_ex_1_reg_write_2), .ALU_RESULT(alu_8_by_art_1_p5), .WRITE_REG(multiplexer_6_out),
    .CLK(CLK), .CLR(RESET), .ALU_RESULT_2(EX_MEM_RegData), .WRITE_REG_2(ex_mem_1_write_reg_2),
    .Reg_Data_2(multiplexer_4_out), .Reg_Data_2_2(ex_mem_1_reg_data_2_2), .MEM_TO_REG(id_ex_1_mem_to_reg_2),
    .JUMP(id_ex_1_jump_2), .BNEQ(id_ex_1_bneq_2), .BEQ(id_ex_1_beq_2), .MEM_WRITE(id_ex_1_mem_write_2),
    .MEM_READ(ID_EX_MEM_READ), .ZERO(alu_8_by_art_1_p4), .MEM_READ_2(MEM_READ), .MEM_WRITE_2(MEM_WRITE),
    .BNEQ_2(ex_mem_1_bneq_2), .BEQ_2(ex_mem_1_beq_2), .JUMP_2(alu_8_by_art_1_p6),
    .MEM_TO_REG_2(ex_mem_1_mem_to_reg_2), .REG_WRITE_2(EX_MEM_REG_WRITE), .ZERO_2(ex_mem_1_zero_2),
    .PC(adder_1_out), .PC_2(Branch_PC));
  Multiplexer #(.enable("false")) multiplexer_7 (
    .in0(ex_mem_1_bneq_2), .in1(ex_mem_1_beq_2), .out(Branch_PC_Src), .sel(ex_mem_1_zero_2));
  MEM mem_1 (
    .Address(EX_MEM_RegData), .WriteData(ex_mem_1_reg_data_2_2), .Data_Read(mem_1_data_read),
    .MemWrite(MEM_WRITE), .CLK(CLK), .MemRead(MEM_READ), .CLR(RESET));
  MEM_WB mem_wb_1 (
    .ALU_RESULT(EX_MEM_RegData), .Reg_Data_2(mem_1_data_read), .CLK(CLK), .CLR(RESET),
    .ALU_RESULT_2(mem_wb_1_alu_result_2), .Reg_Data_2_2(mem_wb_1_reg_data_2_2),
    .MEM_TO_REG(ex_mem_1_mem_to_reg_2), .MEM_TO_REG_2(MEM_TO_REG), .REG_WRITE(EX_MEM_REG_WRITE),
    .REG_WRITE_2(MEM_WB_REG_WRITE), .WRITE_REG(ex_mem_1_write_reg_2), .WRITE_REG_2(mem_wb_1_write_reg_2));
  Multiplexer #(.width(8), .enable("false")) multiplexer_8 (
    .in0(mem_wb_1_alu_result_2), .in1(mem_wb_1_reg_data_2_2), .out(MEM_WB_RegData), .sel(MEM_TO_REG));

  // Other names for the same wires on the sheet: CLR = RESET
endmodule

module IF (
  input  [7:0] PC_Write,
  input  Stall,
  input  CLK,
  input  RESET,
  output [7:0] PC_Read,
  output [7:0] PC___1,
  output [19:0] Instruction
);

  wire not_1_out;

  Register register_1 (.D(PC_Write), .en(not_1_out), .Q(PC_Read), .clk(CLK), .clr(RESET));
  not not_1 (not_1_out, Stall);
  Adder adder_1 (.a(PC_Read), .b(8'h1), .out(PC___1), .cin(1'b0));  // open: cout
  ROM #(.dataWidth(20)) rom_1 (.addr(PC_Read), .data(Instruction), .sel(1'b1));

  // Notes on the sheet:
  //   contents of rom_1 (hex, n*v repeats v):
  //   a06ff a050a a0101 0 0 0 7151c 0 0 0 a0102 0 0 0 71514 0 0 0 a0101 a0201 a0402 c1230 c0210 c0320
  //   a4401 0 0 0 554f8 4*0 f2400 0 a0301 86300 96601 13504 86500 96601 b5405 86400 96601 844a2 86400
  //   96601 d41a2 86100 96601 a1288 86200 96601 92381 3230 86300 96601 a0546 a0155 65120 86200 96601 223fe
  //   86300 96601 a0380 a04aa e3410 86100 96601 312ff 86200 96601 0 f4900
endmodule

module ID (
  input  [19:0] Instruction,
  output [3:0] Opcode,
  output [3:0] Src_1,
  output [3:0] Src_2,
  output [3:0] Dest,
  output [7:0] Addr___Immd,
  output [7:0] Jump_Addr
);


  assign Addr___Immd = Instruction[7:0];
  assign Dest = Instruction[7:4];
  assign Jump_Addr = Instruction[15:8];
  assign Opcode = Instruction[19:16];
  assign Src_1 = Instruction[15:12];
  assign Src_2 = Instruction[11:8];

  // Notes on the sheet:
  //   Shift Amt
endmodule

module REG_FILE (
  input  RegWrite,
  input  [3:0] Dest_1,
  input  [3:0] Src_1,
  input  [3:0] Src_2,
  input  [7:0] WriteData,
  input  CLK,
  input  CLR,
  output [23:0] t4__t3__t2,
  output [23:0] t1__t0__sp,
  output [7:0] ReadData1,
  output [7:0] ReadData2
);

  wire and_1_out, and_2_out, comparator_1_eq, comparator_2_eq, comparator_3_eq, comparator_4_eq,
       demultiplexer_1_out1, demultiplexer_1_out2, demultiplexer_1_out3, demultiplexer_1_out4,
       demultiplexer_1_out5, demultiplexer_1_out6, not_1_out, not_2_out;
  wire [2:0] bit_extender_1_out, bit_extender_2_out, bit_extender_3_out;
  wire [7:0] multiplexer_1_out, multiplexer_3_out;

  Comparator #(.width(4), .mode("unsigned")) comparator_1 (
    .a(Dest_1), .b(Src_1), .eq(comparator_1_eq));  // open: gt, lt
  Comparator #(.width(4), .mode("unsigned")) comparator_2 (
    .a(Dest_1), .b(4'b0000), .eq(comparator_2_eq));  // open: gt, lt
  Register t1 (.D(WriteData), .en(demultiplexer_1_out1), .Q(t1__t0__sp[23:16]), .clk(CLK), .clr(CLR));
  Bit_Extender #(.in_width(4), .out_width(3)) bit_extender_1 (.in(Src_1), .out(bit_extender_1_out));
  and and_1 (and_1_out, comparator_1_eq, RegWrite, not_1_out);
  not not_1 (not_1_out, comparator_2_eq);
  Bit_Extender #(.in_width(4), .out_width(3)) bit_extender_2 (.in(Dest_1), .out(bit_extender_2_out));
  Register t2 (.D(WriteData), .en(demultiplexer_1_out2), .Q(t4__t3__t2[7:0]), .clk(CLK), .clr(CLR));
  Multiplexer #(.select(3), .width(8), .enable("false")) multiplexer_1 (
    .in0({8{1'b0}}), .in1(t1__t0__sp[23:16]), .in2(t4__t3__t2[7:0]), .in3(t4__t3__t2[15:8]),
    .in4(t4__t3__t2[23:16]), .in5(t1__t0__sp[15:8]), .in6(t1__t0__sp[7:0]), .out(multiplexer_1_out),
    .sel(bit_extender_1_out));  // open: in7
  Multiplexer #(.width(8), .enable("false")) multiplexer_2 (
    .in0(multiplexer_1_out), .in1(WriteData), .out(ReadData1), .sel(and_1_out));
  Demultiplexer #(.select(3), .enable("false")) demultiplexer_1 (
    .out1(demultiplexer_1_out1), .out2(demultiplexer_1_out2), .out3(demultiplexer_1_out3),
    .out4(demultiplexer_1_out4), .out5(demultiplexer_1_out5), .out6(demultiplexer_1_out6), .in(RegWrite),
    .sel(bit_extender_2_out));  // open: out0, out7
  Register t3 (.D(WriteData), .en(demultiplexer_1_out3), .Q(t4__t3__t2[15:8]), .clk(CLK), .clr(CLR));
  Register t4 (.D(WriteData), .en(demultiplexer_1_out4), .Q(t4__t3__t2[23:16]), .clk(CLK), .clr(CLR));
  Bit_Extender #(.in_width(4), .out_width(3)) bit_extender_3 (.in(Src_2), .out(bit_extender_3_out));
  Comparator #(.width(4), .mode("unsigned")) comparator_3 (
    .a(Dest_1), .b(Src_2), .eq(comparator_3_eq));  // open: gt, lt
  not not_2 (not_2_out, comparator_4_eq);
  Comparator #(.width(4), .mode("unsigned")) comparator_4 (
    .a(Dest_1), .b(4'b0000), .eq(comparator_4_eq));  // open: gt, lt
  Register t0 (.D(WriteData), .en(demultiplexer_1_out5), .Q(t1__t0__sp[15:8]), .clk(CLK), .clr(CLR));
  Multiplexer #(.select(3), .width(8), .enable("false")) multiplexer_3 (
    .in0({8{1'b0}}), .in1(t1__t0__sp[23:16]), .in2(t4__t3__t2[7:0]), .in3(t4__t3__t2[15:8]),
    .in4(t4__t3__t2[23:16]), .in5(t1__t0__sp[15:8]), .in6(t1__t0__sp[7:0]), .out(multiplexer_3_out),
    .sel(bit_extender_3_out));  // open: in7
  and and_2 (and_2_out, comparator_3_eq, RegWrite, not_2_out);
  Multiplexer #(.width(8), .enable("false")) multiplexer_4 (
    .in0(multiplexer_3_out), .in1(WriteData), .out(ReadData2), .sel(and_2_out));
  Register sp (.D(WriteData), .en(demultiplexer_1_out6), .Q(t1__t0__sp[7:0]), .clk(CLK), .clr(CLR));

  // Other names for the same wires on the sheet: D1[3:0] = Dest_1; READ_DATA_1[7:0] = ReadData1;
  //   READ_DATA_2[7:0] = ReadData2; S1[3:0] = Src_1; S2[3:0] = Src_2; WD[7:0] = WriteData

  // Notes on the sheet:
  //   Registers typically write on rising edge and reads on falling edge. But in logsim we have no way (at least IDK) to control when to read.
  //   So what we are doing here is we are checking if the register we are trying to read is also getting updated if so we just pass the new value of it using MUX.
  //   But we must be careful to not pass it when reading or writing to zero register. Also the write register flag should be checked.
endmodule

module UPDATED_REG_FILE (
  input  RegWrite,
  input  [3:0] Dest_1,
  input  [3:0] Src_1,
  input  [3:0] Src_2,
  input  [7:0] WriteData,
  input  CLK,
  input  CLR,
  output [7:0] ReadData1,
  output [7:0] ReadData2
);

  wire demultiplexer_1_out1, demultiplexer_1_out2, demultiplexer_1_out3, demultiplexer_1_out4,
       demultiplexer_1_out5, demultiplexer_1_out6, demultiplexer_1_out7, demultiplexer_1_out8,
       demultiplexer_1_out9, demultiplexer_1_out10, demultiplexer_1_out11, demultiplexer_1_out12,
       demultiplexer_1_out13, demultiplexer_1_out14, demultiplexer_1_out15;
  wire [7:0] a0_q, a1_q, s0_q, s1_q, s2_q, s3_q, s4_q, t0_q, t1_q, t2_q, t3_q, t4_q, t5_q, v0_q, v1_q;

  Demultiplexer #(.select(4), .enable("false")) demultiplexer_1 (
    .out1(demultiplexer_1_out1), .out2(demultiplexer_1_out2), .out3(demultiplexer_1_out3),
    .out4(demultiplexer_1_out4), .out5(demultiplexer_1_out5), .out6(demultiplexer_1_out6),
    .out7(demultiplexer_1_out7), .out8(demultiplexer_1_out8), .out9(demultiplexer_1_out9),
    .out10(demultiplexer_1_out10), .out11(demultiplexer_1_out11), .out12(demultiplexer_1_out12),
    .out13(demultiplexer_1_out13), .out14(demultiplexer_1_out14), .out15(demultiplexer_1_out15),
    .in(RegWrite), .sel(Dest_1));  // open: out0
  Register t0 (.D(WriteData), .en(demultiplexer_1_out1), .Q(t0_q), .clk(CLK), .clr(CLR));
  Register t1 (.D(WriteData), .en(demultiplexer_1_out2), .Q(t1_q), .clk(CLK), .clr(CLR));
  Register t2 (.D(WriteData), .en(demultiplexer_1_out3), .Q(t2_q), .clk(CLK), .clr(CLR));
  Register t3 (.D(WriteData), .en(demultiplexer_1_out4), .Q(t3_q), .clk(CLK), .clr(CLR));
  Register t4 (.D(WriteData), .en(demultiplexer_1_out5), .Q(t4_q), .clk(CLK), .clr(CLR));
  Register t5 (.D(WriteData), .en(demultiplexer_1_out6), .Q(t5_q), .clk(CLK), .clr(CLR));
  Register v0 (.D(WriteData), .en(demultiplexer_1_out7), .Q(v0_q), .clk(CLK), .clr(CLR));
  Register v1 (.D(WriteData), .en(demultiplexer_1_out8), .Q(v1_q), .clk(CLK), .clr(CLR));
  Register a0 (.D(WriteData), .en(demultiplexer_1_out9), .Q(a0_q), .clk(CLK), .clr(CLR));
  Register a1 (.D(WriteData), .en(demultiplexer_1_out10), .Q(a1_q), .clk(CLK), .clr(CLR));
  Register s0 (.D(WriteData), .en(demultiplexer_1_out11), .Q(s0_q), .clk(CLK), .clr(CLR));
  Register s1 (.D(WriteData), .en(demultiplexer_1_out12), .Q(s1_q), .clk(CLK), .clr(CLR));
  Register s2 (.D(WriteData), .en(demultiplexer_1_out13), .Q(s2_q), .clk(CLK), .clr(CLR));
  Register s3 (.D(WriteData), .en(demultiplexer_1_out14), .Q(s3_q), .clk(CLK), .clr(CLR));
  Register s4 (.D(WriteData), .en(demultiplexer_1_out15), .Q(s4_q), .clk(CLK), .clr(CLR));
  Multiplexer #(.select(4), .width(8), .enable("false")) multiplexer_1 (
    .in0({8{1'b0}}), .in1(t0_q), .in2(t1_q), .in3(t2_q), .in4(t3_q), .in5(t4_q), .in6(t5_q), .in7(v0_q),
    .in8(v1_q), .in9(a0_q), .in10(a1_q), .in11(s0_q), .in12(s1_q), .in13(s2_q), .in14(s3_q), .in15(s4_q),
    .out(ReadData1), .sel(Src_1));
  Multiplexer #(.select(4), .width(8), .enable("false")) multiplexer_2 (
    .in0({8{1'b0}}), .in1(t0_q), .in2(t1_q), .in3(t2_q), .in4(t3_q), .in5(t4_q), .in6(t5_q), .in7(v0_q),
    .in8(v1_q), .in9(a0_q), .in10(a1_q), .in11(s0_q), .in12(s1_q), .in13(s2_q), .in14(s3_q), .in15(s4_q),
    .out(ReadData2), .sel(Src_2));

  // Other names for the same wires on the sheet: D1[3:0] = Dest_1; READ_DATA_1[7:0] = ReadData1;
  //   READ_DATA_2[7:0] = ReadData2; S1[3:0] = Src_1; S2[3:0] = Src_2; WD[7:0] = WriteData
endmodule

module MEM (
  input  [7:0] Address,
  input  [7:0] WriteData,
  input  CLK,
  input  CLR,
  input  MemWrite,
  input  MemRead,
  output [7:0] Data_Read
);

  RAM #(.bus("separate")) ram_1 (
    .addr(Address), .din(WriteData), .data(Data_Read), .str(MemWrite), .sel(1'b1), .clk(CLK), .ld(MemRead),
    .clr(CLR));
endmodule

module CNTRL (
  input  [3:0] OP_Code,
  input  NOP,
  output RegDst,
  output ALUSrc,
  output MemToReg,
  output RegWrite,
  output MemRead,
  output MemWrite,
  output beq,
  output bneq,
  output Jump,
  output [2:0] ALUOp
);

  wire [11:0] rom_1_data;

  ROM #(.addrWidth(4), .dataWidth(12)) rom_1 (.addr(OP_Code), .data(rom_1_data), .sel(1'b1));
  Multiplexer #(.width(12), .enable("false")) multiplexer_1 (
    .in0(rom_1_data), .in1({12{1'b0}}),
    .out({RegDst, ALUSrc, MemToReg, RegWrite, MemRead, MemWrite, beq, bneq, Jump, ALUOp}), .sel(NOP));

  // Notes on the sheet:
  //   contents of rom_1 (hex, n*v repeats v):
  //   901 506 503 502 904 11 903 21 c40 501 500 505 900 780 902 8
endmodule

module IF_ID (
  input  Stall,
  input  [7:0] PC,
  input  [19:0] Instruction,
  input  CLK,
  input  CLR,
  output [7:0] PC_2,
  output [19:0] Instruction_2
);

  wire EnableWrite;

  not not_1 (EnableWrite, Stall);
  Register u_PC (.D(PC), .en(EnableWrite), .Q(PC_2), .clk(CLK), .clr(CLR));
  Register #(.width(20)) IF_ID_REG (.D(Instruction), .en(EnableWrite), .Q(Instruction_2), .clk(CLK), .clr(CLR));
endmodule

module ID_EX (
  input  [2:0] in_1,
  input  in_2,
  input  in_3,
  input  MEM_READ,
  input  MEM_WRITE,
  input  BNEQ,
  input  BEQ,
  input  JUMP,
  input  MEM_TO_REG,
  input  REG_WRITE,
  input  [7:0] PC,
  input  [7:0] Reg_Data_1,
  input  [7:0] Reg_Data_2,
  input  [7:0] IMM,
  input  [3:0] SRC_1,
  input  [3:0] SRC_2,
  input  [3:0] DEST_REG,
  input  CLK,
  input  CLR,
  output [2:0] out_20,
  output out_21,
  output out_22,
  output MEM_READ_2,
  output MEM_WRITE_2,
  output BNEQ_2,
  output BEQ_2,
  output JUMP_2,
  output MEM_TO_REG_2,
  output REG_WRITE_2,
  output [7:0] PC_2,
  output [7:0] Reg_Data_1_2,
  output [7:0] Reg_Data_2_2,
  output [7:0] IMM_2,
  output [3:0] SRC_1_2,
  output [3:0] SRC_2_2,
  output [3:0] DEST_REG_2
);

  Register #(.width(3)) ALUOp (.D(in_1), .en(1'b1), .Q(out_20), .clk(CLK), .clr(CLR));
  Register #(.width(1)) ALUSrc (.D(in_2), .en(1'b1), .Q(out_21), .clk(CLK), .clr(CLR));
  Register #(.width(1)) RegDest (.D(in_3), .en(1'b1), .Q(out_22), .clk(CLK), .clr(CLR));
  Register #(.width(1)) u_MEM_READ (.D(MEM_READ), .en(1'b1), .Q(MEM_READ_2), .clk(CLK), .clr(CLR));
  Register #(.width(1)) u_MEM_WRITE (.D(MEM_WRITE), .en(1'b1), .Q(MEM_WRITE_2), .clk(CLK), .clr(CLR));
  Register #(.width(1)) u_BNEQ (.D(BNEQ), .en(1'b1), .Q(BNEQ_2), .clk(CLK), .clr(CLR));
  Register #(.width(1)) u_BEQ (.D(BEQ), .en(1'b1), .Q(BEQ_2), .clk(CLK), .clr(CLR));
  Register #(.width(1)) u_JUMP (.D(JUMP), .en(1'b1), .Q(JUMP_2), .clk(CLK), .clr(CLR));
  Register #(.width(1)) u_MEM_TO_REG (.D(MEM_TO_REG), .en(1'b1), .Q(MEM_TO_REG_2), .clk(CLK), .clr(CLR));
  Register #(.width(1)) u_REG_WRITE (.D(REG_WRITE), .en(1'b1), .Q(REG_WRITE_2), .clk(CLK), .clr(CLR));
  Register u_PC (.D(PC), .en(1'b1), .Q(PC_2), .clk(CLK), .clr(CLR));
  Register u_Reg_Data_1 (.D(Reg_Data_1), .en(1'b1), .Q(Reg_Data_1_2), .clk(CLK), .clr(CLR));
  Register u_Reg_Data_2 (.D(Reg_Data_2), .en(1'b1), .Q(Reg_Data_2_2), .clk(CLK), .clr(CLR));
  Register u_IMM (.D(IMM), .en(1'b1), .Q(IMM_2), .clk(CLK), .clr(CLR));
  Register #(.width(4)) u_SRC_1 (.D(SRC_1), .en(1'b1), .Q(SRC_1_2), .clk(CLK), .clr(CLR));
  Register #(.width(4)) u_SRC_2 (.D(SRC_2), .en(1'b1), .Q(SRC_2_2), .clk(CLK), .clr(CLR));
  Register #(.width(4)) u_DEST_REG (.D(DEST_REG), .en(1'b1), .Q(DEST_REG_2), .clk(CLK), .clr(CLR));
endmodule

module EX_MEM (
  input  MEM_READ,
  input  MEM_WRITE,
  input  BNEQ,
  input  BEQ,
  input  JUMP,
  input  MEM_TO_REG,
  input  REG_WRITE,
  input  [7:0] PC,
  input  ZERO,
  input  [7:0] ALU_RESULT,
  input  [7:0] Reg_Data_2,
  input  [3:0] WRITE_REG,
  input  CLK,
  input  CLR,
  output MEM_READ_2,
  output MEM_WRITE_2,
  output BNEQ_2,
  output BEQ_2,
  output JUMP_2,
  output MEM_TO_REG_2,
  output REG_WRITE_2,
  output [7:0] PC_2,
  output ZERO_2,
  output [7:0] ALU_RESULT_2,
  output [7:0] Reg_Data_2_2,
  output [3:0] WRITE_REG_2
);

  Register #(.width(1)) u_MEM_READ (.D(MEM_READ), .en(1'b1), .Q(MEM_READ_2), .clk(CLK), .clr(CLR));
  Register #(.width(1)) u_MEM_WRITE (.D(MEM_WRITE), .en(1'b1), .Q(MEM_WRITE_2), .clk(CLK), .clr(CLR));
  Register #(.width(1)) u_BNEQ (.D(BNEQ), .en(1'b1), .Q(BNEQ_2), .clk(CLK), .clr(CLR));
  Register #(.width(1)) u_BEQ (.D(BEQ), .en(1'b1), .Q(BEQ_2), .clk(CLK), .clr(CLR));
  Register #(.width(1)) u_JUMP (.D(JUMP), .en(1'b1), .Q(JUMP_2), .clk(CLK), .clr(CLR));
  Register #(.width(1)) u_MEM_TO_REG (.D(MEM_TO_REG), .en(1'b1), .Q(MEM_TO_REG_2), .clk(CLK), .clr(CLR));
  Register #(.width(1)) u_REG_WRITE (.D(REG_WRITE), .en(1'b1), .Q(REG_WRITE_2), .clk(CLK), .clr(CLR));
  Register u_PC (.D(PC), .en(1'b1), .Q(PC_2), .clk(CLK), .clr(CLR));
  Register #(.width(1)) u_ZERO (.D(ZERO), .en(1'b1), .Q(ZERO_2), .clk(CLK), .clr(CLR));
  Register u_ALU_RESULT (.D(ALU_RESULT), .en(1'b1), .Q(ALU_RESULT_2), .clk(CLK), .clr(CLR));
  Register u_Reg_Data_2 (.D(Reg_Data_2), .en(1'b1), .Q(Reg_Data_2_2), .clk(CLK), .clr(CLR));
  Register #(.width(4)) u_WRITE_REG (.D(WRITE_REG), .en(1'b1), .Q(WRITE_REG_2), .clk(CLK), .clr(CLR));
endmodule

module MEM_WB (
  input  MEM_TO_REG,
  input  REG_WRITE,
  input  [7:0] ALU_RESULT,
  input  [7:0] Reg_Data_2,
  input  [3:0] WRITE_REG,
  input  CLK,
  input  CLR,
  output MEM_TO_REG_2,
  output REG_WRITE_2,
  output [7:0] ALU_RESULT_2,
  output [7:0] Reg_Data_2_2,
  output [3:0] WRITE_REG_2
);

  Register #(.width(1)) u_MEM_TO_REG (.D(MEM_TO_REG), .en(1'b1), .Q(MEM_TO_REG_2), .clk(CLK), .clr(CLR));
  Register #(.width(1)) u_REG_WRITE (.D(REG_WRITE), .en(1'b1), .Q(REG_WRITE_2), .clk(CLK), .clr(CLR));
  Register u_ALU_RESULT (.D(ALU_RESULT), .en(1'b1), .Q(ALU_RESULT_2), .clk(CLK), .clr(CLR));
  Register u_Reg_Data_2 (.D(Reg_Data_2), .en(1'b1), .Q(Reg_Data_2_2), .clk(CLK), .clr(CLR));
  Register #(.width(4)) u_WRITE_REG (.D(WRITE_REG), .en(1'b1), .Q(WRITE_REG_2), .clk(CLK), .clr(CLR));
endmodule

module FORWARDING_UNIT (
  input  [3:0] ID_EX_RegisterRs,
  input  [3:0] ID_EX_RegisterRt,
  input  [3:0] EX_MEM_RegisterRd,
  input  EX_MEM_RegWrite,
  input  [3:0] MEM_WB_RegisterRd,
  input  MEM_WB_RegWrite,
  output [1:0] Forward_A,
  output [1:0] Forward_B
);

  wire comparator_1_eq, comparator_2_eq, comparator_3_eq, comparator_4_eq, comparator_5_eq, comparator_6_eq,
       EX_Hazard_A, EX_Hazard_B, MEM_Hazard_A, MEM_Hazard_B, not_1_out, not_2_out;
  wire [1:0] bit_extender_1_out, bit_extender_2_out;

  Comparator #(.width(4), .mode("unsigned")) comparator_1 (
    .a(EX_MEM_RegisterRd), .b(4'b0000), .eq(comparator_1_eq));  // open: gt, lt
  Comparator #(.width(4), .mode("unsigned")) comparator_2 (
    .a(EX_MEM_RegisterRd), .b(ID_EX_RegisterRs), .eq(comparator_2_eq));  // open: gt, lt
  Comparator #(.width(4), .mode("unsigned")) comparator_3 (
    .a(EX_MEM_RegisterRd), .b(ID_EX_RegisterRt), .eq(comparator_3_eq));  // open: gt, lt
  Comparator #(.width(4), .mode("unsigned")) comparator_4 (
    .a(MEM_WB_RegisterRd), .b(4'b0000), .eq(comparator_4_eq));  // open: gt, lt
  Comparator #(.width(4), .mode("unsigned")) comparator_5 (
    .a(MEM_WB_RegisterRd), .b(ID_EX_RegisterRs), .eq(comparator_5_eq));  // open: gt, lt
  Comparator #(.width(4), .mode("unsigned")) comparator_6 (
    .a(MEM_WB_RegisterRd), .b(ID_EX_RegisterRt), .eq(comparator_6_eq));  // open: gt, lt
  not not_1 (not_1_out, comparator_1_eq);
  not not_2 (not_2_out, comparator_4_eq);
  assign bit_extender_1_out = {{1{1'b0}}, MEM_Hazard_A};  // Bit_Extender bit_extender_1
  assign bit_extender_2_out = {{1{1'b0}}, MEM_Hazard_B};  // Bit_Extender bit_extender_2
  and and_1 (EX_Hazard_A, EX_MEM_RegWrite, not_1_out, comparator_2_eq);
  and and_2 (EX_Hazard_B, EX_MEM_RegWrite, not_1_out, comparator_3_eq);
  and and_3 (MEM_Hazard_A, MEM_WB_RegWrite, not_2_out, comparator_5_eq);
  and and_4 (MEM_Hazard_B, MEM_WB_RegWrite, not_2_out, comparator_6_eq);
  Multiplexer #(.width(2), .enable("false")) multiplexer_1 (
    .in0(bit_extender_1_out), .in1(2'b10), .out(Forward_A), .sel(EX_Hazard_A));
  Multiplexer #(.width(2), .enable("false")) multiplexer_2 (
    .in0(bit_extender_2_out), .in1(2'b10), .out(Forward_B), .sel(EX_Hazard_B));

  // Notes on the sheet:
  //   EX HAZARD
  //   MEM HAZARD
endmodule

module HAZARD_DETECTION (
  input  ID_EX_MemRead,
  input  [3:0] ID_EX_RegisterRt,
  input  [3:0] IF_ID_RegisterRs,
  input  [3:0] IF_ID_RegisterRt,
  output Hazard
);

  wire comparator_1_eq, comparator_2_eq, or_1_out;

  Comparator #(.width(4), .mode("unsigned")) comparator_1 (
    .a(ID_EX_RegisterRt), .b(IF_ID_RegisterRs), .eq(comparator_1_eq));  // open: gt, lt
  Comparator #(.width(4), .mode("unsigned")) comparator_2 (
    .a(ID_EX_RegisterRt), .b(IF_ID_RegisterRt), .eq(comparator_2_eq));  // open: gt, lt
  or or_1 (or_1_out, comparator_1_eq, comparator_2_eq);
  and and_1 (Hazard, ID_EX_MemRead, or_1_out);

  // Notes on the sheet:
  //   We always write to Rt register in case of lw. So no need to consider ID/EX.RegisterRd
endmodule

module non_pipelined (
  input  RESET
);

  wire ALU_SRC, BRANCH, CLK, control_1_beq, control_1_bneq, JUMP, MEM_READ, MEM_TO_REG, MEM_WRITE, REG_DEST,
       REG_WRITE, ZERO;
  wire [2:0] ALU_OP;
  wire [3:0] instruction_1_dest, instruction_1_src_1, instruction_1_src_2, multiplexer_1_out, OP_CODE;
  wire [7:0] adder_1_out, adder_2_out, alu_8_by_art_1_p5, CURRENT_PC, IMM, JUMP_ADDR, memory_1_data_read,
       multiplexer_3_out, multiplexer_4_out, multiplexer_6_out, registers_1_readdata1, registers_1_readdata2,
       UPDATED_PC;
  wire [23:0] REG_10S, REG_432;

  // Probe on CURRENT_PC
  Clock u_CLK (.out(CLK));
  // Probe on OP_CODE
  Instruction instruction_1 (
    .PC_Write(UPDATED_PC), .CLK(CLK), .RESET(RESET), .PC_Read(CURRENT_PC), .Opcode(OP_CODE),
    .Src_1(instruction_1_src_1), .Src_2(instruction_1_src_2), .Dest(instruction_1_dest), .Addr___Immd(IMM),
    .Jump_Addr(JUMP_ADDR));
  Control control_1 (
    .OP_Code(OP_CODE), .RegDst(REG_DEST), .ALUSrc(ALU_SRC), .MemToReg(MEM_TO_REG), .RegWrite(REG_WRITE),
    .MemRead(MEM_READ), .MemWrite(MEM_WRITE), .beq(control_1_beq), .bneq(control_1_bneq), .Jump(JUMP),
    .ALUOp(ALU_OP));
  Adder adder_1 (.a(CURRENT_PC), .b(8'h1), .out(adder_1_out), .cin(1'b0));  // open: cout
  Multiplexer #(.width(4), .enable("false")) multiplexer_1 (
    .in0(instruction_1_src_2), .in1(instruction_1_dest), .out(multiplexer_1_out), .sel(REG_DEST));
  Multiplexer #(.enable("false")) multiplexer_2 (.in0(control_1_bneq), .in1(control_1_beq), .out(BRANCH), .sel(ZERO));
  Adder adder_2 (.a(adder_1_out), .b(IMM), .out(adder_2_out), .cin(1'b0));  // open: cout
  Multiplexer #(.width(8), .enable("false")) multiplexer_3 (
    .in0(adder_1_out), .in1(adder_2_out), .out(multiplexer_3_out), .sel(BRANCH));
  Registers registers_1 (
    .RegWrite(REG_WRITE), .Src_1(instruction_1_src_1), .Src_2(instruction_1_src_2),
    .Dest_1(multiplexer_1_out), .WriteData(multiplexer_6_out), .CLK(CLK), .CLR(RESET),
    .ReadData1(registers_1_readdata1), .ReadData2(registers_1_readdata2), .t4__t3__t2(REG_432),
    .t1__t0__sp(REG_10S));
  Multiplexer #(.width(8), .enable("false")) multiplexer_4 (
    .in0(registers_1_readdata2), .in1(IMM), .out(multiplexer_4_out), .sel(ALU_SRC));
  Multiplexer #(.width(8), .enable("false")) multiplexer_5 (
    .in0(multiplexer_3_out), .in1(JUMP_ADDR), .out(UPDATED_PC), .sel(JUMP));
  // ALU_8_by_ART alu_8_by_art_1: pin names not known; wires that end beside it: registers_1_readdata1, multiplexer_4_out, ALU_OP, ZERO, alu_8_by_art_1_p5
  // Probe on REG_10S[15:8]
  // Probe on REG_10S[23:16]
  // Probe on REG_432[7:0]
  // Probe on REG_432[15:8]
  // Probe on REG_432[23:16]
  // Probe on REG_10S[7:0]
  Memory memory_1 (
    .Address(alu_8_by_art_1_p5), .WriteData(registers_1_readdata2), .CLK(CLK), .CLR(RESET),
    .Data_Read(memory_1_data_read), .MemRead(MEM_READ), .MemWrite(MEM_WRITE));
  Multiplexer #(.width(8), .enable("false")) multiplexer_6 (
    .in0(alu_8_by_art_1_p5), .in1(memory_1_data_read), .out(multiplexer_6_out), .sel(MEM_TO_REG));
endmodule

module Instruction (
  input  [7:0] PC_Write,
  input  CLK,
  input  RESET,
  output [7:0] PC_Read,
  output [3:0] Opcode,
  output [3:0] Src_1,
  output [3:0] Src_2,
  output [3:0] Dest,
  output [7:0] Addr___Immd,
  output [7:0] Jump_Addr
);

  Register register_1 (.D(PC_Write), .en(1'b1), .Q(PC_Read), .clk(CLK), .clr(RESET));
  ROM #(.dataWidth(20)) rom_1 (.addr(PC_Read), .data({Opcode, Jump_Addr, Addr___Immd}), .sel(1'b1));

  assign Dest = Addr___Immd[7:4];
  assign Src_1 = Jump_Addr[7:4];
  assign Src_2 = Jump_Addr[3:0];

  // Notes on the sheet:
  //   contents of rom_1 (hex, n*v repeats v):
  //   a0503 a0104 a0205 a030c a0407 a0608 93203 94211 a2203 a4311 b3301 b4402 c3440 c5130 e3420 e5130
  //   Shift Amt
endmodule

module Control (
  input  [3:0] OP_Code,
  output RegDst,
  output ALUSrc,
  output MemToReg,
  output RegWrite,
  output MemRead,
  output MemWrite,
  output beq,
  output bneq,
  output Jump,
  output [2:0] ALUOp
);

  ROM #(.addrWidth(4), .dataWidth(12)) rom_1 (
    .addr(OP_Code), .data({RegDst, ALUSrc, MemToReg, RegWrite, MemRead, MemWrite, beq, bneq, Jump, ALUOp}),
    .sel(1'b1));

  // Notes on the sheet:
  //   contents of rom_1 (hex, n*v repeats v):
  //   901 506 503 502 904 11 903 21 c40 501 500 505 900 780 902 8
endmodule

module Registers (
  input  RegWrite,
  input  [3:0] Src_1,
  input  [3:0] Src_2,
  input  [3:0] Dest_1,
  input  [7:0] WriteData,
  input  CLK,
  input  CLR,
  output [23:0] t4__t3__t2,
  output [23:0] t1__t0__sp,
  output [7:0] ReadData1,
  output [7:0] ReadData2
);

  wire demultiplexer_1_out1, demultiplexer_1_out2, demultiplexer_1_out3, demultiplexer_1_out4,
       demultiplexer_1_out5, demultiplexer_1_out6;
  wire [2:0] bit_extender_1_out, bit_extender_2_out, bit_extender_3_out;

  Register t1 (.D(WriteData), .en(demultiplexer_1_out1), .Q(t1__t0__sp[23:16]), .clk(CLK), .clr(CLR));
  Bit_Extender #(.in_width(4), .out_width(3)) bit_extender_1 (.in(Src_1), .out(bit_extender_1_out));
  Bit_Extender #(.in_width(4), .out_width(3)) bit_extender_2 (.in(Dest_1), .out(bit_extender_2_out));
  Register t2 (.D(WriteData), .en(demultiplexer_1_out2), .Q(t4__t3__t2[7:0]), .clk(CLK), .clr(CLR));
  Multiplexer #(.select(3), .width(8), .enable("false")) multiplexer_1 (
    .in0({8{1'b0}}), .in1(t1__t0__sp[23:16]), .in2(t4__t3__t2[7:0]), .in3(t4__t3__t2[15:8]),
    .in4(t4__t3__t2[23:16]), .in5(t1__t0__sp[15:8]), .in6(t1__t0__sp[7:0]), .out(ReadData1),
    .sel(bit_extender_1_out));  // open: in7
  Demultiplexer #(.select(3), .enable("false")) demultiplexer_1 (
    .out1(demultiplexer_1_out1), .out2(demultiplexer_1_out2), .out3(demultiplexer_1_out3),
    .out4(demultiplexer_1_out4), .out5(demultiplexer_1_out5), .out6(demultiplexer_1_out6), .in(RegWrite),
    .sel(bit_extender_2_out));  // open: out0, out7
  Register t3 (.D(WriteData), .en(demultiplexer_1_out3), .Q(t4__t3__t2[15:8]), .clk(CLK), .clr(CLR));
  Register t4 (.D(WriteData), .en(demultiplexer_1_out4), .Q(t4__t3__t2[23:16]), .clk(CLK), .clr(CLR));
  Bit_Extender #(.in_width(4), .out_width(3)) bit_extender_3 (.in(Src_2), .out(bit_extender_3_out));
  Register t0 (.D(WriteData), .en(demultiplexer_1_out5), .Q(t1__t0__sp[15:8]), .clk(CLK), .clr(CLR));
  Multiplexer #(.select(3), .width(8), .enable("false")) multiplexer_2 (
    .in0({8{1'b0}}), .in1(t1__t0__sp[23:16]), .in2(t4__t3__t2[7:0]), .in3(t4__t3__t2[15:8]),
    .in4(t4__t3__t2[23:16]), .in5(t1__t0__sp[15:8]), .in6(t1__t0__sp[7:0]), .out(ReadData2),
    .sel(bit_extender_3_out));  // open: in7
  Register sp (.D(WriteData), .en(demultiplexer_1_out6), .Q(t1__t0__sp[7:0]), .clk(CLK), .clr(CLR));

  // Other names for the same wires on the sheet: S1[3:0] = Src_1; S2[3:0] = Src_2; WD[7:0] = WriteData
endmodule

module Memory (
  input  [7:0] Address,
  input  [7:0] WriteData,
  input  CLK,
  input  CLR,
  input  MemWrite,
  input  MemRead,
  output [7:0] Data_Read
);

  RAM #(.bus("separate")) ram_1 (
    .addr(Address), .din(WriteData), .data(Data_Read), .str(MemWrite), .sel(1'b1), .clk(CLK), .ld(MemRead),
    .clr(CLR));
endmodule

module ALU_TEST (
  input  [7:0] in_1,
  input  [7:0] in_2,
  input  [2:0] in_3,
  output out_4,
  output [7:0] out_5
);

  // ALU_8_by_ART alu_8_by_art_1: pin names not known; wires that end beside it: in_1, in_2, in_3, out_4, out_5
endmodule

module DisplayAdapter (
  input  CLR,
  input  WRITE_BUFFER,
  input  FLUSH_BUFFER,
  input  [15:0] DATA,
  input  [15:0] DATA_2,
  input  [4:0] ADDR,
  input  [7:0] DATA_3
);

  wire CLK;
  wire [15:0] n32_x_16b_buffer_1_r0_3, n32_x_16b_buffer_1_r0_4, n32_x_16b_buffer_1_r1_3,
       n32_x_16b_buffer_1_r1_4, n32_x_16b_buffer_1_r2_3, n32_x_16b_buffer_1_r2_4, n32_x_16b_buffer_1_r3_3,
       n32_x_16b_buffer_1_r3_4, n32_x_16b_buffer_1_r4_3, n32_x_16b_buffer_1_r4_4, n32_x_16b_buffer_1_r5_3,
       n32_x_16b_buffer_1_r5_4, n32_x_16b_buffer_1_r6_3, n32_x_16b_buffer_1_r6_4, n32_x_16b_buffer_1_r7_3,
       n32_x_16b_buffer_1_r7_4, n32_x_16b_buffer_1_r8_3, n32_x_16b_buffer_1_r8_4, n32_x_16b_buffer_1_r9_3,
       n32_x_16b_buffer_1_r9_4, n32_x_16b_buffer_1_r10_3, n32_x_16b_buffer_1_r10_4, n32_x_16b_buffer_1_r11_3,
       n32_x_16b_buffer_1_r11_4, n32_x_16b_buffer_1_r12_3, n32_x_16b_buffer_1_r12_4,
       n32_x_16b_buffer_1_r13_3, n32_x_16b_buffer_1_r13_4, n32_x_16b_buffer_1_r14_3,
       n32_x_16b_buffer_1_r14_4, n32_x_16b_buffer_1_r15_3, n32_x_16b_buffer_1_r15_4;

  Clock clock_1 (.out(CLK));
  _32_x_8b_REGISTER u_32_x_8b_register_1 (
    .CLK(CLK), .CLR(CLR), .FLUSH(WRITE_BUFFER), .ADDR(ADDR), .WRITE_DATA(DATA_3));  // open: R0, R1, R2, R3, R4, R5, R6, R7, R8, R9, R10, R11, R12, R13, R14, R15, R0_2, R1_2, R2_2, R3_2, R4_2, R5_2, R6_2, R7_2, R8_2, R9_2, R10_2, R11_2, R12_2, R13_2, R14_2, R15_2
  DotMatrix #(.matrixcols(32), .matrixrows(16)) dotmatrix_1 (
    .col0(n32_x_16b_buffer_1_r0_3), .col1(n32_x_16b_buffer_1_r1_3), .col2(n32_x_16b_buffer_1_r2_3),
    .col3(n32_x_16b_buffer_1_r3_3), .col4(n32_x_16b_buffer_1_r4_3), .col5(n32_x_16b_buffer_1_r5_3),
    .col6(n32_x_16b_buffer_1_r6_3), .col7(n32_x_16b_buffer_1_r7_3), .col8(n32_x_16b_buffer_1_r8_3),
    .col9(n32_x_16b_buffer_1_r9_3), .col10(n32_x_16b_buffer_1_r10_3), .col11(n32_x_16b_buffer_1_r11_3),
    .col12(n32_x_16b_buffer_1_r12_3), .col13(n32_x_16b_buffer_1_r13_3), .col14(n32_x_16b_buffer_1_r14_3),
    .col15(n32_x_16b_buffer_1_r15_3), .col16(n32_x_16b_buffer_1_r0_4), .col17(n32_x_16b_buffer_1_r1_4),
    .col18(n32_x_16b_buffer_1_r2_4), .col19(n32_x_16b_buffer_1_r3_4), .col20(n32_x_16b_buffer_1_r4_4),
    .col21(n32_x_16b_buffer_1_r5_4), .col22(n32_x_16b_buffer_1_r6_4), .col23(n32_x_16b_buffer_1_r7_4),
    .col24(n32_x_16b_buffer_1_r8_4), .col25(n32_x_16b_buffer_1_r9_4), .col26(n32_x_16b_buffer_1_r10_4),
    .col27(n32_x_16b_buffer_1_r11_4), .col28(n32_x_16b_buffer_1_r12_4), .col29(n32_x_16b_buffer_1_r13_4),
    .col30(n32_x_16b_buffer_1_r14_4), .col31(n32_x_16b_buffer_1_r15_4));
  _32_x_16b_BUFFER u_32_x_16b_buffer_1 (
    .CLK(CLK), .CLR(CLR), .FLUSH(FLUSH_BUFFER), .R0(DATA), .R1(DATA_2), .R0_3(n32_x_16b_buffer_1_r0_3),
    .R1_3(n32_x_16b_buffer_1_r1_3), .R2_3(n32_x_16b_buffer_1_r2_3), .R3_3(n32_x_16b_buffer_1_r3_3),
    .R4_3(n32_x_16b_buffer_1_r4_3), .R5_3(n32_x_16b_buffer_1_r5_3), .R6_3(n32_x_16b_buffer_1_r6_3),
    .R7_3(n32_x_16b_buffer_1_r7_3), .R8_3(n32_x_16b_buffer_1_r8_3), .R9_3(n32_x_16b_buffer_1_r9_3),
    .R10_3(n32_x_16b_buffer_1_r10_3), .R11_3(n32_x_16b_buffer_1_r11_3), .R12_3(n32_x_16b_buffer_1_r12_3),
    .R13_3(n32_x_16b_buffer_1_r13_3), .R14_3(n32_x_16b_buffer_1_r14_3), .R15_3(n32_x_16b_buffer_1_r15_3),
    .R0_4(n32_x_16b_buffer_1_r0_4), .R1_4(n32_x_16b_buffer_1_r1_4), .R2_4(n32_x_16b_buffer_1_r2_4),
    .R3_4(n32_x_16b_buffer_1_r3_4), .R4_4(n32_x_16b_buffer_1_r4_4), .R5_4(n32_x_16b_buffer_1_r5_4),
    .R6_4(n32_x_16b_buffer_1_r6_4), .R7_4(n32_x_16b_buffer_1_r7_4), .R8_4(n32_x_16b_buffer_1_r8_4),
    .R9_4(n32_x_16b_buffer_1_r9_4), .R10_4(n32_x_16b_buffer_1_r10_4), .R11_4(n32_x_16b_buffer_1_r11_4),
    .R12_4(n32_x_16b_buffer_1_r12_4), .R13_4(n32_x_16b_buffer_1_r13_4), .R14_4(n32_x_16b_buffer_1_r14_4),
    .R15_4(n32_x_16b_buffer_1_r15_4));  // open: R2, R3, R4, R5, R6, R7, R8, R9, R10, R11, R12, R13, R14, R15, R0_2, R1_2, R2_2, R3_2, R4_2, R5_2, R6_2, R7_2, R8_2, R9_2, R10_2, R11_2, R12_2, R13_2, R14_2, R15_2

  // Notes on the sheet:
  //   MSB
  //   LSB
endmodule

module _32_x_8b_REGISTER (
  input  CLK,
  input  CLR,
  input  FLUSH,
  input  [4:0] ADDR,
  input  [7:0] WRITE_DATA,
  output [7:0] R0,
  output [7:0] R1,
  output [7:0] R2,
  output [7:0] R3,
  output [7:0] R4,
  output [7:0] R5,
  output [7:0] R6,
  output [7:0] R7,
  output [7:0] R8,
  output [7:0] R9,
  output [7:0] R10,
  output [7:0] R11,
  output [7:0] R12,
  output [7:0] R13,
  output [7:0] R14,
  output [7:0] R15,
  output [7:0] R0_2,
  output [7:0] R1_2,
  output [7:0] R2_2,
  output [7:0] R3_2,
  output [7:0] R4_2,
  output [7:0] R5_2,
  output [7:0] R6_2,
  output [7:0] R7_2,
  output [7:0] R8_2,
  output [7:0] R9_2,
  output [7:0] R10_2,
  output [7:0] R11_2,
  output [7:0] R12_2,
  output [7:0] R13_2,
  output [7:0] R14_2,
  output [7:0] R15_2
);

  wire demultiplexer_1_out0, demultiplexer_1_out1, demultiplexer_1_out2, demultiplexer_1_out3,
       demultiplexer_1_out4, demultiplexer_1_out5, demultiplexer_1_out6, demultiplexer_1_out7,
       demultiplexer_1_out8, demultiplexer_1_out9, demultiplexer_1_out10, demultiplexer_1_out11,
       demultiplexer_1_out12, demultiplexer_1_out13, demultiplexer_1_out14, demultiplexer_1_out15,
       demultiplexer_1_out16, demultiplexer_1_out17, demultiplexer_1_out18, demultiplexer_1_out19,
       demultiplexer_1_out20, demultiplexer_1_out21, demultiplexer_1_out22, demultiplexer_1_out23,
       demultiplexer_1_out24, demultiplexer_1_out25, demultiplexer_1_out26, demultiplexer_1_out27,
       demultiplexer_1_out28, demultiplexer_1_out29, demultiplexer_1_out30, demultiplexer_1_out31;

  Demultiplexer #(.select(5), .enable("false")) demultiplexer_1 (
    .out0(demultiplexer_1_out0), .out1(demultiplexer_1_out1), .out2(demultiplexer_1_out2),
    .out3(demultiplexer_1_out3), .out4(demultiplexer_1_out4), .out5(demultiplexer_1_out5),
    .out6(demultiplexer_1_out6), .out7(demultiplexer_1_out7), .out8(demultiplexer_1_out8),
    .out9(demultiplexer_1_out9), .out10(demultiplexer_1_out10), .out11(demultiplexer_1_out11),
    .out12(demultiplexer_1_out12), .out13(demultiplexer_1_out13), .out14(demultiplexer_1_out14),
    .out15(demultiplexer_1_out15), .out16(demultiplexer_1_out16), .out17(demultiplexer_1_out17),
    .out18(demultiplexer_1_out18), .out19(demultiplexer_1_out19), .out20(demultiplexer_1_out20),
    .out21(demultiplexer_1_out21), .out22(demultiplexer_1_out22), .out23(demultiplexer_1_out23),
    .out24(demultiplexer_1_out24), .out25(demultiplexer_1_out25), .out26(demultiplexer_1_out26),
    .out27(demultiplexer_1_out27), .out28(demultiplexer_1_out28), .out29(demultiplexer_1_out29),
    .out30(demultiplexer_1_out30), .out31(demultiplexer_1_out31), .in(FLUSH), .sel(ADDR));
  Register register_1 (.D(WRITE_DATA), .en(demultiplexer_1_out1), .Q(R1), .clk(CLK), .clr(CLR));
  Register register_2 (.D(WRITE_DATA), .en(demultiplexer_1_out3), .Q(R3), .clk(CLK), .clr(CLR));
  Register register_3 (.D(WRITE_DATA), .en(demultiplexer_1_out5), .Q(R5), .clk(CLK), .clr(CLR));
  Register register_4 (.D(WRITE_DATA), .en(demultiplexer_1_out7), .Q(R7), .clk(CLK), .clr(CLR));
  Register register_5 (.D(WRITE_DATA), .en(demultiplexer_1_out9), .Q(R9), .clk(CLK), .clr(CLR));
  Register register_6 (.D(WRITE_DATA), .en(demultiplexer_1_out11), .Q(R11), .clk(CLK), .clr(CLR));
  Register register_7 (.D(WRITE_DATA), .en(demultiplexer_1_out13), .Q(R13), .clk(CLK), .clr(CLR));
  Register register_8 (.D(WRITE_DATA), .en(demultiplexer_1_out15), .Q(R15), .clk(CLK), .clr(CLR));
  Register register_9 (.D(WRITE_DATA), .en(demultiplexer_1_out17), .Q(R1_2), .clk(CLK), .clr(CLR));
  Register register_10 (.D(WRITE_DATA), .en(demultiplexer_1_out19), .Q(R3_2), .clk(CLK), .clr(CLR));
  Register register_11 (.D(WRITE_DATA), .en(demultiplexer_1_out21), .Q(R5_2), .clk(CLK), .clr(CLR));
  Register register_12 (.D(WRITE_DATA), .en(demultiplexer_1_out23), .Q(R7_2), .clk(CLK), .clr(CLR));
  Register register_13 (.D(WRITE_DATA), .en(demultiplexer_1_out25), .Q(R9_2), .clk(CLK), .clr(CLR));
  Register register_14 (.D(WRITE_DATA), .en(demultiplexer_1_out27), .Q(R11_2), .clk(CLK), .clr(CLR));
  Register register_15 (.D(WRITE_DATA), .en(demultiplexer_1_out29), .Q(R13_2), .clk(CLK), .clr(CLR));
  Register register_16 (.D(WRITE_DATA), .en(demultiplexer_1_out31), .Q(R15_2), .clk(CLK), .clr(CLR));
  Register register_17 (.D(WRITE_DATA), .en(demultiplexer_1_out0), .Q(R0), .clk(CLK), .clr(CLR));
  Register register_18 (.D(WRITE_DATA), .en(demultiplexer_1_out2), .Q(R2), .clk(CLK), .clr(CLR));
  Register register_19 (.D(WRITE_DATA), .en(demultiplexer_1_out4), .Q(R4), .clk(CLK), .clr(CLR));
  Register register_20 (.D(WRITE_DATA), .en(demultiplexer_1_out6), .Q(R6), .clk(CLK), .clr(CLR));
  Register register_21 (.D(WRITE_DATA), .en(demultiplexer_1_out8), .Q(R8), .clk(CLK), .clr(CLR));
  Register register_22 (.D(WRITE_DATA), .en(demultiplexer_1_out10), .Q(R10), .clk(CLK), .clr(CLR));
  Register register_23 (.D(WRITE_DATA), .en(demultiplexer_1_out12), .Q(R12), .clk(CLK), .clr(CLR));
  Register register_24 (.D(WRITE_DATA), .en(demultiplexer_1_out14), .Q(R14), .clk(CLK), .clr(CLR));
  Register register_25 (.D(WRITE_DATA), .en(demultiplexer_1_out16), .Q(R0_2), .clk(CLK), .clr(CLR));
  Register register_26 (.D(WRITE_DATA), .en(demultiplexer_1_out18), .Q(R2_2), .clk(CLK), .clr(CLR));
  Register register_27 (.D(WRITE_DATA), .en(demultiplexer_1_out20), .Q(R4_2), .clk(CLK), .clr(CLR));
  Register register_28 (.D(WRITE_DATA), .en(demultiplexer_1_out22), .Q(R6_2), .clk(CLK), .clr(CLR));
  Register register_29 (.D(WRITE_DATA), .en(demultiplexer_1_out24), .Q(R8_2), .clk(CLK), .clr(CLR));
  Register register_30 (.D(WRITE_DATA), .en(demultiplexer_1_out26), .Q(R10_2), .clk(CLK), .clr(CLR));
  Register register_31 (.D(WRITE_DATA), .en(demultiplexer_1_out28), .Q(R12_2), .clk(CLK), .clr(CLR));
  Register register_32 (.D(WRITE_DATA), .en(demultiplexer_1_out30), .Q(R14_2), .clk(CLK), .clr(CLR));

  // Other names for the same wires on the sheet: WD[7:0] = WRITE_DATA; WRITE = FLUSH
endmodule

module _32_x_16b_BUFFER (
  input  CLK,
  input  CLR,
  input  FLUSH,
  input  [15:0] R0,
  input  [15:0] R1,
  input  [15:0] R2,
  input  [15:0] R3,
  input  [15:0] R4,
  input  [15:0] R5,
  input  [15:0] R6,
  input  [15:0] R7,
  input  [15:0] R8,
  input  [15:0] R9,
  input  [15:0] R10,
  input  [15:0] R11,
  input  [15:0] R12,
  input  [15:0] R13,
  input  [15:0] R14,
  input  [15:0] R15,
  input  [15:0] R0_2,
  input  [15:0] R1_2,
  input  [15:0] R2_2,
  input  [15:0] R3_2,
  input  [15:0] R4_2,
  input  [15:0] R5_2,
  input  [15:0] R6_2,
  input  [15:0] R7_2,
  input  [15:0] R8_2,
  input  [15:0] R9_2,
  input  [15:0] R10_2,
  input  [15:0] R11_2,
  input  [15:0] R12_2,
  input  [15:0] R13_2,
  input  [15:0] R14_2,
  input  [15:0] R15_2,
  output [15:0] R0_3,
  output [15:0] R1_3,
  output [15:0] R2_3,
  output [15:0] R3_3,
  output [15:0] R4_3,
  output [15:0] R5_3,
  output [15:0] R6_3,
  output [15:0] R7_3,
  output [15:0] R8_3,
  output [15:0] R9_3,
  output [15:0] R10_3,
  output [15:0] R11_3,
  output [15:0] R12_3,
  output [15:0] R13_3,
  output [15:0] R14_3,
  output [15:0] R15_3,
  output [15:0] R0_4,
  output [15:0] R1_4,
  output [15:0] R2_4,
  output [15:0] R3_4,
  output [15:0] R4_4,
  output [15:0] R5_4,
  output [15:0] R6_4,
  output [15:0] R7_4,
  output [15:0] R8_4,
  output [15:0] R9_4,
  output [15:0] R10_4,
  output [15:0] R11_4,
  output [15:0] R12_4,
  output [15:0] R13_4,
  output [15:0] R14_4,
  output [15:0] R15_4
);

  Register #(.width(16)) register_1 (.D(R1), .en(FLUSH), .Q(R1_3), .clk(CLK), .clr(CLR));
  Register #(.width(16)) register_2 (.D(R3), .en(FLUSH), .Q(R3_3), .clk(CLK), .clr(CLR));
  Register #(.width(16)) register_3 (.D(R5), .en(FLUSH), .Q(R5_3), .clk(CLK), .clr(CLR));
  Register #(.width(16)) register_4 (.D(R7), .en(FLUSH), .Q(R7_3), .clk(CLK), .clr(CLR));
  Register #(.width(16)) register_5 (.D(R9), .en(FLUSH), .Q(R9_3), .clk(CLK), .clr(CLR));
  Register #(.width(16)) register_6 (.D(R11), .en(FLUSH), .Q(R11_3), .clk(CLK), .clr(CLR));
  Register #(.width(16)) register_7 (.D(R13), .en(FLUSH), .Q(R13_3), .clk(CLK), .clr(CLR));
  Register #(.width(16)) register_8 (.D(R15), .en(FLUSH), .Q(R15_3), .clk(CLK), .clr(CLR));
  Register #(.width(16)) register_9 (.D(R1_2), .en(FLUSH), .Q(R1_4), .clk(CLK), .clr(CLR));
  Register #(.width(16)) register_10 (.D(R3_2), .en(FLUSH), .Q(R3_4), .clk(CLK), .clr(CLR));
  Register #(.width(16)) register_11 (.D(R5_2), .en(FLUSH), .Q(R5_4), .clk(CLK), .clr(CLR));
  Register #(.width(16)) register_12 (.D(R7_2), .en(FLUSH), .Q(R7_4), .clk(CLK), .clr(CLR));
  Register #(.width(16)) register_13 (.D(R9_2), .en(FLUSH), .Q(R9_4), .clk(CLK), .clr(CLR));
  Register #(.width(16)) register_14 (.D(R11_2), .en(FLUSH), .Q(R11_4), .clk(CLK), .clr(CLR));
  Register #(.width(16)) register_15 (.D(R13_2), .en(FLUSH), .Q(R13_4), .clk(CLK), .clr(CLR));
  Register #(.width(16)) register_16 (.D(R15_2), .en(FLUSH), .Q(R15_4), .clk(CLK), .clr(CLR));
  Register #(.width(16)) register_17 (.D(R0), .en(FLUSH), .Q(R0_3), .clk(CLK), .clr(CLR));
  Register #(.width(16)) register_18 (.D(R2), .en(FLUSH), .Q(R2_3), .clk(CLK), .clr(CLR));
  Register #(.width(16)) register_19 (.D(R4), .en(FLUSH), .Q(R4_3), .clk(CLK), .clr(CLR));
  Register #(.width(16)) register_20 (.D(R6), .en(FLUSH), .Q(R6_3), .clk(CLK), .clr(CLR));
  Register #(.width(16)) register_21 (.D(R8), .en(FLUSH), .Q(R8_3), .clk(CLK), .clr(CLR));
  Register #(.width(16)) register_22 (.D(R10), .en(FLUSH), .Q(R10_3), .clk(CLK), .clr(CLR));
  Register #(.width(16)) register_23 (.D(R12), .en(FLUSH), .Q(R12_3), .clk(CLK), .clr(CLR));
  Register #(.width(16)) register_24 (.D(R14), .en(FLUSH), .Q(R14_3), .clk(CLK), .clr(CLR));
  Register #(.width(16)) register_25 (.D(R0_2), .en(FLUSH), .Q(R0_4), .clk(CLK), .clr(CLR));
  Register #(.width(16)) register_26 (.D(R2_2), .en(FLUSH), .Q(R2_4), .clk(CLK), .clr(CLR));
  Register #(.width(16)) register_27 (.D(R4_2), .en(FLUSH), .Q(R4_4), .clk(CLK), .clr(CLR));
  Register #(.width(16)) register_28 (.D(R6_2), .en(FLUSH), .Q(R6_4), .clk(CLK), .clr(CLR));
  Register #(.width(16)) register_29 (.D(R8_2), .en(FLUSH), .Q(R8_4), .clk(CLK), .clr(CLR));
  Register #(.width(16)) register_30 (.D(R10_2), .en(FLUSH), .Q(R10_4), .clk(CLK), .clr(CLR));
  Register #(.width(16)) register_31 (.D(R12_2), .en(FLUSH), .Q(R12_4), .clk(CLK), .clr(CLR));
  Register #(.width(16)) register_32 (.D(R14_2), .en(FLUSH), .Q(R14_4), .clk(CLK), .clr(CLR));

  // Other names for the same wires on the sheet: WRITE = FLUSH
endmodule
