// Logisim project MIPS_COMPLETE_TEMP.circ as structural Verilog: 19 circuits, main circuit Pipelined
module Pipelined (
  input  RESET
);

  wire ALU_SRC, BEQ, BNEQ, BRANCH, Branch_FWD_Stall, Branch_Load_Use_Stall, BRANCH_PC_SRC, CLK,
       cntrl_1_alusrc, cntrl_1_memread, cntrl_1_memtoreg, cntrl_1_memwrite, cntrl_1_regdst, cntrl_1_regwrite,
       comparator_1_eq, ex_mem_1_mem_to_reg_2, EX_MEM_REG_WRITE, id_ex_1_mem_to_reg_2, id_ex_1_mem_write_2,
       ID_EX_MEM_READ, ID_EX_REG_WRITE, JUMP_PC_SRC, Load_Use_Stall, MEM_READ, MEM_TO_REG, MEM_WB_REG_WRITE,
       MEM_WRITE, or_1_out, or_2_out, or_3_out, or_4_out, REG_DEST;
  wire [1:0] Branch_FWD_A, Branch_FWD_B, forwarding_unit_1_forward_a, forwarding_unit_1_forward_b;
  wire [2:0] ALU_OP, cntrl_1_aluop;
  wire [3:0] EX_MEM_RD, id_1_dest, id_1_opcode, id_1_src_1, id_1_src_2, id_ex_1_src_1_2, id_ex_1_src_2_2,
       ID_EX_RD, ID_EX_RT, MEM_WB_RD;
  wire [7:0] alu_8_by_art_1_p4, Branch_PC, ex_mem_1_reg_data_2_2, EX_MEM_RegData, id_1_addr___immd,
       id_ex_1_reg_data_1_2, id_ex_1_reg_data_2_2, ID_EX_IMM, if_1_pc___1, if_1_pc_read, if_id_1_pc_2,
       Jump_Address, mem_1_data_read, mem_wb_1_alu_result_2, mem_wb_1_reg_data_2_2, MEM_WB_RegData,
       multiplexer_1_out, multiplexer_2_out, multiplexer_3_out, multiplexer_4_out, multiplexer_6_out,
       multiplexer_7_out, multiplexer_8_out, reg_file_1_readdata1, reg_file_1_readdata2;
  wire [19:0] if_1_instruction, if_id_1_instruction_2;
  wire [23:0] R10S, R432;

  Clock u_CLK (.out(CLK));
  Multiplexer #(.width(8), .enable("false")) multiplexer_1 (
    .in0(multiplexer_2_out), .in1(Jump_Address), .out(multiplexer_1_out), .sel(JUMP_PC_SRC));
  or or_1 (or_1_out, Branch_FWD_Stall, Load_Use_Stall, Branch_Load_Use_Stall);
  Multiplexer #(.width(8), .enable("false")) multiplexer_2 (
    .in0(if_1_pc___1), .in1(Branch_PC), .out(multiplexer_2_out), .sel(BRANCH_PC_SRC));
  IF if_1 (
    .PC_Write(multiplexer_1_out), .CLK(CLK), .RESET(RESET), .PC_Read(if_1_pc_read),
    .Instruction(if_1_instruction), .PC___1(if_1_pc___1), .Stall(or_1_out));
  // Probe on if_1_instruction
  // Probe on R10S[15:8]
  // Probe on R10S[23:16]
  // Probe on R432[7:0]
  // Probe on R432[15:8]
  // Probe on R432[23:16]
  // Probe on R10S[7:0]
  // Probe on if_1_pc_read
  or or_2 (or_2_out, BRANCH_PC_SRC, JUMP_PC_SRC);
  or or_3 (or_3_out, Branch_FWD_Stall, Load_Use_Stall, Branch_Load_Use_Stall);
  IF_ID if_id_1 (
    .Instruction(if_1_instruction), .Instruction_2(if_id_1_instruction_2), .PC(if_1_pc___1),
    .PC_2(if_id_1_pc_2), .CLK(CLK), .CLR(RESET), .Stall(or_3_out), .FLUSH(or_2_out));
  // Probe on if_id_1_instruction_2
  // Probe on id_1_opcode
  ID id_1 (
    .Instruction(if_id_1_instruction_2), .Opcode(id_1_opcode), .Src_1(id_1_src_1), .Src_2(id_1_src_2),
    .Dest(id_1_dest), .Addr___Immd(id_1_addr___immd), .Jump_Addr(Jump_Address));
  BRANCH_FORWARDING_UNIT branch_forwarding_unit_1 (
    .IF_ID_RegisterRs(id_1_src_1), .IF_ID_RegisterRt(id_1_src_2), .EX_MEM_RegisterRd(EX_MEM_RD),
    .EX_MEM_RegWrite(EX_MEM_REG_WRITE), .MEM_WB_RegisterRd(MEM_WB_RD), .MEM_WB_RegWrite(MEM_WB_REG_WRITE),
    .Forward_A(Branch_FWD_A), .Forward_B(Branch_FWD_B), .ID_EX_RegWrite(ID_EX_REG_WRITE),
    .ID_EX_RegisterRd(ID_EX_RD), .Stall(Branch_FWD_Stall), .Is_Branch(BRANCH));
  Adder adder_1 (.a(if_id_1_pc_2), .b(id_1_addr___immd), .out(Branch_PC));  // open: cin, cout
  or or_4 (or_4_out, Branch_FWD_Stall, Load_Use_Stall, Branch_Load_Use_Stall);
  CNTRL cntrl_1 (
    .OP_Code(id_1_opcode), .RegDst(cntrl_1_regdst), .ALUSrc(cntrl_1_alusrc), .MemToReg(cntrl_1_memtoreg),
    .RegWrite(cntrl_1_regwrite), .MemRead(cntrl_1_memread), .MemWrite(cntrl_1_memwrite), .beq(BEQ),
    .bneq(BNEQ), .Jump(JUMP_PC_SRC), .ALUOp(cntrl_1_aluop), .NOP(or_4_out));
  REG_FILE reg_file_1 (
    .Src_1(id_1_src_1), .Src_2(id_1_src_2), .WriteData(MEM_WB_RegData), .CLK(CLK), .CLR(RESET),
    .t4__t3__t2(R432), .t1__t0__sp(R10S), .ReadData1(reg_file_1_readdata1), .ReadData2(reg_file_1_readdata2),
    .Dest_1(MEM_WB_RD), .RegWrite(MEM_WB_REG_WRITE));
  LOAD_USE_HAZARD load_use_hazard_1 (
    .ID_EX_MemRead(ID_EX_MEM_READ), .ID_EX_RegisterRt(ID_EX_RT), .IF_ID_RegisterRs(id_1_src_1),
    .IF_ID_RegisterRt(id_1_src_2), .Hazard(Load_Use_Stall));
  or or_5 (BRANCH, BNEQ, BEQ);
  Multiplexer #(.select(2), .width(8), .enable("false")) multiplexer_3 (
    .in0(reg_file_1_readdata1), .in1(MEM_WB_RegData), .in2(EX_MEM_RegData), .out(multiplexer_3_out),
    .sel(Branch_FWD_A));  // open: in3
  Multiplexer #(.select(2), .width(8), .enable("false")) multiplexer_4 (
    .in0(reg_file_1_readdata2), .in1(MEM_WB_RegData), .in2(EX_MEM_RegData), .out(multiplexer_4_out),
    .sel(Branch_FWD_B));  // open: in3
  Multiplexer #(.enable("false")) multiplexer_5 (.in0(BNEQ), .in1(BEQ), .out(BRANCH_PC_SRC), .sel(comparator_1_eq));
  Comparator comparator_1 (.a(multiplexer_3_out), .b(multiplexer_4_out), .eq(comparator_1_eq));  // open: gt, lt
  BRANCH_LOAD_USE_HAZARD branch_load_use_hazard_1 (
    .ID_EX_MemRead(ID_EX_MEM_READ), .ID_EX_RegisterRt(ID_EX_RT), .IF_ID_RegisterRs(id_1_src_1),
    .IF_ID_RegisterRt(id_1_src_2), .Hazard(Branch_Load_Use_Stall), .CLK(CLK), .Is_Branch(BRANCH));
  ID_EX id_ex_1 (
    .Reg_Data_1(reg_file_1_readdata1), .Reg_Data_2(reg_file_1_readdata2), .IMM(id_1_addr___immd),
    .DEST_REG(id_1_src_2), .CLK(CLK), .CLR(RESET), .Reg_Data_1_2(id_ex_1_reg_data_1_2),
    .Reg_Data_2_2(id_ex_1_reg_data_2_2), .IMM_2(ID_EX_IMM), .DEST_REG_2(ID_EX_RT), .SRC_2(id_1_dest),
    .SRC_2_2(id_ex_1_src_2_2), .SRC_1(id_1_src_1), .SRC_1_2(id_ex_1_src_1_2), .MEM_READ(cntrl_1_memread),
    .MEM_READ_2(ID_EX_MEM_READ), .MEM_WRITE(cntrl_1_memwrite), .MEM_WRITE_2(id_ex_1_mem_write_2),
    .MEM_TO_REG(cntrl_1_memtoreg), .MEM_TO_REG_2(id_ex_1_mem_to_reg_2), .REG_WRITE(cntrl_1_regwrite),
    .REG_WRITE_2(ID_EX_REG_WRITE), .out_20(ALU_OP), .in_1(cntrl_1_aluop), .in_2(cntrl_1_alusrc),
    .out_21(ALU_SRC), .in_3(cntrl_1_regdst), .out_22(REG_DEST));  // open: PC, PC_2, BNEQ, BNEQ_2, BEQ, BEQ_2, JUMP, JUMP_2
  Multiplexer #(.select(2), .width(8), .enable("false")) multiplexer_6 (
    .in0(id_ex_1_reg_data_1_2), .in1(MEM_WB_RegData), .in2(EX_MEM_RegData), .out(multiplexer_6_out),
    .sel(forwarding_unit_1_forward_a));  // open: in3
  Multiplexer #(.select(2), .width(8), .enable("false")) multiplexer_7 (
    .in0(id_ex_1_reg_data_2_2), .in1(MEM_WB_RegData), .in2(EX_MEM_RegData), .out(multiplexer_7_out),
    .sel(forwarding_unit_1_forward_b));  // open: in3
  // Probe on forwarding_unit_1_forward_b
  // Probe on forwarding_unit_1_forward_a
  FORWARDING_UNIT forwarding_unit_1 (
    .ID_EX_RegisterRs(id_ex_1_src_1_2), .ID_EX_RegisterRt(ID_EX_RT), .EX_MEM_RegisterRd(EX_MEM_RD),
    .EX_MEM_RegWrite(EX_MEM_REG_WRITE), .MEM_WB_RegisterRd(MEM_WB_RD), .MEM_WB_RegWrite(MEM_WB_REG_WRITE),
    .Forward_A(forwarding_unit_1_forward_a), .Forward_B(forwarding_unit_1_forward_b));
  Multiplexer #(.width(8), .enable("false")) multiplexer_8 (
    .in0(multiplexer_7_out), .in1(ID_EX_IMM), .out(multiplexer_8_out), .sel(ALU_SRC));
  // ALU_8_by_ART alu_8_by_art_1: pin names not known; wires that end beside it: multiplexer_6_out, multiplexer_8_out, ALU_OP, alu_8_by_art_1_p4
  Multiplexer #(.width(4), .enable("false")) multiplexer_9 (
    .in0(ID_EX_RT), .in1(id_ex_1_src_2_2), .out(ID_EX_RD), .sel(REG_DEST));
  EX_MEM ex_mem_1 (
    .REG_WRITE(ID_EX_REG_WRITE), .ALU_RESULT(alu_8_by_art_1_p4), .WRITE_REG(ID_EX_RD), .CLK(CLK),
    .CLR(RESET), .ALU_RESULT_2(EX_MEM_RegData), .WRITE_REG_2(EX_MEM_RD), .Reg_Data_2(multiplexer_7_out),
    .Reg_Data_2_2(ex_mem_1_reg_data_2_2), .MEM_TO_REG(id_ex_1_mem_to_reg_2), .MEM_WRITE(id_ex_1_mem_write_2),
    .MEM_READ(ID_EX_MEM_READ), .MEM_READ_2(MEM_READ), .MEM_WRITE_2(MEM_WRITE),
    .MEM_TO_REG_2(ex_mem_1_mem_to_reg_2), .REG_WRITE_2(EX_MEM_REG_WRITE));  // open: JUMP, BNEQ, BEQ, ZERO, BNEQ_2, BEQ_2, JUMP_2, ZERO_2, PC, PC_2
  MEM mem_1 (
    .Address(EX_MEM_RegData), .WriteData(ex_mem_1_reg_data_2_2), .Data_Read(mem_1_data_read),
    .MemWrite(MEM_WRITE), .CLK(CLK), .MemRead(MEM_READ), .CLR(RESET));
  MEM_WB mem_wb_1 (
    .ALU_RESULT(EX_MEM_RegData), .Reg_Data_2(mem_1_data_read), .CLK(CLK), .CLR(RESET),
    .ALU_RESULT_2(mem_wb_1_alu_result_2), .Reg_Data_2_2(mem_wb_1_reg_data_2_2),
    .MEM_TO_REG(ex_mem_1_mem_to_reg_2), .MEM_TO_REG_2(MEM_TO_REG), .REG_WRITE(EX_MEM_REG_WRITE),
    .REG_WRITE_2(MEM_WB_REG_WRITE), .WRITE_REG(EX_MEM_RD), .WRITE_REG_2(MEM_WB_RD));
  Multiplexer #(.width(8), .enable("false")) multiplexer_10 (
    .in0(mem_wb_1_alu_result_2), .in1(mem_wb_1_reg_data_2_2), .out(MEM_WB_RegData), .sel(MEM_TO_REG));

  // Other names for the same wires on the sheet: CLR = RESET

  // Notes on the sheet:
  //   FULL CAPITAL NAME -----> Control Flags
endmodule

module IF (
  input  [7:0] PC_Write,
  input  Stall,
  input  CLK,
  input  RESET,
  output [7:0] PC_Read,
  output [7:0] PC___1,
  output [19:0] Instruction
);

  wire not_1_out;

  Register register_1 (.D(PC_Write), .en(not_1_out), .Q(PC_Read), .clk(CLK), .clr(RESET));
  not not_1 (not_1_out, Stall);
  Adder adder_1 (.a(PC_Read), .b(8'h1), .out(PC___1), .cin(1'b0));  // open: cout
  ROM #(.dataWidth(20)) rom_1 (.addr(PC_Read), .data(Instruction), .sel(1'b1));

  // Notes on the sheet:
  //   contents of rom_1 (hex, n*v repeats v):
  //   a06ff a0501 a0102 0 0 0 80500 0 0 0 d0200 80201
endmodule

module ID (
  input  [19:0] Instruction,
  output [3:0] Opcode,
  output [3:0] Src_1,
  output [3:0] Src_2,
  output [3:0] Dest,
  output [7:0] Addr___Immd,
  output [7:0] Jump_Addr
);


  assign Addr___Immd = Instruction[7:0];
  assign Dest = Instruction[7:4];
  assign Jump_Addr = Instruction[15:8];
  assign Opcode = Instruction[19:16];
  assign Src_1 = Instruction[15:12];
  assign Src_2 = Instruction[11:8];

  // Notes on the sheet:
  //   Shift Amt
endmodule

module REG_FILE (
  input  RegWrite,
  input  [3:0] Dest_1,
  input  [3:0] Src_1,
  input  [3:0] Src_2,
  input  [7:0] WriteData,
  input  CLK,
  input  CLR,
  output [23:0] t4__t3__t2,
  output [23:0] t1__t0__sp,
  output [7:0] ReadData1,
  output [7:0] ReadData2
);

  wire and_1_out, and_2_out, comparator_1_eq, comparator_2_eq, comparator_3_eq, comparator_4_eq,
       demultiplexer_1_out1, demultiplexer_1_out2, demultiplexer_1_out3, demultiplexer_1_out4,
       demultiplexer_1_out5, demultiplexer_1_out6, not_1_out, not_2_out;
  wire [2:0] bit_extender_1_out, bit_extender_2_out, bit_extender_3_out;
  wire [7:0] multiplexer_1_out, multiplexer_3_out;

  Comparator #(.width(4), .mode("unsigned")) comparator_1 (
    .a(Dest_1), .b(Src_1), .eq(comparator_1_eq));  // open: gt, lt
  Comparator #(.width(4), .mode("unsigned")) comparator_2 (
    .a(Dest_1), .b(4'b0000), .eq(comparator_2_eq));  // open: gt, lt
  Register t1 (.D(WriteData), .en(demultiplexer_1_out1), .Q(t1__t0__sp[23:16]), .clk(CLK), .clr(CLR));
  Bit_Extender #(.in_width(4), .out_width(3)) bit_extender_1 (.in(Src_1), .out(bit_extender_1_out));
  and and_1 (and_1_out, comparator_1_eq, RegWrite, not_1_out);
  not not_1 (not_1_out, comparator_2_eq);
  Bit_Extender #(.in_width(4), .out_width(3)) bit_extender_2 (.in(Dest_1), .out(bit_extender_2_out));
  Register t2 (.D(WriteData), .en(demultiplexer_1_out2), .Q(t4__t3__t2[7:0]), .clk(CLK), .clr(CLR));
  Multiplexer #(.select(3), .width(8), .enable("false")) multiplexer_1 (
    .in0({8{1'b0}}), .in1(t1__t0__sp[23:16]), .in2(t4__t3__t2[7:0]), .in3(t4__t3__t2[15:8]),
    .in4(t4__t3__t2[23:16]), .in5(t1__t0__sp[15:8]), .in6(t1__t0__sp[7:0]), .out(multiplexer_1_out),
    .sel(bit_extender_1_out));  // open: in7
  Multiplexer #(.width(8), .enable("false")) multiplexer_2 (
    .in0(multiplexer_1_out), .in1(WriteData), .out(ReadData1), .sel(and_1_out));
  Demultiplexer #(.select(3), .enable("false")) demultiplexer_1 (
    .out1(demultiplexer_1_out1), .out2(demultiplexer_1_out2), .out3(demultiplexer_1_out3),
    .out4(demultiplexer_1_out4), .out5(demultiplexer_1_out5), .out6(demultiplexer_1_out6), .in(RegWrite),
    .sel(bit_extender_2_out));  // open: out0, out7
  Register t3 (.D(WriteData), .en(demultiplexer_1_out3), .Q(t4__t3__t2[15:8]), .clk(CLK), .clr(CLR));
  Register t4 (.D(WriteData), .en(demultiplexer_1_out4), .Q(t4__t3__t2[23:16]), .clk(CLK), .clr(CLR));
  Bit_Extender #(.in_width(4), .out_width(3)) bit_extender_3 (.in(Src_2), .out(bit_extender_3_out));
  Comparator #(.width(4), .mode("unsigned")) comparator_3 (
    .a(Dest_1), .b(Src_2), .eq(comparator_3_eq));  // open: gt, lt
  not not_2 (not_2_out, comparator_4_eq);
  Comparator #(.width(4), .mode("unsigned")) comparator_4 (
    .a(Dest_1), .b(4'b0000), .eq(comparator_4_eq));  // open: gt, lt
  Register t0 (.D(WriteData), .en(demultiplexer_1_out5), .Q(t1__t0__sp[15:8]), .clk(CLK), .clr(CLR));
  Multiplexer #(.select(3), .width(8), .enable("false")) multiplexer_3 (
    .in0({8{1'b0}}), .in1(t1__t0__sp[23:16]), .in2(t4__t3__t2[7:0]), .in3(t4__t3__t2[15:8]),
    .in4(t4__t3__t2[23:16]), .in5(t1__t0__sp[15:8]), .in6(t1__t0__sp[7:0]), .out(multiplexer_3_out),
    .sel(bit_extender_3_out));  // open: in7
  and and_2 (and_2_out, comparator_3_eq, RegWrite, not_2_out);
  Multiplexer #(.width(8), .enable("false")) multiplexer_4 (
    .in0(multiplexer_3_out), .in1(WriteData), .out(ReadData2), .sel(and_2_out));
  Register sp (.D(WriteData), .en(demultiplexer_1_out6), .Q(t1__t0__sp[7:0]), .clk(CLK), .clr(CLR));

  // Other names for the same wires on the sheet: D1[3:0] = Dest_1; READ_DATA_1[7:0] = ReadData1;
  //   READ_DATA_2[7:0] = ReadData2; S1[3:0] = Src_1; S2[3:0] = Src_2; WD[7:0] = WriteData

  // Notes on the sheet:
  //   Registers typically write on rising edge and reads on falling edge. But in logsim we have no way (at least IDK) to control when to read.
  //   So what we are doing here is we are checking if the register we are trying to read is also getting updated if so we just pass the new value of it using MUX.
  //   But we must be careful to not pass it when reading or writing to zero register. Also the write register flag should be checked.
endmodule

module MEM (
  input  [7:0] Address,
  input  [7:0] WriteData,
  input  CLK,
  input  CLR,
  input  MemWrite,
  input  MemRead,
  output [7:0] Data_Read
);

  RAM #(.bus("separate")) ram_1 (
    .addr(Address), .din(WriteData), .data(Data_Read), .str(MemWrite), .sel(1'b1), .clk(CLK), .ld(MemRead),
    .clr(CLR));
endmodule

module CNTRL (
  input  [3:0] OP_Code,
  input  NOP,
  output RegDst,
  output ALUSrc,
  output MemToReg,
  output RegWrite,
  output MemRead,
  output MemWrite,
  output beq,
  output bneq,
  output Jump,
  output [2:0] ALUOp
);

  wire [11:0] rom_1_data;

  ROM #(.addrWidth(4), .dataWidth(12)) rom_1 (.addr(OP_Code), .data(rom_1_data), .sel(1'b1));
  Multiplexer #(.width(12), .enable("false")) multiplexer_1 (
    .in0(rom_1_data), .in1({12{1'b0}}),
    .out({RegDst, ALUSrc, MemToReg, RegWrite, MemRead, MemWrite, beq, bneq, Jump, ALUOp}), .sel(NOP));

  // Notes on the sheet:
  //   contents of rom_1 (hex, n*v repeats v):
  //   901 506 503 502 904 11 903 21 c40 501 500 505 900 780 902 8
endmodule

module IF_ID (
  input  Stall,
  input  [7:0] PC,
  input  [19:0] Instruction,
  input  CLK,
  input  CLR,
  input  FLUSH,
  output [7:0] PC_2,
  output [19:0] Instruction_2
);

  wire EnableWrite;
  wire [7:0] multiplexer_1_out;
  wire [19:0] multiplexer_2_out;

  Multiplexer #(.width(8), .enable("false")) multiplexer_1 (
    .in0(PC), .in1({8{1'b0}}), .out(multiplexer_1_out), .sel(FLUSH));
  Multiplexer #(.width(20), .enable("false")) multiplexer_2 (
    .in0(Instruction), .in1({20{1'b0}}), .out(multiplexer_2_out), .sel(FLUSH));
  not not_1 (EnableWrite, Stall);
  Register u_PC (.D(multiplexer_1_out), .en(EnableWrite), .Q(PC_2), .clk(CLK), .clr(CLR));
  Register #(.width(20)) IF_ID_REG (.D(multiplexer_2_out), .en(EnableWrite), .Q(Instruction_2), .clk(CLK), .clr(CLR));
endmodule

module ID_EX (
  input  [2:0] in_1,
  input  in_2,
  input  in_3,
  input  MEM_READ,
  input  MEM_WRITE,
  input  BNEQ,
  input  BEQ,
  input  JUMP,
  input  MEM_TO_REG,
  input  REG_WRITE,
  input  [7:0] PC,
  input  [7:0] Reg_Data_1,
  input  [7:0] Reg_Data_2,
  input  [7:0] IMM,
  input  [3:0] SRC_1,
  input  [3:0] SRC_2,
  input  [3:0] DEST_REG,
  input  CLK,
  input  CLR,
  output [2:0] out_20,
  output out_21,
  output out_22,
  output MEM_READ_2,
  output MEM_WRITE_2,
  output BNEQ_2,
  output BEQ_2,
  output JUMP_2,
  output MEM_TO_REG_2,
  output REG_WRITE_2,
  output [7:0] PC_2,
  output [7:0] Reg_Data_1_2,
  output [7:0] Reg_Data_2_2,
  output [7:0] IMM_2,
  output [3:0] SRC_1_2,
  output [3:0] SRC_2_2,
  output [3:0] DEST_REG_2
);

  Register #(.width(3)) ALUOp (.D(in_1), .en(1'b1), .Q(out_20), .clk(CLK), .clr(CLR));
  Register #(.width(1)) ALUSrc (.D(in_2), .en(1'b1), .Q(out_21), .clk(CLK), .clr(CLR));
  Register #(.width(1)) RegDest (.D(in_3), .en(1'b1), .Q(out_22), .clk(CLK), .clr(CLR));
  Register #(.width(1)) u_MEM_READ (.D(MEM_READ), .en(1'b1), .Q(MEM_READ_2), .clk(CLK), .clr(CLR));
  Register #(.width(1)) u_MEM_WRITE (.D(MEM_WRITE), .en(1'b1), .Q(MEM_WRITE_2), .clk(CLK), .clr(CLR));
  Register #(.width(1)) u_BNEQ (.D(BNEQ), .en(1'b1), .Q(BNEQ_2), .clk(CLK), .clr(CLR));
  Register #(.width(1)) u_BEQ (.D(BEQ), .en(1'b1), .Q(BEQ_2), .clk(CLK), .clr(CLR));
  Register #(.width(1)) u_JUMP (.D(JUMP), .en(1'b1), .Q(JUMP_2), .clk(CLK), .clr(CLR));
  Register #(.width(1)) u_MEM_TO_REG (.D(MEM_TO_REG), .en(1'b1), .Q(MEM_TO_REG_2), .clk(CLK), .clr(CLR));
  Register #(.width(1)) u_REG_WRITE (.D(REG_WRITE), .en(1'b1), .Q(REG_WRITE_2), .clk(CLK), .clr(CLR));
  Register u_PC (.D(PC), .en(1'b1), .Q(PC_2), .clk(CLK), .clr(CLR));
  Register u_Reg_Data_1 (.D(Reg_Data_1), .en(1'b1), .Q(Reg_Data_1_2), .clk(CLK), .clr(CLR));
  Register u_Reg_Data_2 (.D(Reg_Data_2), .en(1'b1), .Q(Reg_Data_2_2), .clk(CLK), .clr(CLR));
  Register u_IMM (.D(IMM), .en(1'b1), .Q(IMM_2), .clk(CLK), .clr(CLR));
  Register #(.width(4)) u_SRC_1 (.D(SRC_1), .en(1'b1), .Q(SRC_1_2), .clk(CLK), .clr(CLR));
  Register #(.width(4)) u_SRC_2 (.D(SRC_2), .en(1'b1), .Q(SRC_2_2), .clk(CLK), .clr(CLR));
  Register #(.width(4)) u_DEST_REG (.D(DEST_REG), .en(1'b1), .Q(DEST_REG_2), .clk(CLK), .clr(CLR));
endmodule

module EX_MEM (
  input  MEM_READ,
  input  MEM_WRITE,
  input  BNEQ,
  input  BEQ,
  input  JUMP,
  input  MEM_TO_REG,
  input  REG_WRITE,
  input  [7:0] PC,
  input  ZERO,
  input  [7:0] ALU_RESULT,
  input  [7:0] Reg_Data_2,
  input  [3:0] WRITE_REG,
  input  CLK,
  input  CLR,
  output MEM_READ_2,
  output MEM_WRITE_2,
  output BNEQ_2,
  output BEQ_2,
  output JUMP_2,
  output MEM_TO_REG_2,
  output REG_WRITE_2,
  output [7:0] PC_2,
  output ZERO_2,
  output [7:0] ALU_RESULT_2,
  output [7:0] Reg_Data_2_2,
  output [3:0] WRITE_REG_2
);

  Register #(.width(1)) u_MEM_READ (.D(MEM_READ), .en(1'b1), .Q(MEM_READ_2), .clk(CLK), .clr(CLR));
  Register #(.width(1)) u_MEM_WRITE (.D(MEM_WRITE), .en(1'b1), .Q(MEM_WRITE_2), .clk(CLK), .clr(CLR));
  Register #(.width(1)) u_BNEQ (.D(BNEQ), .en(1'b1), .Q(BNEQ_2), .clk(CLK), .clr(CLR));
  Register #(.width(1)) u_BEQ (.D(BEQ), .en(1'b1), .Q(BEQ_2), .clk(CLK), .clr(CLR));
  Register #(.width(1)) u_JUMP (.D(JUMP), .en(1'b1), .Q(JUMP_2), .clk(CLK), .clr(CLR));
  Register #(.width(1)) u_MEM_TO_REG (.D(MEM_TO_REG), .en(1'b1), .Q(MEM_TO_REG_2), .clk(CLK), .clr(CLR));
  Register #(.width(1)) u_REG_WRITE (.D(REG_WRITE), .en(1'b1), .Q(REG_WRITE_2), .clk(CLK), .clr(CLR));
  Register u_PC (.D(PC), .en(1'b1), .Q(PC_2), .clk(CLK), .clr(CLR));
  Register #(.width(1)) u_ZERO (.D(ZERO), .en(1'b1), .Q(ZERO_2), .clk(CLK), .clr(CLR));
  Register u_ALU_RESULT (.D(ALU_RESULT), .en(1'b1), .Q(ALU_RESULT_2), .clk(CLK), .clr(CLR));
  Register u_Reg_Data_2 (.D(Reg_Data_2), .en(1'b1), .Q(Reg_Data_2_2), .clk(CLK), .clr(CLR));
  Register #(.width(4)) u_WRITE_REG (.D(WRITE_REG), .en(1'b1), .Q(WRITE_REG_2), .clk(CLK), .clr(CLR));
endmodule

module MEM_WB (
  input  MEM_TO_REG,
  input  REG_WRITE,
  input  [7:0] ALU_RESULT,
  input  [7:0] Reg_Data_2,
  input  [3:0] WRITE_REG,
  input  CLK,
  input  CLR,
  output MEM_TO_REG_2,
  output REG_WRITE_2,
  output [7:0] ALU_RESULT_2,
  output [7:0] Reg_Data_2_2,
  output [3:0] WRITE_REG_2
);

  Register #(.width(1)) u_MEM_TO_REG (.D(MEM_TO_REG), .en(1'b1), .Q(MEM_TO_REG_2), .clk(CLK), .clr(CLR));
  Register #(.width(1)) u_REG_WRITE (.D(REG_WRITE), .en(1'b1), .Q(REG_WRITE_2), .clk(CLK), .clr(CLR));
  Register u_ALU_RESULT (.D(ALU_RESULT), .en(1'b1), .Q(ALU_RESULT_2), .clk(CLK), .clr(CLR));
  Register u_Reg_Data_2 (.D(Reg_Data_2), .en(1'b1), .Q(Reg_Data_2_2), .clk(CLK), .clr(CLR));
  Register #(.width(4)) u_WRITE_REG (.D(WRITE_REG), .en(1'b1), .Q(WRITE_REG_2), .clk(CLK), .clr(CLR));
endmodule

module FORWARDING_UNIT (
  input  [3:0] ID_EX_RegisterRs,
  input  [3:0] ID_EX_RegisterRt,
  input  [3:0] EX_MEM_RegisterRd,
  input  EX_MEM_RegWrite,
  input  [3:0] MEM_WB_RegisterRd,
  input  MEM_WB_RegWrite,
  output [1:0] Forward_A,
  output [1:0] Forward_B
);

  wire comparator_1_eq, comparator_2_eq, comparator_3_eq, comparator_4_eq, comparator_5_eq, comparator_6_eq,
       EX_Hazard_A, EX_Hazard_B, MEM_Hazard_A, MEM_Hazard_B, not_1_out, not_2_out;
  wire [1:0] bit_extender_1_out, bit_extender_2_out;

  Comparator #(.width(4), .mode("unsigned")) comparator_1 (
    .a(EX_MEM_RegisterRd), .b(4'b0000), .eq(comparator_1_eq));  // open: gt, lt
  Comparator #(.width(4), .mode("unsigned")) comparator_2 (
    .a(EX_MEM_RegisterRd), .b(ID_EX_RegisterRs), .eq(comparator_2_eq));  // open: gt, lt
  Comparator #(.width(4), .mode("unsigned")) comparator_3 (
    .a(EX_MEM_RegisterRd), .b(ID_EX_RegisterRt), .eq(comparator_3_eq));  // open: gt, lt
  Comparator #(.width(4), .mode("unsigned")) comparator_4 (
    .a(MEM_WB_RegisterRd), .b(4'b0000), .eq(comparator_4_eq));  // open: gt, lt
  Comparator #(.width(4), .mode("unsigned")) comparator_5 (
    .a(MEM_WB_RegisterRd), .b(ID_EX_RegisterRs), .eq(comparator_5_eq));  // open: gt, lt
  Comparator #(.width(4), .mode("unsigned")) comparator_6 (
    .a(MEM_WB_RegisterRd), .b(ID_EX_RegisterRt), .eq(comparator_6_eq));  // open: gt, lt
  not not_1 (not_1_out, comparator_1_eq);
  not not_2 (not_2_out, comparator_4_eq);
  assign bit_extender_1_out = {{1{1'b0}}, MEM_Hazard_A};  // Bit_Extender bit_extender_1
  assign bit_extender_2_out = {{1{1'b0}}, MEM_Hazard_B};  // Bit_Extender bit_extender_2
  and and_1 (EX_Hazard_A, EX_MEM_RegWrite, not_1_out, comparator_2_eq);
  and and_2 (EX_Hazard_B, EX_MEM_RegWrite, not_1_out, comparator_3_eq);
  and and_3 (MEM_Hazard_A, MEM_WB_RegWrite, not_2_out, comparator_5_eq);
  and and_4 (MEM_Hazard_B, MEM_WB_RegWrite, not_2_out, comparator_6_eq);
  Multiplexer #(.width(2), .enable("false")) multiplexer_1 (
    .in0(bit_extender_1_out), .in1(2'b10), .out(Forward_A), .sel(EX_Hazard_A));
  Multiplexer #(.width(2), .enable("false")) multiplexer_2 (
    .in0(bit_extender_2_out), .in1(2'b10), .out(Forward_B), .sel(EX_Hazard_B));

  // Notes on the sheet:
  //   EX HAZARD
  //   MEM HAZARD
  //   00 - NO FORWARDING
  //   01 - FORWARDED FROM MEM/WB REGISTER
  //   10 - FORWARDED FROM EX/MEM
  //   10 OR FORWARDING FROM EX/MEM GETS PRIORITY (AS LATEST VALUE)
endmodule

module LOAD_USE_HAZARD (
  input  ID_EX_MemRead,
  input  [3:0] ID_EX_RegisterRt,
  input  [3:0] IF_ID_RegisterRs,
  input  [3:0] IF_ID_RegisterRt,
  output Hazard
);

  wire comparator_1_eq, comparator_2_eq, or_1_out;

  Comparator #(.width(4), .mode("unsigned")) comparator_1 (
    .a(ID_EX_RegisterRt), .b(IF_ID_RegisterRs), .eq(comparator_1_eq));  // open: gt, lt
  Comparator #(.width(4), .mode("unsigned")) comparator_2 (
    .a(ID_EX_RegisterRt), .b(IF_ID_RegisterRt), .eq(comparator_2_eq));  // open: gt, lt
  or or_1 (or_1_out, comparator_1_eq, comparator_2_eq);
  and and_1 (Hazard, ID_EX_MemRead, or_1_out);

  // Notes on the sheet:
  //   LOAD USE HAZARD - 1 CLOCK CYCLE STALL MANDATORY
  //   We always write to Rt register in case of lw. So no need to consider ID/EX.RegisterRd
endmodule

module BRANCH_FORWARDING_UNIT (
  input  [3:0] IF_ID_RegisterRs,
  input  [3:0] IF_ID_RegisterRt,
  input  [3:0] EX_MEM_RegisterRd,
  input  EX_MEM_RegWrite,
  input  [3:0] MEM_WB_RegisterRd,
  input  MEM_WB_RegWrite,
  input  [3:0] ID_EX_RegisterRd,
  input  ID_EX_RegWrite,
  input  Is_Branch,
  output [1:0] Forward_A,
  output [1:0] Forward_B,
  output Stall
);

  wire and_6_out, and_7_out, comparator_1_eq, comparator_2_eq, comparator_3_eq, comparator_4_eq,
       comparator_5_eq, comparator_6_eq, comparator_7_eq, comparator_8_eq, comparator_9_eq, EX_Hazard_A,
       EX_Hazard_B, MEM_Hazard_A, MEM_Hazard_B, not_1_out, not_2_out, not_3_out, Stall_t;
  wire [1:0] bit_extender_1_out, bit_extender_2_out, multiplexer_1_out, multiplexer_2_out;

  Comparator #(.width(4), .mode("unsigned")) comparator_1 (
    .a(EX_MEM_RegisterRd), .b(4'b0000), .eq(comparator_1_eq));  // open: gt, lt
  Comparator #(.width(4), .mode("unsigned")) comparator_2 (
    .a(EX_MEM_RegisterRd), .b(IF_ID_RegisterRs), .eq(comparator_2_eq));  // open: gt, lt
  Comparator #(.width(4), .mode("unsigned")) comparator_3 (
    .a(EX_MEM_RegisterRd), .b(IF_ID_RegisterRt), .eq(comparator_3_eq));  // open: gt, lt
  Comparator #(.width(4), .mode("unsigned")) comparator_4 (
    .a(MEM_WB_RegisterRd), .b(4'b0000), .eq(comparator_4_eq));  // open: gt, lt
  Comparator #(.width(4), .mode("unsigned")) comparator_5 (
    .a(MEM_WB_RegisterRd), .b(IF_ID_RegisterRs), .eq(comparator_5_eq));  // open: gt, lt
  Comparator #(.width(4), .mode("unsigned")) comparator_6 (
    .a(MEM_WB_RegisterRd), .b(IF_ID_RegisterRt), .eq(comparator_6_eq));  // open: gt, lt
  not not_1 (not_1_out, comparator_1_eq);
  not not_2 (not_2_out, comparator_4_eq);
  and and_1 (EX_Hazard_A, EX_MEM_RegWrite, not_1_out, comparator_2_eq);
  and and_2 (EX_Hazard_B, EX_MEM_RegWrite, not_1_out, comparator_3_eq);
  and and_3 (MEM_Hazard_A, MEM_WB_RegWrite, not_2_out, comparator_5_eq);
  and and_4 (MEM_Hazard_B, MEM_WB_RegWrite, not_2_out, comparator_6_eq);
  assign bit_extender_1_out = {{1{1'b0}}, MEM_Hazard_A};  // Bit_Extender bit_extender_1
  assign bit_extender_2_out = {{1{1'b0}}, MEM_Hazard_B};  // Bit_Extender bit_extender_2
  Multiplexer #(.width(2), .enable("false")) multiplexer_1 (
    .in0(bit_extender_1_out), .in1(2'b10), .out(multiplexer_1_out), .sel(EX_Hazard_A));
  Multiplexer #(.width(2), .enable("false")) multiplexer_2 (
    .in0(bit_extender_2_out), .in1(2'b10), .out(multiplexer_2_out), .sel(EX_Hazard_B));
  Multiplexer #(.width(2), .enable("false")) multiplexer_3 (
    .in0(2'b00), .in1(multiplexer_1_out), .out(Forward_A), .sel(Is_Branch));
  Multiplexer #(.width(2), .enable("false")) multiplexer_4 (
    .in0(2'b00), .in1(multiplexer_2_out), .out(Forward_B), .sel(Is_Branch));
  and and_5 (Stall, Is_Branch, Stall_t);
  Comparator #(.width(4), .mode("unsigned")) comparator_7 (
    .a(ID_EX_RegisterRd), .b(4'b0000), .eq(comparator_7_eq));  // open: gt, lt
  Comparator #(.width(4), .mode("unsigned")) comparator_8 (
    .a(ID_EX_RegisterRd), .b(IF_ID_RegisterRs), .eq(comparator_8_eq));  // open: gt, lt
  Comparator #(.width(4), .mode("unsigned")) comparator_9 (
    .a(ID_EX_RegisterRd), .b(IF_ID_RegisterRt), .eq(comparator_9_eq));  // open: gt, lt
  not not_3 (not_3_out, comparator_7_eq);
  and and_6 (and_6_out, ID_EX_RegWrite, not_3_out, comparator_8_eq);
  or or_1 (Stall_t, and_6_out, and_7_out);
  and and_7 (and_7_out, ID_EX_RegWrite, not_3_out, comparator_9_eq);

  // Notes on the sheet:
  //   EX HAZARD
  //   MEM HAZARD
  //   00 - NO FORWARDING
  //   01 - FORWARDED FROM MEM/WB REGISTER
  //   10 - FORWARDED FROM EX/MEM
  //   10 OR FORWARDING FROM EX/MEM GETS PRIORITY (AS LATEST VALUE)
  //   ID HAZARD (NON FORWARDABLE - STALL 1 CYCLE)
endmodule

module BRANCH_LOAD_USE_HAZARD (
  input  ID_EX_MemRead,
  input  [3:0] ID_EX_RegisterRt,
  input  [3:0] IF_ID_RegisterRs,
  input  CLK,
  input  [3:0] IF_ID_RegisterRt,
  input  Is_Branch,
  output Hazard
);

  wire and_1_out, and_2_out, comparator_1_eq, comparator_2_eq, or_1_out, register_1_q;

  Comparator #(.width(4), .mode("unsigned")) comparator_1 (
    .a(ID_EX_RegisterRt), .b(IF_ID_RegisterRs), .eq(comparator_1_eq));  // open: gt, lt
  Comparator #(.width(4), .mode("unsigned")) comparator_2 (
    .a(ID_EX_RegisterRt), .b(IF_ID_RegisterRt), .eq(comparator_2_eq));  // open: gt, lt
  or or_1 (or_1_out, comparator_1_eq, comparator_2_eq);
  and and_1 (and_1_out, ID_EX_MemRead, or_1_out);
  and and_2 (and_2_out, Is_Branch, and_1_out);
  or or_2 (Hazard, and_2_out, register_1_q);
  Register #(.width(1)) register_1 (.D(and_2_out), .en(1'b1), .Q(register_1_q), .clk(CLK));  // open: clr

  // Notes on the sheet:
  //   BRANCH LOAD USE HAZARD - 2 CLOCK CYCLE STALL MANDATORY
  //   We always write to Rt register in case of lw. So no need to consider ID/EX.RegisterRd
endmodule

module Non_Pipelined (
  input  RESET
);

  wire ALU_SRC, BRANCH, CLK, control_1_beq, control_1_bneq, JUMP, MEM_READ, MEM_TO_REG, MEM_WRITE, REG_DEST,
       REG_WRITE, ZERO;
  wire [2:0] ALU_OP;
  wire [3:0] instruction_1_dest, instruction_1_src_1, instruction_1_src_2, multiplexer_1_out, OP_CODE;
  wire [7:0] adder_1_out, adder_2_out, alu_8_by_art_1_p5, CURRENT_PC, IMM, JUMP_ADDR, memory_1_data_read,
       multiplexer_3_out, multiplexer_4_out, multiplexer_6_out, registers_1_readdata1, registers_1_readdata2,
       UPDATED_PC;
  wire [23:0] REG_10S, REG_432;

  // Probe on CURRENT_PC
  Clock u_CLK (.out(CLK));
  // Probe on OP_CODE
  Instruction instruction_1 (
    .PC_Write(UPDATED_PC), .CLK(CLK), .RESET(RESET), .PC_Read(CURRENT_PC), .Opcode(OP_CODE),
    .Src_1(instruction_1_src_1), .Src_2(instruction_1_src_2), .Dest(instruction_1_dest), .Addr___Immd(IMM),
    .Jump_Addr(JUMP_ADDR));
  Control control_1 (
    .OP_Code(OP_CODE), .RegDst(REG_DEST), .ALUSrc(ALU_SRC), .MemToReg(MEM_TO_REG), .RegWrite(REG_WRITE),
    .MemRead(MEM_READ), .MemWrite(MEM_WRITE), .beq(control_1_beq), .bneq(control_1_bneq), .Jump(JUMP),
    .ALUOp(ALU_OP));
  Adder adder_1 (.a(CURRENT_PC), .b(8'h1), .out(adder_1_out), .cin(1'b0));  // open: cout
  Multiplexer #(.width(4), .enable("false")) multiplexer_1 (
    .in0(instruction_1_src_2), .in1(instruction_1_dest), .out(multiplexer_1_out), .sel(REG_DEST));
  Multiplexer #(.enable("false")) multiplexer_2 (.in0(control_1_bneq), .in1(control_1_beq), .out(BRANCH), .sel(ZERO));
  Adder adder_2 (.a(adder_1_out), .b(IMM), .out(adder_2_out), .cin(1'b0));  // open: cout
  Multiplexer #(.width(8), .enable("false")) multiplexer_3 (
    .in0(adder_1_out), .in1(adder_2_out), .out(multiplexer_3_out), .sel(BRANCH));
  Registers registers_1 (
    .RegWrite(REG_WRITE), .Src_1(instruction_1_src_1), .Src_2(instruction_1_src_2),
    .Dest_1(multiplexer_1_out), .WriteData(multiplexer_6_out), .CLK(CLK), .CLR(RESET),
    .ReadData1(registers_1_readdata1), .ReadData2(registers_1_readdata2), .t4__t3__t2(REG_432),
    .t1__t0__sp(REG_10S));
  Multiplexer #(.width(8), .enable("false")) multiplexer_4 (
    .in0(registers_1_readdata2), .in1(IMM), .out(multiplexer_4_out), .sel(ALU_SRC));
  Multiplexer #(.width(8), .enable("false")) multiplexer_5 (
    .in0(multiplexer_3_out), .in1(JUMP_ADDR), .out(UPDATED_PC), .sel(JUMP));
  // ALU_8_by_ART alu_8_by_art_1: pin names not known; wires that end beside it: registers_1_readdata1, multiplexer_4_out, ALU_OP, ZERO, alu_8_by_art_1_p5
  // Probe on REG_10S[15:8]
  // Probe on REG_10S[23:16]
  // Probe on REG_432[7:0]
  // Probe on REG_432[15:8]
  // Probe on REG_432[23:16]
  // Probe on REG_10S[7:0]
  Memory memory_1 (
    .Address(alu_8_by_art_1_p5), .WriteData(registers_1_readdata2), .CLK(CLK), .CLR(RESET),
    .Data_Read(memory_1_data_read), .MemRead(MEM_READ), .MemWrite(MEM_WRITE));
  Multiplexer #(.width(8), .enable("false")) multiplexer_6 (
    .in0(alu_8_by_art_1_p5), .in1(memory_1_data_read), .out(multiplexer_6_out), .sel(MEM_TO_REG));
endmodule

module Instruction (
  input  [7:0] PC_Write,
  input  CLK,
  input  RESET,
  output [7:0] PC_Read,
  output [3:0] Opcode,
  output [3:0] Src_1,
  output [3:0] Src_2,
  output [3:0] Dest,
  output [7:0] Addr___Immd,
  output [7:0] Jump_Addr
);

  Register register_1 (.D(PC_Write), .en(1'b1), .Q(PC_Read), .clk(CLK), .clr(RESET));
  ROM #(.dataWidth(20)) rom_1 (.addr(PC_Read), .data({Opcode, Jump_Addr, Addr___Immd}), .sel(1'b1));

  assign Dest = Addr___Immd[7:4];
  assign Src_1 = Jump_Addr[7:4];
  assign Src_2 = Jump_Addr[3:0];

  // Notes on the sheet:
  //   contents of rom_1 (hex, n*v repeats v):
  //   a06ff a050a a110c 8150f d150f
  //   Shift Amt
endmodule

module Control (
  input  [3:0] OP_Code,
  output RegDst,
  output ALUSrc,
  output MemToReg,
  output RegWrite,
  output MemRead,
  output MemWrite,
  output beq,
  output bneq,
  output Jump,
  output [2:0] ALUOp
);

  ROM #(.addrWidth(4), .dataWidth(12)) rom_1 (
    .addr(OP_Code), .data({RegDst, ALUSrc, MemToReg, RegWrite, MemRead, MemWrite, beq, bneq, Jump, ALUOp}),
    .sel(1'b1));

  // Notes on the sheet:
  //   contents of rom_1 (hex, n*v repeats v):
  //   901 506 503 502 904 11 903 21 c40 501 500 505 900 780 902 8
endmodule

module Registers (
  input  RegWrite,
  input  [3:0] Src_1,
  input  [3:0] Src_2,
  input  [3:0] Dest_1,
  input  [7:0] WriteData,
  input  CLK,
  input  CLR,
  output [23:0] t4__t3__t2,
  output [23:0] t1__t0__sp,
  output [7:0] ReadData1,
  output [7:0] ReadData2
);

  wire demultiplexer_1_out1, demultiplexer_1_out2, demultiplexer_1_out3, demultiplexer_1_out4,
       demultiplexer_1_out5, demultiplexer_1_out6;
  wire [2:0] bit_extender_1_out, bit_extender_2_out, bit_extender_3_out;

  Register t1 (.D(WriteData), .en(demultiplexer_1_out1), .Q(t1__t0__sp[23:16]), .clk(CLK), .clr(CLR));
  Bit_Extender #(.in_width(4), .out_width(3)) bit_extender_1 (.in(Src_1), .out(bit_extender_1_out));
  Bit_Extender #(.in_width(4), .out_width(3)) bit_extender_2 (.in(Dest_1), .out(bit_extender_2_out));
  Register t2 (.D(WriteData), .en(demultiplexer_1_out2), .Q(t4__t3__t2[7:0]), .clk(CLK), .clr(CLR));
  Multiplexer #(.select(3), .width(8), .enable("false")) multiplexer_1 (
    .in0({8{1'b0}}), .in1(t1__t0__sp[23:16]), .in2(t4__t3__t2[7:0]), .in3(t4__t3__t2[15:8]),
    .in4(t4__t3__t2[23:16]), .in5(t1__t0__sp[15:8]), .in6(t1__t0__sp[7:0]), .out(ReadData1),
    .sel(bit_extender_1_out));  // open: in7
  Demultiplexer #(.select(3), .enable("false")) demultiplexer_1 (
    .out1(demultiplexer_1_out1), .out2(demultiplexer_1_out2), .out3(demultiplexer_1_out3),
    .out4(demultiplexer_1_out4), .out5(demultiplexer_1_out5), .out6(demultiplexer_1_out6), .in(RegWrite),
    .sel(bit_extender_2_out));  // open: out0, out7
  Register t3 (.D(WriteData), .en(demultiplexer_1_out3), .Q(t4__t3__t2[15:8]), .clk(CLK), .clr(CLR));
  Register t4 (.D(WriteData), .en(demultiplexer_1_out4), .Q(t4__t3__t2[23:16]), .clk(CLK), .clr(CLR));
  Bit_Extender #(.in_width(4), .out_width(3)) bit_extender_3 (.in(Src_2), .out(bit_extender_3_out));
  Register t0 (.D(WriteData), .en(demultiplexer_1_out5), .Q(t1__t0__sp[15:8]), .clk(CLK), .clr(CLR));
  Multiplexer #(.select(3), .width(8), .enable("false")) multiplexer_2 (
    .in0({8{1'b0}}), .in1(t1__t0__sp[23:16]), .in2(t4__t3__t2[7:0]), .in3(t4__t3__t2[15:8]),
    .in4(t4__t3__t2[23:16]), .in5(t1__t0__sp[15:8]), .in6(t1__t0__sp[7:0]), .out(ReadData2),
    .sel(bit_extender_3_out));  // open: in7
  Register sp (.D(WriteData), .en(demultiplexer_1_out6), .Q(t1__t0__sp[7:0]), .clk(CLK), .clr(CLR));

  // Other names for the same wires on the sheet: S1[3:0] = Src_1; S2[3:0] = Src_2; WD[7:0] = WriteData
endmodule

module Memory (
  input  [7:0] Address,
  input  [7:0] WriteData,
  input  CLK,
  input  CLR,
  input  MemWrite,
  input  MemRead,
  output [7:0] Data_Read
);

  RAM #(.bus("separate")) ram_1 (
    .addr(Address), .din(WriteData), .data(Data_Read), .str(MemWrite), .sel(1'b1), .clk(CLK), .ld(MemRead),
    .clr(CLR));
endmodule
