// Logisim project MIPS_NonPipelined_Extended.circ as structural Verilog: 17 circuits, main circuit IO_SETUP
module IO_SETUP (
  input  RESET
);

  wire CLK, E4, E13, mips_extended_io_1_enable_0, mips_extended_io_1_enable_1, mips_extended_io_1_enable_2,
       mips_extended_io_1_enable_3, mips_extended_io_1_enable_5, mips_extended_io_1_enable_14,
       mips_extended_io_1_enable_15, n8_bit_to_7_seg_adapter_1_out_6, n8_bit_to_7_seg_adapter_1_out_7,
       n8_bit_to_7_seg_adapter_1_out_8, n8_bit_to_7_seg_adapter_1_out_9, n8_bit_to_7_seg_adapter_1_out_10,
       n8_bit_to_7_seg_adapter_1_out_11, n8_bit_to_7_seg_adapter_1_out_12, n8_bit_to_7_seg_adapter_1_out_13,
       n8_bit_to_7_seg_adapter_1_out_14, n8_bit_to_7_seg_adapter_1_out_15, n8_bit_to_7_seg_adapter_1_out_16,
       n8_bit_to_7_seg_adapter_1_out_17, n8_bit_to_7_seg_adapter_1_out_18, n8_bit_to_7_seg_adapter_1_out_19,
       n8_bit_to_7_seg_adapter_1_out_20, n8_bit_to_7_seg_adapter_1_out_21, n8_bit_to_7_seg_adapter_1_out_22,
       n8_bit_to_7_seg_adapter_1_out_23, n8_bit_to_7_seg_adapter_1_out_24, n8_bit_to_7_seg_adapter_1_out_25,
       n8_bit_to_7_seg_adapter_1_out_26, n8_bit_to_7_seg_adapter_1_sign;
  wire [6:0] bit_extender_1_out, keyboard_1_data;
  wire [7:0] Input_04, Input_15, mips_extended_io_1_current_pc, register_1_q, register_2_q, WRITE;
  wire [15:0] n16_x_32_display_adapter_1_out_9, n16_x_32_display_adapter_1_out_10,
       n16_x_32_display_adapter_1_out_11, n16_x_32_display_adapter_1_out_12,
       n16_x_32_display_adapter_1_out_13, n16_x_32_display_adapter_1_out_14,
       n16_x_32_display_adapter_1_out_15, n16_x_32_display_adapter_1_out_16,
       n16_x_32_display_adapter_1_out_17, n16_x_32_display_adapter_1_out_18,
       n16_x_32_display_adapter_1_out_19, n16_x_32_display_adapter_1_out_20,
       n16_x_32_display_adapter_1_out_21, n16_x_32_display_adapter_1_out_22,
       n16_x_32_display_adapter_1_out_23, n16_x_32_display_adapter_1_out_24,
       n16_x_32_display_adapter_1_out_25, n16_x_32_display_adapter_1_out_26,
       n16_x_32_display_adapter_1_out_27, n16_x_32_display_adapter_1_out_28,
       n16_x_32_display_adapter_1_out_29, n16_x_32_display_adapter_1_out_30,
       n16_x_32_display_adapter_1_out_31, n16_x_32_display_adapter_1_out_32,
       n16_x_32_display_adapter_1_out_33, n16_x_32_display_adapter_1_out_34,
       n16_x_32_display_adapter_1_out_35, n16_x_32_display_adapter_1_out_36,
       n16_x_32_display_adapter_1_out_37, n16_x_32_display_adapter_1_out_38,
       n16_x_32_display_adapter_1_out_39, n16_x_32_display_adapter_1_out_40;

  // Probe on mips_extended_io_1_current_pc
  MIPS_EXTENDED_IO mips_extended_io_1 (
    .RESET(RESET), .CLK(CLK), .OUTPUT(WRITE), .Current_PC(mips_extended_io_1_current_pc),
    .Enable_0(mips_extended_io_1_enable_0), .Enable_1(mips_extended_io_1_enable_1),
    .Enable_2(mips_extended_io_1_enable_2), .Enable_3(mips_extended_io_1_enable_3), .Enable_4(E4),
    .Enable_5(mips_extended_io_1_enable_5), .Enable_13(E13), .Enable_14(mips_extended_io_1_enable_14),
    .Enable_15(mips_extended_io_1_enable_15), .Input_4(Input_04), .Input_15(Input_15));  // open: Enable_6, Enable_7, Enable_8, Enable_9, Enable_10, Enable_11, Enable_12, Input_0, Input_1, Input_2, Input_3, Input_5, Input_6, Input_7, Input_8, Input_9, Input_10, Input_11, Input_12, Input_13, Input_14
  Bit_Extender #(.out_width(7)) bit_extender_1 (.in(WRITE), .out(bit_extender_1_out));
  TTY tty_1 (.data(bit_extender_1_out), .clk(CLK), .we(mips_extended_io_1_enable_5), .clr(RESET));
  _16_x_32_Display_Adapter u_16_x_32_display_adapter_1 (
    .CLR(RESET), .UPDATE(mips_extended_io_1_enable_2), .FLUSH_BUFFER(mips_extended_io_1_enable_3), .X(WRITE),
    .Y(WRITE), .out_9(n16_x_32_display_adapter_1_out_9), .out_10(n16_x_32_display_adapter_1_out_10),
    .out_11(n16_x_32_display_adapter_1_out_11), .out_12(n16_x_32_display_adapter_1_out_12),
    .out_13(n16_x_32_display_adapter_1_out_13), .out_14(n16_x_32_display_adapter_1_out_14),
    .out_15(n16_x_32_display_adapter_1_out_15), .out_16(n16_x_32_display_adapter_1_out_16),
    .out_17(n16_x_32_display_adapter_1_out_17), .out_18(n16_x_32_display_adapter_1_out_18),
    .out_19(n16_x_32_display_adapter_1_out_19), .out_20(n16_x_32_display_adapter_1_out_20),
    .out_21(n16_x_32_display_adapter_1_out_21), .out_22(n16_x_32_display_adapter_1_out_22),
    .out_23(n16_x_32_display_adapter_1_out_23), .out_24(n16_x_32_display_adapter_1_out_24),
    .out_25(n16_x_32_display_adapter_1_out_25), .out_26(n16_x_32_display_adapter_1_out_26),
    .out_27(n16_x_32_display_adapter_1_out_27), .out_28(n16_x_32_display_adapter_1_out_28),
    .out_29(n16_x_32_display_adapter_1_out_29), .out_30(n16_x_32_display_adapter_1_out_30),
    .out_31(n16_x_32_display_adapter_1_out_31), .out_32(n16_x_32_display_adapter_1_out_32),
    .out_33(n16_x_32_display_adapter_1_out_33), .out_34(n16_x_32_display_adapter_1_out_34),
    .out_35(n16_x_32_display_adapter_1_out_35), .out_36(n16_x_32_display_adapter_1_out_36),
    .out_37(n16_x_32_display_adapter_1_out_37), .out_38(n16_x_32_display_adapter_1_out_38),
    .out_39(n16_x_32_display_adapter_1_out_39), .out_40(n16_x_32_display_adapter_1_out_40),
    .X_Enable(mips_extended_io_1_enable_0), .Y_Enable(mips_extended_io_1_enable_1), .CLK(CLK));
  Random_Number_Generator random_number_generator_1 (
    .CLK(CLK), .Enable(mips_extended_io_1_enable_15), .Random(Input_15));
  DotMatrix #(.matrixcols(32), .matrixrows(16)) dotmatrix_1 (
    .col0(n16_x_32_display_adapter_1_out_9), .col1(n16_x_32_display_adapter_1_out_10),
    .col2(n16_x_32_display_adapter_1_out_11), .col3(n16_x_32_display_adapter_1_out_12),
    .col4(n16_x_32_display_adapter_1_out_13), .col5(n16_x_32_display_adapter_1_out_14),
    .col6(n16_x_32_display_adapter_1_out_15), .col7(n16_x_32_display_adapter_1_out_16),
    .col8(n16_x_32_display_adapter_1_out_17), .col9(n16_x_32_display_adapter_1_out_18),
    .col10(n16_x_32_display_adapter_1_out_19), .col11(n16_x_32_display_adapter_1_out_20),
    .col12(n16_x_32_display_adapter_1_out_21), .col13(n16_x_32_display_adapter_1_out_22),
    .col14(n16_x_32_display_adapter_1_out_23), .col15(n16_x_32_display_adapter_1_out_24),
    .col16(n16_x_32_display_adapter_1_out_25), .col17(n16_x_32_display_adapter_1_out_26),
    .col18(n16_x_32_display_adapter_1_out_27), .col19(n16_x_32_display_adapter_1_out_28),
    .col20(n16_x_32_display_adapter_1_out_29), .col21(n16_x_32_display_adapter_1_out_30),
    .col22(n16_x_32_display_adapter_1_out_31), .col23(n16_x_32_display_adapter_1_out_32),
    .col24(n16_x_32_display_adapter_1_out_33), .col25(n16_x_32_display_adapter_1_out_34),
    .col26(n16_x_32_display_adapter_1_out_35), .col27(n16_x_32_display_adapter_1_out_36),
    .col28(n16_x_32_display_adapter_1_out_37), .col29(n16_x_32_display_adapter_1_out_38),
    .col30(n16_x_32_display_adapter_1_out_39), .col31(n16_x_32_display_adapter_1_out_40));
  Register register_1 (.D(WRITE), .en(mips_extended_io_1_enable_14), .Q(register_1_q), .clk(CLK), .clr(RESET));
  Register register_2 (.D(register_1_q), .en(mips_extended_io_1_enable_14), .Q(register_2_q), .clk(CLK), .clr(RESET));
  Keyboard #(.buflen(5)) keyboard_1 (.clk(CLK), .re(E4), .clr(RESET), .data(keyboard_1_data));  // open: avail
  // Probe on register_1_q
  // Probe on register_2_q
  _7_Segment_Display u_7_segment_display_1 (.g(n8_bit_to_7_seg_adapter_1_sign));  // open: f, a, b, e, d, c, dp
  // Probe on register_1_q
  // Probe on register_1_q
  // Probe on register_2_q
  // Probe on register_2_q
  _7_Segment_Display u_7_segment_display_2 (
    .g(n8_bit_to_7_seg_adapter_1_out_13), .f(n8_bit_to_7_seg_adapter_1_out_14),
    .a(n8_bit_to_7_seg_adapter_1_out_15), .b(n8_bit_to_7_seg_adapter_1_out_16),
    .e(n8_bit_to_7_seg_adapter_1_out_17), .d(n8_bit_to_7_seg_adapter_1_out_18),
    .c(n8_bit_to_7_seg_adapter_1_out_19));  // open: dp
  _7_Segment_Display u_7_segment_display_3 (
    .g(n8_bit_to_7_seg_adapter_1_out_20), .f(n8_bit_to_7_seg_adapter_1_out_21),
    .a(n8_bit_to_7_seg_adapter_1_out_22), .b(n8_bit_to_7_seg_adapter_1_out_23),
    .e(n8_bit_to_7_seg_adapter_1_out_24), .d(n8_bit_to_7_seg_adapter_1_out_25),
    .c(n8_bit_to_7_seg_adapter_1_out_26));  // open: dp
  _7_Segment_Display u_7_segment_display_4 (
    .g(n8_bit_to_7_seg_adapter_1_out_6), .f(n8_bit_to_7_seg_adapter_1_out_7),
    .a(n8_bit_to_7_seg_adapter_1_out_8), .b(n8_bit_to_7_seg_adapter_1_out_9),
    .e(n8_bit_to_7_seg_adapter_1_out_10), .d(n8_bit_to_7_seg_adapter_1_out_11),
    .c(n8_bit_to_7_seg_adapter_1_out_12));  // open: dp
  _8_bit_to_7_Seg_Adapter u_8_bit_to_7_seg_adapter_1 (
    .out_6(n8_bit_to_7_seg_adapter_1_out_6), .out_7(n8_bit_to_7_seg_adapter_1_out_7),
    .out_8(n8_bit_to_7_seg_adapter_1_out_8), .out_9(n8_bit_to_7_seg_adapter_1_out_9),
    .out_10(n8_bit_to_7_seg_adapter_1_out_10), .out_11(n8_bit_to_7_seg_adapter_1_out_11),
    .out_12(n8_bit_to_7_seg_adapter_1_out_12), .out_13(n8_bit_to_7_seg_adapter_1_out_13),
    .out_14(n8_bit_to_7_seg_adapter_1_out_14), .out_15(n8_bit_to_7_seg_adapter_1_out_15),
    .out_16(n8_bit_to_7_seg_adapter_1_out_16), .out_17(n8_bit_to_7_seg_adapter_1_out_17),
    .out_18(n8_bit_to_7_seg_adapter_1_out_18), .out_19(n8_bit_to_7_seg_adapter_1_out_19),
    .out_20(n8_bit_to_7_seg_adapter_1_out_20), .out_21(n8_bit_to_7_seg_adapter_1_out_21),
    .out_22(n8_bit_to_7_seg_adapter_1_out_22), .out_23(n8_bit_to_7_seg_adapter_1_out_23),
    .out_24(n8_bit_to_7_seg_adapter_1_out_24), .out_25(n8_bit_to_7_seg_adapter_1_out_25),
    .out_26(n8_bit_to_7_seg_adapter_1_out_26), .Sign(n8_bit_to_7_seg_adapter_1_sign), .Data(WRITE),
    .Write_Enable(E13), .Is_Signed(1'b1), .CLK(CLK), .CLR(RESET));
  assign Input_04 = {{1{1'b0}}, keyboard_1_data};  // Bit_Extender bit_extender_2

  // Other names for the same wires on the sheet: CLR = RESET

  // Notes on the sheet:
  //   SCORE:
  //   KEYBOARD
  //   DEBUG VALUES
  //   Latest
  //   History
endmodule

module MIPS_EXTENDED_IO (
  input  RESET,
  input  [7:0] Input_0,
  input  [7:0] Input_1,
  input  [7:0] Input_2,
  input  [7:0] Input_3,
  input  [7:0] Input_4,
  input  [7:0] Input_5,
  input  [7:0] Input_6,
  input  [7:0] Input_7,
  input  [7:0] Input_8,
  input  [7:0] Input_9,
  input  [7:0] Input_10,
  input  [7:0] Input_11,
  input  [7:0] Input_12,
  input  [7:0] Input_13,
  input  [7:0] Input_14,
  input  [7:0] Input_15,
  output CLK,
  output [7:0] Current_PC,
  output [7:0] OUTPUT,
  output Enable_0,
  output Enable_1,
  output Enable_2,
  output Enable_3,
  output Enable_4,
  output Enable_5,
  output Enable_6,
  output Enable_7,
  output Enable_8,
  output Enable_9,
  output Enable_10,
  output Enable_11,
  output Enable_12,
  output Enable_13,
  output Enable_14,
  output Enable_15
);

  wire ALU_SRC, and_1_out, BRANCH, control_1_beq, control_1_bneq, IO, JUMP, MEM_READ, MEM_TO_REG, MEM_WRITE,
       or_1_out, REG_DEST, REG_WRITE, ZERO;
  wire [2:0] ALU_OP;
  wire [3:0] instruction_1_dest, instruction_1_src_1, instruction_1_src_2, IO_ADDR, multiplexer_1_out,
       OP_CODE;
  wire [7:0] adder_1_out, adder_2_out, alu_8_by_art_1_p5, demultiplexer_2_out0, demultiplexer_2_out1,
       extended_registers_1_readdata1, extended_registers_1_readdata2, IMM, INPUT, JUMP_ADDR,
       memory_1_data_read, multiplexer_3_out, multiplexer_4_out, multiplexer_8_out, multiplexer_9_out,
       UPDATED_PC;

  // Probe on Current_PC
  Clock u_CLK (.out(CLK));
  // Probe on OP_CODE
  Instruction instruction_1 (
    .PC_Write(UPDATED_PC), .CLK(CLK), .RESET(RESET), .PC_Read(Current_PC), .Opcode(OP_CODE),
    .Src_1(instruction_1_src_1), .Src_2(instruction_1_src_2), .Dest(instruction_1_dest), .Addr___Immd(IMM),
    .Jump_Addr(JUMP_ADDR));
  Control control_1 (
    .OP_Code(OP_CODE), .RegDst(REG_DEST), .ALUSrc(ALU_SRC), .MemToReg(MEM_TO_REG), .RegWrite(REG_WRITE),
    .MemRead(MEM_READ), .MemWrite(MEM_WRITE), .beq(control_1_beq), .bneq(control_1_bneq), .Jump(JUMP),
    .ALUOp(ALU_OP));
  Adder adder_1 (.a(Current_PC), .b(8'h1), .out(adder_1_out), .cin(1'b0));  // open: cout
  Multiplexer #(.width(4), .enable("false")) multiplexer_1 (
    .in0(instruction_1_src_2), .in1(instruction_1_dest), .out(multiplexer_1_out), .sel(REG_DEST));
  Multiplexer #(.enable("false")) multiplexer_2 (.in0(control_1_bneq), .in1(control_1_beq), .out(BRANCH), .sel(ZERO));
  Adder adder_2 (.a(adder_1_out), .b(IMM), .out(adder_2_out), .cin(1'b0));  // open: cout
  Multiplexer #(.width(8), .enable("false")) multiplexer_3 (
    .in0(adder_1_out), .in1(adder_2_out), .out(multiplexer_3_out), .sel(BRANCH));
  Extended_Registers extended_registers_1 (
    .RegWrite(REG_WRITE), .Dest_1(multiplexer_1_out), .Src_1(instruction_1_src_1),
    .Src_2(instruction_1_src_2), .WriteData(multiplexer_9_out), .CLK(CLK), .CLR(RESET),
    .ReadData1(extended_registers_1_readdata1), .ReadData2(extended_registers_1_readdata2));
  Multiplexer #(.width(8), .enable("false")) multiplexer_4 (
    .in0(extended_registers_1_readdata2), .in1(IMM), .out(multiplexer_4_out), .sel(ALU_SRC));
  or or_1 (or_1_out, MEM_READ, MEM_WRITE);
  Multiplexer #(.width(8), .enable("false")) multiplexer_5 (
    .in0(multiplexer_3_out), .in1(JUMP_ADDR), .out(UPDATED_PC), .sel(JUMP));
  // ALU_8_by_ART alu_8_by_art_1: pin names not known; wires that end beside it: extended_registers_1_readdata1, multiplexer_4_out, ALU_OP, ZERO, alu_8_by_art_1_p5
  Demultiplexer #(.select(4), .enable("false")) demultiplexer_1 (
    .out0(Enable_0), .out1(Enable_1), .out2(Enable_2), .out3(Enable_3), .out4(Enable_4), .out5(Enable_5),
    .out6(Enable_6), .out7(Enable_7), .out8(Enable_8), .out9(Enable_9), .out10(Enable_10), .out11(Enable_11),
    .out12(Enable_12), .out13(Enable_13), .out14(Enable_14), .out15(Enable_15), .in(and_1_out), .sel(IO_ADDR));
  and and_1 (and_1_out, IO, or_1_out);
  Address_Decoder address_decoder_1 (
    .Address(alu_8_by_art_1_p5), .Output_Peripheral_Address(IO_ADDR), .Output_Peripheral(IO));
  Demultiplexer #(.width(8), .enable("false")) demultiplexer_2 (
    .out0(demultiplexer_2_out0), .out1(demultiplexer_2_out1), .in(extended_registers_1_readdata2), .sel(IO));
  Multiplexer #(.width(8), .enable("false")) multiplexer_6 (
    .in0({8{1'b0}}), .in1(demultiplexer_2_out1), .out(OUTPUT), .sel(MEM_WRITE));
  Multiplexer #(.select(4), .width(8), .enable("false")) multiplexer_7 (
    .in0(Input_0), .in1(Input_1), .in2(Input_2), .in3(Input_3), .in4(Input_4), .in5(Input_5), .in6(Input_6),
    .in7(Input_7), .in8(Input_8), .in9(Input_9), .in10(Input_10), .in11(Input_11), .in12(Input_12),
    .in13(Input_13), .in14(Input_14), .in15(Input_15), .out(INPUT), .sel(IO_ADDR));
  Memory memory_1 (
    .Address(alu_8_by_art_1_p5), .WriteData(demultiplexer_2_out0), .CLK(CLK), .CLR(RESET),
    .Data_Read(memory_1_data_read), .MemRead(MEM_READ), .MemWrite(MEM_WRITE));
  Multiplexer #(.width(8), .enable("false")) multiplexer_8 (
    .in0(memory_1_data_read), .in1(INPUT), .out(multiplexer_8_out), .sel(IO));
  Multiplexer #(.width(8), .enable("false")) multiplexer_9 (
    .in0(alu_8_by_art_1_p5), .in1(multiplexer_8_out), .out(multiplexer_9_out), .sel(MEM_TO_REG));

  // Notes on the sheet:
  //   PORT ENABLE FLAGS
  //   PORT ENABLE FLAGS
  //   INPUT PORTS
endmodule

module Instruction (
  input  [7:0] PC_Write,
  input  CLK,
  input  RESET,
  output [7:0] PC_Read,
  output [3:0] Opcode,
  output [3:0] Src_1,
  output [3:0] Src_2,
  output [3:0] Dest,
  output [7:0] Addr___Immd,
  output [7:0] Jump_Addr
);

  Register register_1 (.D(PC_Write), .en(1'b1), .Q(PC_Read), .clk(CLK), .clr(RESET));
  ROM #(.dataWidth(20)) rom_1 (.addr(PC_Read), .data({Opcode, Jump_Addr, Addr___Immd}), .sel(1'b1));

  assign Dest = Addr___Immd[7:4];
  assign Src_1 = Jump_Addr[7:4];
  assign Src_2 = Jump_Addr[3:0];

  // Notes on the sheet:
  //   contents of rom_1 (hex, n*v repeats v):
  //   a0ff0 a06ef f7400 f0500 f2300 dfd0f dfe0f 2dd1f 2ee0f a0b04 a0c00 8fc0d a0400 a4306 a0507 a0107
  //   84500 84101 a0508 a0107 84502 84103 a0509 a0107 84504 84105 a050a a0107 84506 84107 a0703 a0804
  //   a0907 a0a01 f0400 8fd00 8fe01 8f002 a4500 f6b00 8f003 a0200 df204 22207 d3500 d3101 a0703 a0804
  //   7722a 7822d 79230 7a233 77b26 78b29 79b2c 7ab2f a3302 2337f 2551f 2110f 83500 83101 a4200 f4400
  //   7d50e a4402 2447f f2300 d2700 d2801 77504 a2202 2227f 532fa f4000 78101 f4700 fdc00 f0500 5e1f1
  //   acc01 8fc0d dfd0f dfe0f 2dd1f 2ee0f 9c23c 22280 502ea fef00 f0500 79b07 a11ff c07b0 f3800 7ab07
  //   a5501 c08b0 f3800 77bf7 a1101 c09b0 f3800 78bf7 a55ff c0ab0 f3800 d5100 d5201 8f100 8f201 8f002
  //   735b7 a5502 2557f f6b00 a0120 a020a a0553 8f505 a056e 8f505 a0561 8f505 a056b 8f505 a0565 8f505
  //   8f105 a0547 8f505 a0561 8f505 a056d 8f505 a0565 8f505 8f205 a0555 8f505 a0573 8f505 a0565 8f505
  //   8f105 a0550 8f505 a056f 8f505 a056b 8f505 a0565 8f505 8f105 a0554 8f505 a056f 8f505 a056f 8f505
  //   a056c 8f505 8f105 a056f 8f505 a056e 8f505 8f105 a056b 8f505 a0565 8f505 a0579 8f505 a0562 8f505
  //   a056f 8f505 a0561 8f505 a0572 8f505 a0564 8f505 8f205 a0574 8f505 a056f 8f505 8f105 a0570 8f505
  //   a056c 8f505 a0561 8f505 a0579 8f505 8f105 a0528 8f505 a0575 8f505 a0573 8f505 a0565 8f505 8f105
  //   a0557 8f505 a0541 8f505 a0553 8f505 a0544 8f505 a0529 8f505 8f205 f0300 a0559 8f505 a056f 8f505
  //   a0575 8f505 a0520 8f505 a054c 8f505 a056f 8f505 a0573 8f505 a0574 8f505 a050a 8f505 f4e00 a0559
  //   8f505 a056f 8f505 a0575 8f505 a0520 8f505 a0557 8f505 a056f 8f505 a056e 8f505 a050a 8f505 f5a00
  //   Shift Amt
endmodule

module Control (
  input  [3:0] OP_Code,
  output RegDst,
  output ALUSrc,
  output MemToReg,
  output RegWrite,
  output MemRead,
  output MemWrite,
  output beq,
  output bneq,
  output Jump,
  output [2:0] ALUOp
);

  ROM #(.addrWidth(4), .dataWidth(12)) rom_1 (
    .addr(OP_Code), .data({RegDst, ALUSrc, MemToReg, RegWrite, MemRead, MemWrite, beq, bneq, Jump, ALUOp}),
    .sel(1'b1));

  // Notes on the sheet:
  //   contents of rom_1 (hex, n*v repeats v):
  //   901 506 503 502 904 11 903 21 c40 501 500 505 900 780 902 8
endmodule

module Registers (
  input  RegWrite,
  input  [3:0] Src_1,
  input  [3:0] Src_2,
  input  [3:0] Dest_1,
  input  [7:0] WriteData,
  input  CLK,
  input  CLR,
  output [23:0] t4__t3__t2,
  output [23:0] t1__t0__sp,
  output [7:0] ReadData1,
  output [7:0] ReadData2
);

  wire demultiplexer_1_out1, demultiplexer_1_out2, demultiplexer_1_out3, demultiplexer_1_out4,
       demultiplexer_1_out5, demultiplexer_1_out6;
  wire [2:0] bit_extender_1_out, bit_extender_2_out, bit_extender_3_out;

  Register t1 (.D(WriteData), .en(demultiplexer_1_out1), .Q(t1__t0__sp[23:16]), .clk(CLK), .clr(CLR));
  Bit_Extender #(.in_width(4), .out_width(3)) bit_extender_1 (.in(Src_1), .out(bit_extender_1_out));
  Bit_Extender #(.in_width(4), .out_width(3)) bit_extender_2 (.in(Dest_1), .out(bit_extender_2_out));
  Register t2 (.D(WriteData), .en(demultiplexer_1_out2), .Q(t4__t3__t2[7:0]), .clk(CLK), .clr(CLR));
  Multiplexer #(.select(3), .width(8), .enable("false")) multiplexer_1 (
    .in0({8{1'b0}}), .in1(t1__t0__sp[23:16]), .in2(t4__t3__t2[7:0]), .in3(t4__t3__t2[15:8]),
    .in4(t4__t3__t2[23:16]), .in5(t1__t0__sp[15:8]), .in6(t1__t0__sp[7:0]), .out(ReadData1),
    .sel(bit_extender_1_out));  // open: in7
  Demultiplexer #(.select(3), .enable("false")) demultiplexer_1 (
    .out1(demultiplexer_1_out1), .out2(demultiplexer_1_out2), .out3(demultiplexer_1_out3),
    .out4(demultiplexer_1_out4), .out5(demultiplexer_1_out5), .out6(demultiplexer_1_out6), .in(RegWrite),
    .sel(bit_extender_2_out));  // open: out0, out7
  Register t3 (.D(WriteData), .en(demultiplexer_1_out3), .Q(t4__t3__t2[15:8]), .clk(CLK), .clr(CLR));
  Register t4 (.D(WriteData), .en(demultiplexer_1_out4), .Q(t4__t3__t2[23:16]), .clk(CLK), .clr(CLR));
  Bit_Extender #(.in_width(4), .out_width(3)) bit_extender_3 (.in(Src_2), .out(bit_extender_3_out));
  Register t0 (.D(WriteData), .en(demultiplexer_1_out5), .Q(t1__t0__sp[15:8]), .clk(CLK), .clr(CLR));
  Multiplexer #(.select(3), .width(8), .enable("false")) multiplexer_2 (
    .in0({8{1'b0}}), .in1(t1__t0__sp[23:16]), .in2(t4__t3__t2[7:0]), .in3(t4__t3__t2[15:8]),
    .in4(t4__t3__t2[23:16]), .in5(t1__t0__sp[15:8]), .in6(t1__t0__sp[7:0]), .out(ReadData2),
    .sel(bit_extender_3_out));  // open: in7
  Register sp (.D(WriteData), .en(demultiplexer_1_out6), .Q(t1__t0__sp[7:0]), .clk(CLK), .clr(CLR));

  // Other names for the same wires on the sheet: S1[3:0] = Src_1; S2[3:0] = Src_2; WD[7:0] = WriteData
endmodule

module Extended_Registers (
  input  RegWrite,
  input  [3:0] Dest_1,
  input  [3:0] Src_1,
  input  [3:0] Src_2,
  input  [7:0] WriteData,
  input  CLK,
  input  CLR,
  output [7:0] ReadData1,
  output [7:0] ReadData2
);

  wire demultiplexer_1_out1, demultiplexer_1_out2, demultiplexer_1_out3, demultiplexer_1_out4,
       demultiplexer_1_out5, demultiplexer_1_out6, demultiplexer_1_out7, demultiplexer_1_out8,
       demultiplexer_1_out9, demultiplexer_1_out10, demultiplexer_1_out11, demultiplexer_1_out12,
       demultiplexer_1_out13, demultiplexer_1_out14, demultiplexer_1_out15;
  wire [7:0] io_q, s0_q, s1_q, s2_q, s3_q, sp_q, t0_q, t1_q, t2_q, t3_q, t4_q, v0_q, v1_q, v2_q, v3_q;

  Demultiplexer #(.select(4), .enable("false")) demultiplexer_1 (
    .out1(demultiplexer_1_out1), .out2(demultiplexer_1_out2), .out3(demultiplexer_1_out3),
    .out4(demultiplexer_1_out4), .out5(demultiplexer_1_out5), .out6(demultiplexer_1_out6),
    .out7(demultiplexer_1_out7), .out8(demultiplexer_1_out8), .out9(demultiplexer_1_out9),
    .out10(demultiplexer_1_out10), .out11(demultiplexer_1_out11), .out12(demultiplexer_1_out12),
    .out13(demultiplexer_1_out13), .out14(demultiplexer_1_out14), .out15(demultiplexer_1_out15),
    .in(RegWrite), .sel(Dest_1));  // open: out0
  Register t1 (.D(WriteData), .en(demultiplexer_1_out1), .Q(t1_q), .clk(CLK), .clr(CLR));
  Register t2 (.D(WriteData), .en(demultiplexer_1_out2), .Q(t2_q), .clk(CLK), .clr(CLR));
  Register t3 (.D(WriteData), .en(demultiplexer_1_out3), .Q(t3_q), .clk(CLK), .clr(CLR));
  Register t4 (.D(WriteData), .en(demultiplexer_1_out4), .Q(t4_q), .clk(CLK), .clr(CLR));
  Register t0 (.D(WriteData), .en(demultiplexer_1_out5), .Q(t0_q), .clk(CLK), .clr(CLR));
  Register sp (.D(WriteData), .en(demultiplexer_1_out6), .Q(sp_q), .clk(CLK), .clr(CLR));
  Register v0 (.D(WriteData), .en(demultiplexer_1_out7), .Q(v0_q), .clk(CLK), .clr(CLR));
  Register v1 (.D(WriteData), .en(demultiplexer_1_out8), .Q(v1_q), .clk(CLK), .clr(CLR));
  Register v2 (.D(WriteData), .en(demultiplexer_1_out9), .Q(v2_q), .clk(CLK), .clr(CLR));
  Register v3 (.D(WriteData), .en(demultiplexer_1_out10), .Q(v3_q), .clk(CLK), .clr(CLR));
  Register s0 (.D(WriteData), .en(demultiplexer_1_out11), .Q(s0_q), .clk(CLK), .clr(CLR));
  Register s1 (.D(WriteData), .en(demultiplexer_1_out12), .Q(s1_q), .clk(CLK), .clr(CLR));
  Register s2 (.D(WriteData), .en(demultiplexer_1_out13), .Q(s2_q), .clk(CLK), .clr(CLR));
  Register s3 (.D(WriteData), .en(demultiplexer_1_out14), .Q(s3_q), .clk(CLK), .clr(CLR));
  Register io (.D(WriteData), .en(demultiplexer_1_out15), .Q(io_q), .clk(CLK), .clr(CLR));
  Multiplexer #(.select(4), .width(8), .enable("false")) multiplexer_1 (
    .in0({8{1'b0}}), .in1(t1_q), .in2(t2_q), .in3(t3_q), .in4(t4_q), .in5(t0_q), .in6(sp_q), .in7(v0_q),
    .in8(v1_q), .in9(v2_q), .in10(v3_q), .in11(s0_q), .in12(s1_q), .in13(s2_q), .in14(s3_q), .in15(io_q),
    .out(ReadData1), .sel(Src_1));
  Multiplexer #(.select(4), .width(8), .enable("false")) multiplexer_2 (
    .in0({8{1'b0}}), .in1(t1_q), .in2(t2_q), .in3(t3_q), .in4(t4_q), .in5(t0_q), .in6(sp_q), .in7(v0_q),
    .in8(v1_q), .in9(v2_q), .in10(v3_q), .in11(s0_q), .in12(s1_q), .in13(s2_q), .in14(s3_q), .in15(io_q),
    .out(ReadData2), .sel(Src_2));

  // Other names for the same wires on the sheet: D1[3:0] = Dest_1; READ_DATA_1[7:0] = ReadData1;
  //   READ_DATA_2[7:0] = ReadData2; S1[3:0] = Src_1; S2[3:0] = Src_2; WD[7:0] = WriteData
endmodule

module Memory (
  input  [7:0] Address,
  input  [7:0] WriteData,
  input  CLK,
  input  CLR,
  input  MemWrite,
  input  MemRead,
  output [7:0] Data_Read
);

  RAM #(.bus("separate")) ram_1 (
    .addr(Address), .din(WriteData), .data(Data_Read), .str(MemWrite), .sel(1'b1), .clk(CLK), .ld(MemRead),
    .clr(CLR));
endmodule

module Address_Decoder (
  input  [7:0] Address,
  output [3:0] Output_Peripheral_Address,
  output Output_Peripheral
);

  and and_1 (Output_Peripheral, Address[4], Address[5], Address[6], Address[7]);
  Multiplexer #(.width(4), .enable("false")) multiplexer_1 (
    .in0(4'b0000), .in1(Address[3:0]), .out(Output_Peripheral_Address), .sel(Output_Peripheral));

  // Notes on the sheet:
  //   1111 XXXX
  //   This format of 16 addresses are reserved for I/O
  //   1010 XXXX
  //   Last 4 bits (XXXX) is I/O address
endmodule

module _16_x_32_Display_Adapter (
  input  CLK,
  input  CLR,
  input  UPDATE,
  input  FLUSH_BUFFER,
  input  [7:0] X,
  input  X_Enable,
  input  [7:0] Y,
  input  Y_Enable,
  output [15:0] out_9,
  output [15:0] out_10,
  output [15:0] out_11,
  output [15:0] out_12,
  output [15:0] out_13,
  output [15:0] out_14,
  output [15:0] out_15,
  output [15:0] out_16,
  output [15:0] out_17,
  output [15:0] out_18,
  output [15:0] out_19,
  output [15:0] out_20,
  output [15:0] out_21,
  output [15:0] out_22,
  output [15:0] out_23,
  output [15:0] out_24,
  output [15:0] out_25,
  output [15:0] out_26,
  output [15:0] out_27,
  output [15:0] out_28,
  output [15:0] out_29,
  output [15:0] out_30,
  output [15:0] out_31,
  output [15:0] out_32,
  output [15:0] out_33,
  output [15:0] out_34,
  output [15:0] out_35,
  output [15:0] out_36,
  output [15:0] out_37,
  output [15:0] out_38,
  output [15:0] out_39,
  output [15:0] out_40
);

  wire or_1_out, register_3_q, register_4_q;
  wire [3:0] bit_extender_2_out;
  wire [4:0] bit_extender_1_out;
  wire [7:0] register_1_q, register_2_q;
  wire [15:0] n32_x_16b_sticky_reg_1_r0, n32_x_16b_sticky_reg_1_r0_2, n32_x_16b_sticky_reg_1_r1,
       n32_x_16b_sticky_reg_1_r1_2, n32_x_16b_sticky_reg_1_r2, n32_x_16b_sticky_reg_1_r2_2,
       n32_x_16b_sticky_reg_1_r3, n32_x_16b_sticky_reg_1_r3_2, n32_x_16b_sticky_reg_1_r4,
       n32_x_16b_sticky_reg_1_r4_2, n32_x_16b_sticky_reg_1_r5, n32_x_16b_sticky_reg_1_r5_2,
       n32_x_16b_sticky_reg_1_r6, n32_x_16b_sticky_reg_1_r6_2, n32_x_16b_sticky_reg_1_r7,
       n32_x_16b_sticky_reg_1_r7_2, n32_x_16b_sticky_reg_1_r8, n32_x_16b_sticky_reg_1_r8_2,
       n32_x_16b_sticky_reg_1_r9, n32_x_16b_sticky_reg_1_r9_2, n32_x_16b_sticky_reg_1_r10,
       n32_x_16b_sticky_reg_1_r10_2, n32_x_16b_sticky_reg_1_r11, n32_x_16b_sticky_reg_1_r11_2,
       n32_x_16b_sticky_reg_1_r12, n32_x_16b_sticky_reg_1_r12_2, n32_x_16b_sticky_reg_1_r13,
       n32_x_16b_sticky_reg_1_r13_2, n32_x_16b_sticky_reg_1_r14, n32_x_16b_sticky_reg_1_r14_2,
       n32_x_16b_sticky_reg_1_r15, n32_x_16b_sticky_reg_1_r15_2, shifter_1_out, undriven, undriven_2,
       undriven_3, undriven_4, undriven_5, undriven_6, undriven_7, undriven_8, undriven_9, undriven_10,
       undriven_11, undriven_12, undriven_13, undriven_14, undriven_15, undriven_16, undriven_17,
       undriven_18, undriven_19, undriven_20, undriven_21, undriven_22, undriven_23, undriven_24,
       undriven_25, undriven_26, undriven_27, undriven_28, undriven_29, undriven_30, undriven_31, undriven_32;

  Register register_1 (.D(X), .en(X_Enable), .Q(register_1_q), .clk(CLK));  // open: clr
  Register register_2 (.D(Y), .en(Y_Enable), .Q(register_2_q), .clk(CLK));  // open: clr
  Bit_Extender #(.out_width(5)) bit_extender_1 (.in(register_1_q), .out(bit_extender_1_out));
  Bit_Extender #(.out_width(4)) bit_extender_2 (.in(register_2_q), .out(bit_extender_2_out));
  Shifter #(.width(16)) shifter_1 (.in(16'h1), .\dist (bit_extender_2_out), .out(shifter_1_out));
  // Probe on shifter_1_out
  or or_1 (or_1_out, CLR, register_4_q);
  Register #(.width(1), .trigger("falling")) register_3 (
    .D(FLUSH_BUFFER), .en(1'b1), .Q(register_3_q), .clk(CLK));  // open: clr
  Register #(.width(1), .trigger("falling")) register_4 (
    .D(register_3_q), .en(1'b1), .Q(register_4_q), .clk(CLK));  // open: clr
  _32_x_16b_STICKY_REG u_32_x_16b_sticky_reg_1 (
    .CLK(CLK), .CLR(or_1_out), .FLUSH(UPDATE), .ADDR(bit_extender_1_out), .WRITE_DATA(shifter_1_out),
    .R0(n32_x_16b_sticky_reg_1_r0), .R1(n32_x_16b_sticky_reg_1_r1), .R2(n32_x_16b_sticky_reg_1_r2),
    .R3(n32_x_16b_sticky_reg_1_r3), .R4(n32_x_16b_sticky_reg_1_r4), .R5(n32_x_16b_sticky_reg_1_r5),
    .R6(n32_x_16b_sticky_reg_1_r6), .R7(n32_x_16b_sticky_reg_1_r7), .R8(n32_x_16b_sticky_reg_1_r8),
    .R9(n32_x_16b_sticky_reg_1_r9), .R10(n32_x_16b_sticky_reg_1_r10), .R11(n32_x_16b_sticky_reg_1_r11),
    .R12(n32_x_16b_sticky_reg_1_r12), .R13(n32_x_16b_sticky_reg_1_r13), .R14(n32_x_16b_sticky_reg_1_r14),
    .R15(n32_x_16b_sticky_reg_1_r15), .R0_2(n32_x_16b_sticky_reg_1_r0_2), .R1_2(n32_x_16b_sticky_reg_1_r1_2),
    .R2_2(n32_x_16b_sticky_reg_1_r2_2), .R3_2(n32_x_16b_sticky_reg_1_r3_2),
    .R4_2(n32_x_16b_sticky_reg_1_r4_2), .R5_2(n32_x_16b_sticky_reg_1_r5_2),
    .R6_2(n32_x_16b_sticky_reg_1_r6_2), .R7_2(n32_x_16b_sticky_reg_1_r7_2),
    .R8_2(n32_x_16b_sticky_reg_1_r8_2), .R9_2(n32_x_16b_sticky_reg_1_r9_2),
    .R10_2(n32_x_16b_sticky_reg_1_r10_2), .R11_2(n32_x_16b_sticky_reg_1_r11_2),
    .R12_2(n32_x_16b_sticky_reg_1_r12_2), .R13_2(n32_x_16b_sticky_reg_1_r13_2),
    .R14_2(n32_x_16b_sticky_reg_1_r14_2), .R15_2(n32_x_16b_sticky_reg_1_r15_2));
  _32_x_16b_BUFFER u_32_x_16b_buffer_1 (
    .CLK(CLK), .CLR(CLR), .FLUSH(FLUSH_BUFFER), .R0(n32_x_16b_sticky_reg_1_r0),
    .R1(n32_x_16b_sticky_reg_1_r1), .R2(n32_x_16b_sticky_reg_1_r2), .R3(n32_x_16b_sticky_reg_1_r3),
    .R4(n32_x_16b_sticky_reg_1_r4), .R5(n32_x_16b_sticky_reg_1_r5), .R6(n32_x_16b_sticky_reg_1_r6),
    .R7(n32_x_16b_sticky_reg_1_r7), .R8(n32_x_16b_sticky_reg_1_r8), .R9(n32_x_16b_sticky_reg_1_r9),
    .R10(n32_x_16b_sticky_reg_1_r10), .R11(n32_x_16b_sticky_reg_1_r11), .R12(n32_x_16b_sticky_reg_1_r12),
    .R13(n32_x_16b_sticky_reg_1_r13), .R14(n32_x_16b_sticky_reg_1_r14), .R15(n32_x_16b_sticky_reg_1_r15),
    .R0_2(n32_x_16b_sticky_reg_1_r0_2), .R1_2(n32_x_16b_sticky_reg_1_r1_2),
    .R2_2(n32_x_16b_sticky_reg_1_r2_2), .R3_2(n32_x_16b_sticky_reg_1_r3_2),
    .R4_2(n32_x_16b_sticky_reg_1_r4_2), .R5_2(n32_x_16b_sticky_reg_1_r5_2),
    .R6_2(n32_x_16b_sticky_reg_1_r6_2), .R7_2(n32_x_16b_sticky_reg_1_r7_2),
    .R8_2(n32_x_16b_sticky_reg_1_r8_2), .R9_2(n32_x_16b_sticky_reg_1_r9_2),
    .R10_2(n32_x_16b_sticky_reg_1_r10_2), .R11_2(n32_x_16b_sticky_reg_1_r11_2),
    .R12_2(n32_x_16b_sticky_reg_1_r12_2), .R13_2(n32_x_16b_sticky_reg_1_r13_2),
    .R14_2(n32_x_16b_sticky_reg_1_r14_2), .R15_2(n32_x_16b_sticky_reg_1_r15_2), .R0_3(out_9), .R1_3(out_10),
    .R2_3(out_11), .R3_3(out_12), .R4_3(out_13), .R5_3(out_14), .R6_3(out_15), .R7_3(out_16), .R8_3(out_17),
    .R9_3(out_18), .R10_3(out_19), .R11_3(out_20), .R12_3(out_21), .R13_3(out_22), .R14_3(out_23),
    .R15_3(out_24), .R0_4(out_25), .R1_4(out_26), .R2_4(out_27), .R3_4(out_28), .R4_4(out_29), .R5_4(out_30),
    .R6_4(out_31), .R7_4(out_32), .R8_4(out_33), .R9_4(out_34), .R10_4(out_35), .R11_4(out_36),
    .R12_4(out_37), .R13_4(out_38), .R14_4(out_39), .R15_4(out_40));
  DotMatrix #(.matrixcols(32), .matrixrows(16)) dotmatrix_1 (
    .col0(undriven_16), .col1(undriven), .col2(undriven_2), .col3(undriven_3), .col4(undriven_17),
    .col5(undriven_18), .col6(undriven_4), .col7(undriven_19), .col8(undriven_5), .col9(undriven_20),
    .col10(undriven_21), .col11(undriven_6), .col12(undriven_22), .col13(undriven_7), .col14(undriven_8),
    .col15(undriven_23), .col16(undriven_24), .col17(undriven_25), .col18(undriven_9), .col19(undriven_10),
    .col20(undriven_26), .col21(undriven_27), .col22(undriven_28), .col23(undriven_11), .col24(undriven_12),
    .col25(undriven_29), .col26(undriven_13), .col27(undriven_30), .col28(undriven_14), .col29(undriven_31),
    .col30(undriven_32), .col31(undriven_15));

  // Notes on the sheet:
  //   After flushing the screen values to display clear the sticky register.
  //   Give a one full clock delay before clearing the registers to give time to read them.
  //   MSB
  //   LSB
endmodule

module _32_x_16b_STICKY_REG (
  input  CLK,
  input  CLR,
  input  FLUSH,
  input  [4:0] ADDR,
  input  [15:0] WRITE_DATA,
  output [15:0] R0,
  output [15:0] R1,
  output [15:0] R2,
  output [15:0] R3,
  output [15:0] R4,
  output [15:0] R5,
  output [15:0] R6,
  output [15:0] R7,
  output [15:0] R8,
  output [15:0] R9,
  output [15:0] R10,
  output [15:0] R11,
  output [15:0] R12,
  output [15:0] R13,
  output [15:0] R14,
  output [15:0] R15,
  output [15:0] R0_2,
  output [15:0] R1_2,
  output [15:0] R2_2,
  output [15:0] R3_2,
  output [15:0] R4_2,
  output [15:0] R5_2,
  output [15:0] R6_2,
  output [15:0] R7_2,
  output [15:0] R8_2,
  output [15:0] R9_2,
  output [15:0] R10_2,
  output [15:0] R11_2,
  output [15:0] R12_2,
  output [15:0] R13_2,
  output [15:0] R14_2,
  output [15:0] R15_2
);

  wire demultiplexer_1_out0, demultiplexer_1_out1, demultiplexer_1_out2, demultiplexer_1_out3,
       demultiplexer_1_out4, demultiplexer_1_out5, demultiplexer_1_out6, demultiplexer_1_out7,
       demultiplexer_1_out8, demultiplexer_1_out9, demultiplexer_1_out10, demultiplexer_1_out11,
       demultiplexer_1_out12, demultiplexer_1_out13, demultiplexer_1_out14, demultiplexer_1_out15,
       demultiplexer_1_out16, demultiplexer_1_out17, demultiplexer_1_out18, demultiplexer_1_out19,
       demultiplexer_1_out20, demultiplexer_1_out21, demultiplexer_1_out22, demultiplexer_1_out23,
       demultiplexer_1_out24, demultiplexer_1_out25, demultiplexer_1_out26, demultiplexer_1_out27,
       demultiplexer_1_out28, demultiplexer_1_out29, demultiplexer_1_out30, demultiplexer_1_out31;
  wire [15:0] or_1_out, or_2_out, or_3_out, or_4_out, or_5_out, or_6_out, or_7_out, or_8_out, or_9_out,
       or_10_out, or_11_out, or_12_out, or_13_out, or_14_out, or_15_out, or_16_out, or_17_out, or_18_out,
       or_19_out, or_20_out, or_21_out, or_22_out, or_23_out, or_24_out, or_25_out, or_26_out, or_27_out,
       or_28_out, or_29_out, or_30_out, or_31_out, or_32_out;

  Demultiplexer #(.select(5), .enable("false")) demultiplexer_1 (
    .out0(demultiplexer_1_out0), .out1(demultiplexer_1_out1), .out2(demultiplexer_1_out2),
    .out3(demultiplexer_1_out3), .out4(demultiplexer_1_out4), .out5(demultiplexer_1_out5),
    .out6(demultiplexer_1_out6), .out7(demultiplexer_1_out7), .out8(demultiplexer_1_out8),
    .out9(demultiplexer_1_out9), .out10(demultiplexer_1_out10), .out11(demultiplexer_1_out11),
    .out12(demultiplexer_1_out12), .out13(demultiplexer_1_out13), .out14(demultiplexer_1_out14),
    .out15(demultiplexer_1_out15), .out16(demultiplexer_1_out16), .out17(demultiplexer_1_out17),
    .out18(demultiplexer_1_out18), .out19(demultiplexer_1_out19), .out20(demultiplexer_1_out20),
    .out21(demultiplexer_1_out21), .out22(demultiplexer_1_out22), .out23(demultiplexer_1_out23),
    .out24(demultiplexer_1_out24), .out25(demultiplexer_1_out25), .out26(demultiplexer_1_out26),
    .out27(demultiplexer_1_out27), .out28(demultiplexer_1_out28), .out29(demultiplexer_1_out29),
    .out30(demultiplexer_1_out30), .out31(demultiplexer_1_out31), .in(FLUSH), .sel(ADDR));
  assign or_1_out = R1 | WRITE_DATA;  // OR_Gate or_1, 16 bits wide
  assign or_2_out = R3 | WRITE_DATA;  // OR_Gate or_2, 16 bits wide
  assign or_3_out = R5 | WRITE_DATA;  // OR_Gate or_3, 16 bits wide
  assign or_4_out = R7 | WRITE_DATA;  // OR_Gate or_4, 16 bits wide
  assign or_5_out = R9 | WRITE_DATA;  // OR_Gate or_5, 16 bits wide
  assign or_6_out = R11 | WRITE_DATA;  // OR_Gate or_6, 16 bits wide
  assign or_7_out = R13 | WRITE_DATA;  // OR_Gate or_7, 16 bits wide
  assign or_8_out = R15 | WRITE_DATA;  // OR_Gate or_8, 16 bits wide
  assign or_9_out = R1_2 | WRITE_DATA;  // OR_Gate or_9, 16 bits wide
  assign or_10_out = R3_2 | WRITE_DATA;  // OR_Gate or_10, 16 bits wide
  assign or_11_out = R5_2 | WRITE_DATA;  // OR_Gate or_11, 16 bits wide
  assign or_12_out = R7_2 | WRITE_DATA;  // OR_Gate or_12, 16 bits wide
  assign or_13_out = R9_2 | WRITE_DATA;  // OR_Gate or_13, 16 bits wide
  assign or_14_out = R11_2 | WRITE_DATA;  // OR_Gate or_14, 16 bits wide
  assign or_15_out = R13_2 | WRITE_DATA;  // OR_Gate or_15, 16 bits wide
  assign or_16_out = R15_2 | WRITE_DATA;  // OR_Gate or_16, 16 bits wide
  Register #(.width(16)) register_1 (.D(or_1_out), .en(demultiplexer_1_out1), .Q(R1), .clk(CLK), .clr(CLR));
  Register #(.width(16)) register_2 (.D(or_2_out), .en(demultiplexer_1_out3), .Q(R3), .clk(CLK), .clr(CLR));
  Register #(.width(16)) register_3 (.D(or_3_out), .en(demultiplexer_1_out5), .Q(R5), .clk(CLK), .clr(CLR));
  Register #(.width(16)) register_4 (.D(or_4_out), .en(demultiplexer_1_out7), .Q(R7), .clk(CLK), .clr(CLR));
  Register #(.width(16)) register_5 (.D(or_5_out), .en(demultiplexer_1_out9), .Q(R9), .clk(CLK), .clr(CLR));
  Register #(.width(16)) register_6 (.D(or_6_out), .en(demultiplexer_1_out11), .Q(R11), .clk(CLK), .clr(CLR));
  Register #(.width(16)) register_7 (.D(or_7_out), .en(demultiplexer_1_out13), .Q(R13), .clk(CLK), .clr(CLR));
  Register #(.width(16)) register_8 (.D(or_8_out), .en(demultiplexer_1_out15), .Q(R15), .clk(CLK), .clr(CLR));
  Register #(.width(16)) register_9 (.D(or_9_out), .en(demultiplexer_1_out17), .Q(R1_2), .clk(CLK), .clr(CLR));
  Register #(.width(16)) register_10 (.D(or_10_out), .en(demultiplexer_1_out19), .Q(R3_2), .clk(CLK), .clr(CLR));
  Register #(.width(16)) register_11 (.D(or_11_out), .en(demultiplexer_1_out21), .Q(R5_2), .clk(CLK), .clr(CLR));
  Register #(.width(16)) register_12 (.D(or_12_out), .en(demultiplexer_1_out23), .Q(R7_2), .clk(CLK), .clr(CLR));
  Register #(.width(16)) register_13 (.D(or_13_out), .en(demultiplexer_1_out25), .Q(R9_2), .clk(CLK), .clr(CLR));
  Register #(.width(16)) register_14 (.D(or_14_out), .en(demultiplexer_1_out27), .Q(R11_2), .clk(CLK), .clr(CLR));
  Register #(.width(16)) register_15 (.D(or_15_out), .en(demultiplexer_1_out29), .Q(R13_2), .clk(CLK), .clr(CLR));
  Register #(.width(16)) register_16 (.D(or_16_out), .en(demultiplexer_1_out31), .Q(R15_2), .clk(CLK), .clr(CLR));
  assign or_17_out = R0 | WRITE_DATA;  // OR_Gate or_17, 16 bits wide
  Register #(.width(16)) register_17 (.D(or_17_out), .en(demultiplexer_1_out0), .Q(R0), .clk(CLK), .clr(CLR));
  assign or_18_out = R2 | WRITE_DATA;  // OR_Gate or_18, 16 bits wide
  Register #(.width(16)) register_18 (.D(or_18_out), .en(demultiplexer_1_out2), .Q(R2), .clk(CLK), .clr(CLR));
  assign or_19_out = R4 | WRITE_DATA;  // OR_Gate or_19, 16 bits wide
  Register #(.width(16)) register_19 (.D(or_19_out), .en(demultiplexer_1_out4), .Q(R4), .clk(CLK), .clr(CLR));
  assign or_20_out = R6 | WRITE_DATA;  // OR_Gate or_20, 16 bits wide
  Register #(.width(16)) register_20 (.D(or_20_out), .en(demultiplexer_1_out6), .Q(R6), .clk(CLK), .clr(CLR));
  assign or_21_out = R8 | WRITE_DATA;  // OR_Gate or_21, 16 bits wide
  Register #(.width(16)) register_21 (.D(or_21_out), .en(demultiplexer_1_out8), .Q(R8), .clk(CLK), .clr(CLR));
  assign or_22_out = R10 | WRITE_DATA;  // OR_Gate or_22, 16 bits wide
  Register #(.width(16)) register_22 (.D(or_22_out), .en(demultiplexer_1_out10), .Q(R10), .clk(CLK), .clr(CLR));
  assign or_23_out = R12 | WRITE_DATA;  // OR_Gate or_23, 16 bits wide
  Register #(.width(16)) register_23 (.D(or_23_out), .en(demultiplexer_1_out12), .Q(R12), .clk(CLK), .clr(CLR));
  assign or_24_out = R14 | WRITE_DATA;  // OR_Gate or_24, 16 bits wide
  Register #(.width(16)) register_24 (.D(or_24_out), .en(demultiplexer_1_out14), .Q(R14), .clk(CLK), .clr(CLR));
  assign or_25_out = R0_2 | WRITE_DATA;  // OR_Gate or_25, 16 bits wide
  Register #(.width(16)) register_25 (.D(or_25_out), .en(demultiplexer_1_out16), .Q(R0_2), .clk(CLK), .clr(CLR));
  assign or_26_out = R2_2 | WRITE_DATA;  // OR_Gate or_26, 16 bits wide
  Register #(.width(16)) register_26 (.D(or_26_out), .en(demultiplexer_1_out18), .Q(R2_2), .clk(CLK), .clr(CLR));
  assign or_27_out = R4_2 | WRITE_DATA;  // OR_Gate or_27, 16 bits wide
  Register #(.width(16)) register_27 (.D(or_27_out), .en(demultiplexer_1_out20), .Q(R4_2), .clk(CLK), .clr(CLR));
  assign or_28_out = R6_2 | WRITE_DATA;  // OR_Gate or_28, 16 bits wide
  Register #(.width(16)) register_28 (.D(or_28_out), .en(demultiplexer_1_out22), .Q(R6_2), .clk(CLK), .clr(CLR));
  assign or_29_out = R8_2 | WRITE_DATA;  // OR_Gate or_29, 16 bits wide
  Register #(.width(16)) register_29 (.D(or_29_out), .en(demultiplexer_1_out24), .Q(R8_2), .clk(CLK), .clr(CLR));
  assign or_30_out = R10_2 | WRITE_DATA;  // OR_Gate or_30, 16 bits wide
  Register #(.width(16)) register_30 (.D(or_30_out), .en(demultiplexer_1_out26), .Q(R10_2), .clk(CLK), .clr(CLR));
  assign or_31_out = R12_2 | WRITE_DATA;  // OR_Gate or_31, 16 bits wide
  Register #(.width(16)) register_31 (.D(or_31_out), .en(demultiplexer_1_out28), .Q(R12_2), .clk(CLK), .clr(CLR));
  assign or_32_out = R14_2 | WRITE_DATA;  // OR_Gate or_32, 16 bits wide
  Register #(.width(16)) register_32 (.D(or_32_out), .en(demultiplexer_1_out30), .Q(R14_2), .clk(CLK), .clr(CLR));

  // Other names for the same wires on the sheet: WD[15:0] = WRITE_DATA; WRITE = FLUSH
endmodule

module _32_x_16b_BUFFER (
  input  CLK,
  input  CLR,
  input  FLUSH,
  input  [15:0] R0,
  input  [15:0] R1,
  input  [15:0] R2,
  input  [15:0] R3,
  input  [15:0] R4,
  input  [15:0] R5,
  input  [15:0] R6,
  input  [15:0] R7,
  input  [15:0] R8,
  input  [15:0] R9,
  input  [15:0] R10,
  input  [15:0] R11,
  input  [15:0] R12,
  input  [15:0] R13,
  input  [15:0] R14,
  input  [15:0] R15,
  input  [15:0] R0_2,
  input  [15:0] R1_2,
  input  [15:0] R2_2,
  input  [15:0] R3_2,
  input  [15:0] R4_2,
  input  [15:0] R5_2,
  input  [15:0] R6_2,
  input  [15:0] R7_2,
  input  [15:0] R8_2,
  input  [15:0] R9_2,
  input  [15:0] R10_2,
  input  [15:0] R11_2,
  input  [15:0] R12_2,
  input  [15:0] R13_2,
  input  [15:0] R14_2,
  input  [15:0] R15_2,
  output [15:0] R0_3,
  output [15:0] R1_3,
  output [15:0] R2_3,
  output [15:0] R3_3,
  output [15:0] R4_3,
  output [15:0] R5_3,
  output [15:0] R6_3,
  output [15:0] R7_3,
  output [15:0] R8_3,
  output [15:0] R9_3,
  output [15:0] R10_3,
  output [15:0] R11_3,
  output [15:0] R12_3,
  output [15:0] R13_3,
  output [15:0] R14_3,
  output [15:0] R15_3,
  output [15:0] R0_4,
  output [15:0] R1_4,
  output [15:0] R2_4,
  output [15:0] R3_4,
  output [15:0] R4_4,
  output [15:0] R5_4,
  output [15:0] R6_4,
  output [15:0] R7_4,
  output [15:0] R8_4,
  output [15:0] R9_4,
  output [15:0] R10_4,
  output [15:0] R11_4,
  output [15:0] R12_4,
  output [15:0] R13_4,
  output [15:0] R14_4,
  output [15:0] R15_4
);

  Register #(.width(16)) register_1 (.D(R1), .en(FLUSH), .Q(R1_3), .clk(CLK), .clr(CLR));
  Register #(.width(16)) register_2 (.D(R3), .en(FLUSH), .Q(R3_3), .clk(CLK), .clr(CLR));
  Register #(.width(16)) register_3 (.D(R5), .en(FLUSH), .Q(R5_3), .clk(CLK), .clr(CLR));
  Register #(.width(16)) register_4 (.D(R7), .en(FLUSH), .Q(R7_3), .clk(CLK), .clr(CLR));
  Register #(.width(16)) register_5 (.D(R9), .en(FLUSH), .Q(R9_3), .clk(CLK), .clr(CLR));
  Register #(.width(16)) register_6 (.D(R11), .en(FLUSH), .Q(R11_3), .clk(CLK), .clr(CLR));
  Register #(.width(16)) register_7 (.D(R13), .en(FLUSH), .Q(R13_3), .clk(CLK), .clr(CLR));
  Register #(.width(16)) register_8 (.D(R15), .en(FLUSH), .Q(R15_3), .clk(CLK), .clr(CLR));
  Register #(.width(16)) register_9 (.D(R1_2), .en(FLUSH), .Q(R1_4), .clk(CLK), .clr(CLR));
  Register #(.width(16)) register_10 (.D(R3_2), .en(FLUSH), .Q(R3_4), .clk(CLK), .clr(CLR));
  Register #(.width(16)) register_11 (.D(R5_2), .en(FLUSH), .Q(R5_4), .clk(CLK), .clr(CLR));
  Register #(.width(16)) register_12 (.D(R7_2), .en(FLUSH), .Q(R7_4), .clk(CLK), .clr(CLR));
  Register #(.width(16)) register_13 (.D(R9_2), .en(FLUSH), .Q(R9_4), .clk(CLK), .clr(CLR));
  Register #(.width(16)) register_14 (.D(R11_2), .en(FLUSH), .Q(R11_4), .clk(CLK), .clr(CLR));
  Register #(.width(16)) register_15 (.D(R13_2), .en(FLUSH), .Q(R13_4), .clk(CLK), .clr(CLR));
  Register #(.width(16)) register_16 (.D(R15_2), .en(FLUSH), .Q(R15_4), .clk(CLK), .clr(CLR));
  Register #(.width(16)) register_17 (.D(R0), .en(FLUSH), .Q(R0_3), .clk(CLK), .clr(CLR));
  Register #(.width(16)) register_18 (.D(R2), .en(FLUSH), .Q(R2_3), .clk(CLK), .clr(CLR));
  Register #(.width(16)) register_19 (.D(R4), .en(FLUSH), .Q(R4_3), .clk(CLK), .clr(CLR));
  Register #(.width(16)) register_20 (.D(R6), .en(FLUSH), .Q(R6_3), .clk(CLK), .clr(CLR));
  Register #(.width(16)) register_21 (.D(R8), .en(FLUSH), .Q(R8_3), .clk(CLK), .clr(CLR));
  Register #(.width(16)) register_22 (.D(R10), .en(FLUSH), .Q(R10_3), .clk(CLK), .clr(CLR));
  Register #(.width(16)) register_23 (.D(R12), .en(FLUSH), .Q(R12_3), .clk(CLK), .clr(CLR));
  Register #(.width(16)) register_24 (.D(R14), .en(FLUSH), .Q(R14_3), .clk(CLK), .clr(CLR));
  Register #(.width(16)) register_25 (.D(R0_2), .en(FLUSH), .Q(R0_4), .clk(CLK), .clr(CLR));
  Register #(.width(16)) register_26 (.D(R2_2), .en(FLUSH), .Q(R2_4), .clk(CLK), .clr(CLR));
  Register #(.width(16)) register_27 (.D(R4_2), .en(FLUSH), .Q(R4_4), .clk(CLK), .clr(CLR));
  Register #(.width(16)) register_28 (.D(R6_2), .en(FLUSH), .Q(R6_4), .clk(CLK), .clr(CLR));
  Register #(.width(16)) register_29 (.D(R8_2), .en(FLUSH), .Q(R8_4), .clk(CLK), .clr(CLR));
  Register #(.width(16)) register_30 (.D(R10_2), .en(FLUSH), .Q(R10_4), .clk(CLK), .clr(CLR));
  Register #(.width(16)) register_31 (.D(R12_2), .en(FLUSH), .Q(R12_4), .clk(CLK), .clr(CLR));
  Register #(.width(16)) register_32 (.D(R14_2), .en(FLUSH), .Q(R14_4), .clk(CLK), .clr(CLR));

  // Other names for the same wires on the sheet: WRITE = FLUSH
endmodule

module Random_Number_Generator (
  input  CLK,
  input  Enable,
  output [7:0] Random
);

  wire [7:0] random_1_out;

  Random #(.seed(235423)) random_1 (.clk(CLK), .next(CLK), .out(random_1_out));  // open: clr
  Multiplexer #(.width(8), .enable("false")) multiplexer_1 (
    .in0({8{1'b0}}), .in1(random_1_out), .out(Random), .sel(Enable));
endmodule

module Binary_to_BCD (
  input  [7:0] Binary,
  input  WRITE,
  input  Signed,
  input  CLK,
  input  CLR,
  output [3:0] Ones,
  output [3:0] Tens,
  output [3:0] Hundreds,
  output Sign_Bit
);

  wire [7:0] double_dabble_unit_8_output, multiplexer_1_out, register_1_q, subtractor_1_out;
  wire [19:0] double_dabble_unit_1_output, double_dabble_unit_2_output, double_dabble_unit_3_output,
       double_dabble_unit_4_output, double_dabble_unit_5_output, double_dabble_unit_6_output,
       double_dabble_unit_7_output;

  Register register_1 (.D(Binary), .en(WRITE), .Q(register_1_q), .clk(CLK), .clr(CLR));
  Multiplexer #(.width(8), .enable("false")) multiplexer_1 (
    .in0(register_1_q), .in1(subtractor_1_out), .out(multiplexer_1_out), .sel(Sign_Bit));
  Subtractor subtractor_1 (.a({8{1'b0}}), .b(register_1_q), .out(subtractor_1_out));  // open: bin, bout
  and and_1 (Sign_Bit, register_1_q[7], Signed);
  Double_Dabble_Unit double_dabble_unit_1 (
    .Input({{12{1'b0}}, multiplexer_1_out}), .Output(double_dabble_unit_1_output));
  Double_Dabble_Unit double_dabble_unit_2 (.Input(double_dabble_unit_1_output), .Output(double_dabble_unit_2_output));
  Double_Dabble_Unit double_dabble_unit_3 (.Input(double_dabble_unit_2_output), .Output(double_dabble_unit_3_output));
  Double_Dabble_Unit double_dabble_unit_4 (.Input(double_dabble_unit_3_output), .Output(double_dabble_unit_4_output));
  Double_Dabble_Unit double_dabble_unit_5 (.Input(double_dabble_unit_6_output), .Output(double_dabble_unit_5_output));
  Double_Dabble_Unit double_dabble_unit_6 (.Input(double_dabble_unit_4_output), .Output(double_dabble_unit_6_output));
  Double_Dabble_Unit double_dabble_unit_7 (.Input(double_dabble_unit_5_output), .Output(double_dabble_unit_7_output));
  Double_Dabble_Unit double_dabble_unit_8 (
    .Input(double_dabble_unit_7_output), .Output({Hundreds, Tens, Ones, double_dabble_unit_8_output}));
  // Probe on Binary
  // Probe on Ones
  // Probe on Tens
  // Probe on Hundreds

  // Other names for the same wires on the sheet: IS_SIGNED = Signed

  // Notes on the sheet:
  //   Convert to twos complement and set sign bit if signed number and a negative number
  //   Scratch Space
  //   DOUBLE DABBLE ALGORITHM TO CONVERT BINARY TO BCD
endmodule

module Double_Dabble_Unit (
  input  [19:0] Input,
  output [19:0] Output
);

  wire adder_1_cout, adder_2_cout, adder_3_cout, comparator_1_eq, comparator_1_gt, comparator_2_eq,
       comparator_2_gt, comparator_3_eq, comparator_3_gt, or_1_out, or_2_out, or_3_out;
  wire [3:0] adder_1_out, adder_2_out, adder_3_out, multiplexer_1_out, multiplexer_2_out, multiplexer_3_out;

  Comparator #(.width(4), .mode("unsigned")) comparator_1 (
    .a(Input[11:8]), .b(4'b0101), .gt(comparator_1_gt), .eq(comparator_1_eq));  // open: lt
  Comparator #(.width(4), .mode("unsigned")) comparator_2 (
    .a(Input[15:12]), .b(4'b0101), .gt(comparator_2_gt), .eq(comparator_2_eq));  // open: lt
  Comparator #(.width(4), .mode("unsigned")) comparator_3 (
    .a(Input[19:16]), .b(4'b0101), .gt(comparator_3_gt), .eq(comparator_3_eq));  // open: lt
  or or_1 (or_1_out, comparator_1_gt, comparator_1_eq);
  or or_2 (or_2_out, comparator_2_gt, comparator_2_eq);
  or or_3 (or_3_out, comparator_3_gt, comparator_3_eq);
  Multiplexer #(.width(4), .enable("false")) multiplexer_1 (
    .in0(4'b0000), .in1(4'b0011), .out(multiplexer_1_out), .sel(or_1_out));
  Multiplexer #(.width(4), .enable("false")) multiplexer_2 (
    .in0(4'b0000), .in1(4'b0011), .out(multiplexer_2_out), .sel(or_2_out));
  Multiplexer #(.width(4), .enable("false")) multiplexer_3 (
    .in0(4'b0000), .in1(4'b0011), .out(multiplexer_3_out), .sel(or_3_out));
  Adder #(.width(4)) adder_1 (
    .a(Input[11:8]), .b(multiplexer_1_out), .out(adder_1_out), .cin(1'b0), .cout(adder_1_cout));
  Adder #(.width(4)) adder_2 (
    .a(Input[15:12]), .b(multiplexer_2_out), .out(adder_2_out), .cin(1'b0), .cout(adder_2_cout));
  Adder #(.width(4)) adder_3 (
    .a(Input[19:16]), .b(multiplexer_3_out), .out(adder_3_out), .cin(1'b0), .cout(adder_3_cout));
  Shifter #(.width(20)) shifter_1 (
    .in({adder_3_out, adder_2_out, adder_1_out, Input[7:0]}), .\dist (5'b00001), .out(Output));
  // also tied to GND on the sheet: {adder_1_cout, adder_2_cout, adder_3_cout}
endmodule

module BCD_to_Single_7_Seg_Display (
  input  [3:0] BCD,
  output M,
  output LU,
  output UU,
  output RU,
  output LD,
  output DD,
  output RD
);

  wire demultiplexer_1_out0, demultiplexer_1_out1, demultiplexer_1_out2, demultiplexer_1_out3,
       demultiplexer_1_out4, demultiplexer_1_out5, demultiplexer_1_out6, demultiplexer_1_out7,
       demultiplexer_1_out8, demultiplexer_1_out9;

  Demultiplexer #(.select(4), .enable("false")) demultiplexer_1 (
    .out0(demultiplexer_1_out0), .out1(demultiplexer_1_out1), .out2(demultiplexer_1_out2),
    .out3(demultiplexer_1_out3), .out4(demultiplexer_1_out4), .out5(demultiplexer_1_out5),
    .out6(demultiplexer_1_out6), .out7(demultiplexer_1_out7), .out8(demultiplexer_1_out8),
    .out9(demultiplexer_1_out9), .in(1'b1), .sel(BCD));  // open: out10, out11, out12, out13, out14, out15
  or or_1 (M, demultiplexer_1_out2, demultiplexer_1_out3, demultiplexer_1_out4, demultiplexer_1_out5, demultiplexer_1_out6, demultiplexer_1_out8, demultiplexer_1_out9);
  or or_2 (LU, demultiplexer_1_out0, demultiplexer_1_out4, demultiplexer_1_out5, demultiplexer_1_out6, demultiplexer_1_out8, demultiplexer_1_out9);
  or or_3 (UU, demultiplexer_1_out0, demultiplexer_1_out2, demultiplexer_1_out3, demultiplexer_1_out5, demultiplexer_1_out6, demultiplexer_1_out7, demultiplexer_1_out8, demultiplexer_1_out9);
  or or_4 (RU, demultiplexer_1_out0, demultiplexer_1_out1, demultiplexer_1_out2, demultiplexer_1_out3, demultiplexer_1_out4, 1'b0, demultiplexer_1_out7, demultiplexer_1_out8, demultiplexer_1_out9);
  or or_5 (LD, demultiplexer_1_out2, demultiplexer_1_out0, demultiplexer_1_out6, demultiplexer_1_out8);
  or or_6 (DD, demultiplexer_1_out0, demultiplexer_1_out2, demultiplexer_1_out3, demultiplexer_1_out5, demultiplexer_1_out6, demultiplexer_1_out8, demultiplexer_1_out9);
  or or_7 (RD, demultiplexer_1_out0, demultiplexer_1_out1, demultiplexer_1_out3, demultiplexer_1_out4, demultiplexer_1_out5, demultiplexer_1_out6, demultiplexer_1_out7, demultiplexer_1_out8, demultiplexer_1_out9);
endmodule

module _8_bit_to_7_Seg_Adapter (
  input  [7:0] Data,
  input  Write_Enable,
  input  Is_Signed,
  input  CLK,
  input  CLR,
  output out_6,
  output out_7,
  output out_8,
  output out_9,
  output out_10,
  output out_11,
  output out_12,
  output out_13,
  output out_14,
  output out_15,
  output out_16,
  output out_17,
  output out_18,
  output out_19,
  output out_20,
  output out_21,
  output out_22,
  output out_23,
  output out_24,
  output out_25,
  output out_26,
  output Sign
);

  wire [3:0] binary_to_bcd_1_hundreds, binary_to_bcd_1_ones, binary_to_bcd_1_tens;

  Binary_to_BCD binary_to_bcd_1 (
    .Binary(Data), .WRITE(Write_Enable), .Signed(Is_Signed), .Ones(binary_to_bcd_1_ones),
    .Tens(binary_to_bcd_1_tens), .Hundreds(binary_to_bcd_1_hundreds), .Sign_Bit(Sign), .CLK(CLK), .CLR(CLR));
  BCD_to_Single_7_Seg_Display bcd_to_single_7_seg_display_1 (
    .BCD(binary_to_bcd_1_ones), .LD(out_10), .M(out_6), .RU(out_9), .LU(out_7), .UU(out_8), .DD(out_11),
    .RD(out_12));
  BCD_to_Single_7_Seg_Display bcd_to_single_7_seg_display_2 (
    .BCD(binary_to_bcd_1_tens), .LD(out_17), .M(out_13), .RU(out_16), .LU(out_14), .UU(out_15), .DD(out_18),
    .RD(out_19));
  BCD_to_Single_7_Seg_Display bcd_to_single_7_seg_display_3 (
    .BCD(binary_to_bcd_1_hundreds), .LD(out_24), .M(out_20), .RU(out_23), .LU(out_21), .UU(out_22),
    .DD(out_25), .RD(out_26));

  // Notes on the sheet:
  //   ONES
  //   TENS
  //   HUNDREDS
  //   SIGN
endmodule

module _7_Segment_Adapter_NOT_USED (
  input  [7:0] in_1,
  output UU,
  output LU,
  output RU,
  output M,
  output LD,
  output RD,
  output DD,
  output UU_2,
  output LU_2,
  output RU_2,
  output M_2,
  output LD_2,
  output RD_2,
  output DD_2
);

  wire demultiplexer_1_out0, demultiplexer_1_out1, demultiplexer_1_out2, demultiplexer_1_out3,
       demultiplexer_1_out4, demultiplexer_1_out5, demultiplexer_1_out6, demultiplexer_1_out7,
       demultiplexer_1_out8, demultiplexer_1_out9, demultiplexer_1_out10, demultiplexer_1_out11,
       demultiplexer_1_out12, demultiplexer_1_out13, demultiplexer_1_out14, demultiplexer_1_out15,
       demultiplexer_1_out16, demultiplexer_1_out17, demultiplexer_1_out18, demultiplexer_1_out19,
       demultiplexer_1_out20, demultiplexer_1_out21, demultiplexer_1_out22, demultiplexer_1_out23,
       demultiplexer_1_out24, demultiplexer_1_out25, demultiplexer_1_out26, demultiplexer_1_out27,
       demultiplexer_1_out28, demultiplexer_1_out29, demultiplexer_1_out30, demultiplexer_1_out31, T0, T1,
       T2, T3, U0, U1, U2, U3, U4, U5, U6, U7, U8, U9;
  wire [4:0] bit_extender_1_out;

  Demultiplexer #(.select(5), .enable("false")) demultiplexer_1 (
    .out0(demultiplexer_1_out0), .out1(demultiplexer_1_out1), .out2(demultiplexer_1_out2),
    .out3(demultiplexer_1_out3), .out4(demultiplexer_1_out4), .out5(demultiplexer_1_out5),
    .out6(demultiplexer_1_out6), .out7(demultiplexer_1_out7), .out8(demultiplexer_1_out8),
    .out9(demultiplexer_1_out9), .out10(demultiplexer_1_out10), .out11(demultiplexer_1_out11),
    .out12(demultiplexer_1_out12), .out13(demultiplexer_1_out13), .out14(demultiplexer_1_out14),
    .out15(demultiplexer_1_out15), .out16(demultiplexer_1_out16), .out17(demultiplexer_1_out17),
    .out18(demultiplexer_1_out18), .out19(demultiplexer_1_out19), .out20(demultiplexer_1_out20),
    .out21(demultiplexer_1_out21), .out22(demultiplexer_1_out22), .out23(demultiplexer_1_out23),
    .out24(demultiplexer_1_out24), .out25(demultiplexer_1_out25), .out26(demultiplexer_1_out26),
    .out27(demultiplexer_1_out27), .out28(demultiplexer_1_out28), .out29(demultiplexer_1_out29),
    .out30(demultiplexer_1_out30), .out31(demultiplexer_1_out31), .in(1'b1), .sel(bit_extender_1_out));
  Bit_Extender #(.out_width(5)) bit_extender_1 (.in(in_1), .out(bit_extender_1_out));
  or or_1 (T0, demultiplexer_1_out0, demultiplexer_1_out1, demultiplexer_1_out2, demultiplexer_1_out3, demultiplexer_1_out4, demultiplexer_1_out5, demultiplexer_1_out6, demultiplexer_1_out7, demultiplexer_1_out8, demultiplexer_1_out9);
  or or_2 (T1, demultiplexer_1_out10, demultiplexer_1_out11, demultiplexer_1_out12, demultiplexer_1_out13, demultiplexer_1_out14, demultiplexer_1_out15, demultiplexer_1_out16, demultiplexer_1_out17, demultiplexer_1_out18, demultiplexer_1_out19);
  or or_3 (U0, demultiplexer_1_out0, demultiplexer_1_out10, demultiplexer_1_out20, demultiplexer_1_out30);
  or or_4 (T2, demultiplexer_1_out20, demultiplexer_1_out21, demultiplexer_1_out22, demultiplexer_1_out23, demultiplexer_1_out24, demultiplexer_1_out25, demultiplexer_1_out26, demultiplexer_1_out27, demultiplexer_1_out28, demultiplexer_1_out29);
  or or_5 (U1, demultiplexer_1_out1, demultiplexer_1_out11, demultiplexer_1_out21, demultiplexer_1_out31);
  or or_6 (U3, demultiplexer_1_out3, demultiplexer_1_out13, demultiplexer_1_out23);
  or or_7 (U2, demultiplexer_1_out2, demultiplexer_1_out12, demultiplexer_1_out22);
  or or_8 (T3, demultiplexer_1_out30, demultiplexer_1_out31);
  or or_9 (U4, demultiplexer_1_out4, demultiplexer_1_out14, demultiplexer_1_out24);
  or or_10 (U5, demultiplexer_1_out5, demultiplexer_1_out15, demultiplexer_1_out25);
  or or_11 (U6, demultiplexer_1_out6, demultiplexer_1_out16, demultiplexer_1_out26);
  or or_12 (U8, demultiplexer_1_out8, demultiplexer_1_out18, demultiplexer_1_out28);
  or or_13 (U7, demultiplexer_1_out7, demultiplexer_1_out17, demultiplexer_1_out27);
  or or_14 (U9, demultiplexer_1_out9, demultiplexer_1_out19, demultiplexer_1_out29);
  or or_15 (UU, U0, U2, U3, U5, U6, U7, U8, U9);
  or or_16 (LU, U0, U4, U5, U6, U8, U9);
  or or_17 (RU, U0, U1, U2, U3, U4, 1'b0, U7, U8, U9);
  or or_18 (M, U2, U3, U4, U5, U6, U8, U9);
  or or_19 (LD, U2, U0, U6, U8);
  or or_20 (RD, U0, U1, U3, U4, U5, U6, U7, U8, U9);
  or or_21 (DD, U0, U2, U3, U5, U6, U8, U9);
  or or_22 (UU_2, T0, T2, T3, 1'b0, 1'b0, 1'b0, 1'b0, 1'b0);
  or or_23 (LU_2, T0, 1'b0, 1'b0, 1'b0, 1'b0, 1'b0);
  or or_24 (RU_2, T0, T1, T2, T3, 1'b0, 1'b0, 1'b0, 1'b0, 1'b0);
  or or_25 (M_2, T2, T3, 1'b0, 1'b0, 1'b0, 1'b0, 1'b0);
  or or_26 (LD_2, T2, T0, 1'b0, 1'b0);
  or or_27 (RD_2, T0, T1, T3, 1'b0, 1'b0, 1'b0, 1'b0, 1'b0, 1'b0);
  or or_28 (DD_2, T0, T2, T3, 1'b0, 1'b0, 1'b0, 1'b0);
endmodule
