// Logisim project NONPIPELINED_MIPS.circ as structural Verilog: 6 circuits, main circuit Instruction
module main (
  input  RESET
);

  wire ALU_SRC, BRANCH, CLK, control_1_beq, control_1_bneq, JUMP, MEM_READ, MEM_TO_REG, MEM_WRITE, REG_DEST,
       REG_WRITE, ZERO;
  wire [2:0] ALU_OP;
  wire [3:0] instruction_1_dest, instruction_1_src_1, instruction_1_src_2, multiplexer_1_out, OP_CODE,
       SHIFT_AMT;
  wire [7:0] adder_1_out, adder_2_out, alu_8_by_art_1_p5, CURRENT_PC, IMM, JUMP_ADDR, memory_1_data_read,
       multiplexer_3_out, multiplexer_4_out, multiplexer_6_out, registers_1_readdata1, registers_1_readdata2,
       UPDATED_PC;
  wire [23:0] REG_10S, REG_432;

  // Probe on CURRENT_PC
  Clock u_CLK (.out(CLK));
  // Probe on OP_CODE
  Instruction instruction_1 (
    .PC_Write(UPDATED_PC), .CLK(CLK), .RESET(RESET), .PC_Read(CURRENT_PC), .Opcode(OP_CODE),
    .Src_1(instruction_1_src_1), .Src_2(instruction_1_src_2), .Dest(instruction_1_dest),
    .Shift_Amt(SHIFT_AMT), .Addr___Immd(IMM), .Jump_Addr(JUMP_ADDR));
  Control control_1 (
    .OP_Code(OP_CODE), .RegDst(REG_DEST), .ALUSrc(ALU_SRC), .MemToReg(MEM_TO_REG), .RegWrite(REG_WRITE),
    .MemRead(MEM_READ), .MemWrite(MEM_WRITE), .beq(control_1_beq), .bneq(control_1_bneq), .Jump(JUMP),
    .ALUOp(ALU_OP));
  Adder adder_1 (.a(CURRENT_PC), .b(8'h1), .out(adder_1_out), .cin(1'b0));  // open: cout
  Multiplexer #(.width(4), .enable("false")) multiplexer_1 (
    .in0(instruction_1_src_2), .in1(instruction_1_dest), .out(multiplexer_1_out), .sel(REG_DEST));
  Multiplexer #(.enable("false")) multiplexer_2 (.in0(control_1_bneq), .in1(control_1_beq), .out(BRANCH), .sel(ZERO));
  Adder adder_2 (.a(adder_1_out), .b(IMM), .out(adder_2_out), .cin(1'b0));  // open: cout
  Multiplexer #(.width(8), .enable("false")) multiplexer_3 (
    .in0(adder_1_out), .in1(adder_2_out), .out(multiplexer_3_out), .sel(BRANCH));
  Registers registers_1 (
    .RegWrite(REG_WRITE), .Src_1(instruction_1_src_1), .Src_2(instruction_1_src_2),
    .Dest_1(multiplexer_1_out), .WriteData(multiplexer_6_out), .CLK(CLK), .CLR(RESET),
    .ReadData1(registers_1_readdata1), .ReadData2(registers_1_readdata2), .t4__t3__t2(REG_432),
    .t1__t0__sp(REG_10S));
  Multiplexer #(.width(8), .enable("false")) multiplexer_4 (
    .in0(registers_1_readdata2), .in1(IMM), .out(multiplexer_4_out), .sel(ALU_SRC));
  Multiplexer #(.width(8), .enable("false")) multiplexer_5 (
    .in0(multiplexer_3_out), .in1(JUMP_ADDR), .out(UPDATED_PC), .sel(JUMP));
  // ALU_8_by_ART alu_8_by_art_1: pin names not known; wires that end beside it: registers_1_readdata1, multiplexer_4_out, ALU_OP, ZERO, alu_8_by_art_1_p5
  // Probe on REG_10S[15:8]
  // Probe on REG_10S[23:16]
  // Probe on REG_432[7:0]
  // Probe on REG_432[15:8]
  // Probe on REG_432[23:16]
  // Probe on REG_10S[7:0]
  Memory memory_1 (
    .Address(alu_8_by_art_1_p5), .WriteData(registers_1_readdata2), .CLK(CLK), .CLR(RESET),
    .Data_Read(memory_1_data_read), .MemRead(MEM_READ), .MemWrite(MEM_WRITE));
  Multiplexer #(.width(8), .enable("false")) multiplexer_6 (
    .in0(alu_8_by_art_1_p5), .in1(memory_1_data_read), .out(multiplexer_6_out), .sel(MEM_TO_REG));
endmodule

module Instruction (
  input  [7:0] PC_Write,
  input  CLK,
  input  RESET,
  output [7:0] PC_Read,
  output [3:0] Opcode,
  output [3:0] Src_1,
  output [3:0] Src_2,
  output [3:0] Dest,
  output [3:0] Shift_Amt,
  output [7:0] Addr___Immd,
  output [7:0] Jump_Addr
);

  Register register_1 (.D(PC_Write), .en(1'b1), .Q(PC_Read), .clk(CLK), .clr(RESET));
  ROM #(.dataWidth(20)) rom_1 (.addr(PC_Read), .data({Opcode, Jump_Addr, Addr___Immd}), .sel(1'b1));

  assign Dest = Addr___Immd[7:4];
  assign Shift_Amt = Addr___Immd[3:0];
  assign Src_1 = Jump_Addr[7:4];
  assign Src_2 = Jump_Addr[3:0];

  // Notes on the sheet:
  //   contents of rom_1 (hex, n*v repeats v):
  //   a06ff a050a a0101 7150b a0102 71509 a0101 a0201 a0402 c1230 c0210 c0320 a4401 554fb f1000 a0301
  //   86300 96601 13504 86500 96601 b5405 86400 96601 844a2 86400 96601 d41a2 86100 96601 a1288 86200
  //   96601 92381 3230 86300 96601 a0546 a0155 65120 86200 96601 223fe 86300 96601 a0380 a04aa e3410 86100
  //   96601 312ff 86200 96601 f3500
endmodule

module Control (
  input  [3:0] OP_Code,
  output RegDst,
  output ALUSrc,
  output MemToReg,
  output RegWrite,
  output MemRead,
  output MemWrite,
  output beq,
  output bneq,
  output Jump,
  output [2:0] ALUOp
);

  ROM #(.addrWidth(4), .dataWidth(12)) rom_1 (
    .addr(OP_Code), .data({RegDst, ALUSrc, MemToReg, RegWrite, MemRead, MemWrite, beq, bneq, Jump, ALUOp}),
    .sel(1'b1));

  // Notes on the sheet:
  //   contents of rom_1 (hex, n*v repeats v):
  //   901 506 503 502 904 11 903 21 c40 501 500 505 900 780 902 8
endmodule

module Registers (
  input  RegWrite,
  input  [3:0] Src_1,
  input  [3:0] Src_2,
  input  [3:0] Dest_1,
  input  [7:0] WriteData,
  input  CLK,
  input  CLR,
  output [23:0] t4__t3__t2,
  output [23:0] t1__t0__sp,
  output [7:0] ReadData1,
  output [7:0] ReadData2
);

  wire demultiplexer_1_out1, demultiplexer_1_out2, demultiplexer_1_out3, demultiplexer_1_out4,
       demultiplexer_1_out5, demultiplexer_1_out6;
  wire [2:0] bit_extender_1_out, bit_extender_2_out, bit_extender_3_out;

  Register t1 (.D(WriteData), .en(demultiplexer_1_out1), .Q(t1__t0__sp[23:16]), .clk(CLK), .clr(CLR));
  Bit_Extender #(.in_width(4), .out_width(3)) bit_extender_1 (.in(Src_1), .out(bit_extender_1_out));
  Bit_Extender #(.in_width(4), .out_width(3)) bit_extender_2 (.in(Dest_1), .out(bit_extender_2_out));
  Register t2 (.D(WriteData), .en(demultiplexer_1_out2), .Q(t4__t3__t2[7:0]), .clk(CLK), .clr(CLR));
  Multiplexer #(.select(3), .width(8), .enable("false")) multiplexer_1 (
    .in0({8{1'b0}}), .in1(t1__t0__sp[23:16]), .in2(t4__t3__t2[7:0]), .in3(t4__t3__t2[15:8]),
    .in4(t4__t3__t2[23:16]), .in5(t1__t0__sp[15:8]), .in6(t1__t0__sp[7:0]), .out(ReadData1),
    .sel(bit_extender_1_out));  // open: in7
  Demultiplexer #(.select(3), .enable("false")) demultiplexer_1 (
    .out1(demultiplexer_1_out1), .out2(demultiplexer_1_out2), .out3(demultiplexer_1_out3),
    .out4(demultiplexer_1_out4), .out5(demultiplexer_1_out5), .out6(demultiplexer_1_out6), .in(RegWrite),
    .sel(bit_extender_2_out));  // open: out0, out7
  Register t3 (.D(WriteData), .en(demultiplexer_1_out3), .Q(t4__t3__t2[15:8]), .clk(CLK), .clr(CLR));
  Register t4 (.D(WriteData), .en(demultiplexer_1_out4), .Q(t4__t3__t2[23:16]), .clk(CLK), .clr(CLR));
  Bit_Extender #(.in_width(4), .out_width(3)) bit_extender_3 (.in(Src_2), .out(bit_extender_3_out));
  Register t0 (.D(WriteData), .en(demultiplexer_1_out5), .Q(t1__t0__sp[15:8]), .clk(CLK), .clr(CLR));
  Multiplexer #(.select(3), .width(8), .enable("false")) multiplexer_2 (
    .in0({8{1'b0}}), .in1(t1__t0__sp[23:16]), .in2(t4__t3__t2[7:0]), .in3(t4__t3__t2[15:8]),
    .in4(t4__t3__t2[23:16]), .in5(t1__t0__sp[15:8]), .in6(t1__t0__sp[7:0]), .out(ReadData2),
    .sel(bit_extender_3_out));  // open: in7
  Register sp (.D(WriteData), .en(demultiplexer_1_out6), .Q(t1__t0__sp[7:0]), .clk(CLK), .clr(CLR));

  // Other names for the same wires on the sheet: S1[3:0] = Src_1; S2[3:0] = Src_2; WD[7:0] = WriteData
endmodule

module Memory (
  input  [7:0] Address,
  input  [7:0] WriteData,
  input  CLK,
  input  CLR,
  input  MemWrite,
  input  MemRead,
  output [7:0] Data_Read
);

  RAM #(.bus("separate")) ram_1 (
    .addr(Address), .din(WriteData), .data(Data_Read), .str(MemWrite), .sel(1'b1), .clk(CLK), .ld(MemRead),
    .clr(CLR));
endmodule

module ALU_TEST (
  input  [7:0] in_1,
  input  [7:0] in_2,
  input  [2:0] in_3,
  output out_4,
  output [7:0] out_5
);

  // ALU_8_by_ART alu_8_by_art_1: pin names not known; wires that end beside it: in_1, in_2, in_3, out_4, out_5
endmodule
