// Logisim project _MIPS_WITH_IO_PERIPHERAL.circ as structural Verilog: 31 circuits, main circuit main
module main (
  input  RESET
);

  wire alu_8_by_art_1_p4, alu_8_by_art_1_p6, ALU_SRC, Branch_PC_Src, CLK, cntrl_1_alusrc, cntrl_1_beq,
       cntrl_1_bneq, cntrl_1_memread, cntrl_1_memtoreg, cntrl_1_memwrite, cntrl_1_regdst, cntrl_1_regwrite,
       ex_mem_1_beq_2, ex_mem_1_bneq_2, ex_mem_1_mem_to_reg_2, ex_mem_1_zero_2, EX_MEM_REG_WRITE, Hazard,
       id_ex_1_beq_2, id_ex_1_bneq_2, id_ex_1_jump_2, id_ex_1_mem_to_reg_2, id_ex_1_mem_write_2,
       id_ex_1_reg_write_2, ID_EX_MEM_READ, JUMP_PC_Src, MEM_READ, MEM_TO_REG, MEM_WB_REG_WRITE, MEM_WRITE,
       REG_DEST;
  wire [1:0] forwarding_unit_1_forward_a, forwarding_unit_1_forward_b;
  wire [2:0] ALU_OP, cntrl_1_aluop;
  wire [3:0] ex_mem_1_write_reg_2, id_1_dest, id_1_opcode, id_1_src_1, id_1_src_2, id_ex_1_dest_reg_2,
       id_ex_1_src_1_2, id_ex_1_src_2_2, mem_wb_1_write_reg_2, multiplexer_6_out;
  wire [7:0] adder_1_out, alu_8_by_art_1_p2, alu_8_by_art_1_p5, Branch_PC, ex_mem_1_reg_data_2_2,
       EX_MEM_RegData, id_1_addr___immd, id_ex_1_pc_2, id_ex_1_reg_data_1_2, id_ex_1_reg_data_2_2, ID_EX_IMM,
       if_1_pc___1, if_1_pc_read, if_id_1_pc_2, Jump_Address, mem_1_data_read, mem_wb_1_alu_result_2,
       mem_wb_1_reg_data_2_2, MEM_WB_RegData, multiplexer_1_out, multiplexer_2_out, multiplexer_3_out,
       multiplexer_4_out, reg_file_1_readdata1, reg_file_1_readdata2;
  wire [19:0] if_1_instruction, if_id_1_instruction_2;

  Clock u_CLK (.out(CLK));
  Multiplexer #(.width(8), .enable("false")) multiplexer_1 (
    .in0(multiplexer_2_out), .in1(Jump_Address), .out(multiplexer_1_out), .sel(JUMP_PC_Src));
  Multiplexer #(.width(8), .enable("false")) multiplexer_2 (
    .in0(if_1_pc___1), .in1(Branch_PC), .out(multiplexer_2_out), .sel(Branch_PC_Src));
  // Probe on if_1_pc_read
  IF if_1 (
    .PC_Write(multiplexer_1_out), .CLK(CLK), .RESET(RESET), .PC_Read(if_1_pc_read),
    .Instruction(if_1_instruction), .PC___1(if_1_pc___1), .Stall(Hazard));
  IF_ID if_id_1 (
    .Instruction(if_1_instruction), .Instruction_2(if_id_1_instruction_2), .PC(if_1_pc___1),
    .PC_2(if_id_1_pc_2), .CLK(CLK), .CLR(RESET), .Stall(Hazard));
  ID id_1 (
    .Instruction(if_id_1_instruction_2), .Opcode(id_1_opcode), .Src_1(id_1_src_1), .Src_2(id_1_src_2),
    .Dest(id_1_dest), .Addr___Immd(id_1_addr___immd), .Jump_Addr(Jump_Address));
  CNTRL cntrl_1 (
    .OP_Code(id_1_opcode), .RegDst(cntrl_1_regdst), .ALUSrc(cntrl_1_alusrc), .MemToReg(cntrl_1_memtoreg),
    .RegWrite(cntrl_1_regwrite), .MemRead(cntrl_1_memread), .MemWrite(cntrl_1_memwrite), .beq(cntrl_1_beq),
    .bneq(cntrl_1_bneq), .Jump(JUMP_PC_Src), .ALUOp(cntrl_1_aluop), .NOP(Hazard));
  REG_FILE reg_file_1 (
    .Src_1(id_1_src_1), .Src_2(id_1_src_2), .WriteData(MEM_WB_RegData), .CLK(CLK), .CLR(RESET),
    .ReadData1(reg_file_1_readdata1), .ReadData2(reg_file_1_readdata2), .Dest_1(mem_wb_1_write_reg_2),
    .RegWrite(MEM_WB_REG_WRITE));  // open: t4__t3__t2, t1__t0__sp
  HAZARD_DETECTION hazard_detection_1 (
    .ID_EX_MemRead(ID_EX_MEM_READ), .ID_EX_RegisterRt(id_ex_1_dest_reg_2), .IF_ID_RegisterRs(id_1_src_1),
    .IF_ID_RegisterRt(id_1_src_2), .Hazard(Hazard));
  ID_EX id_ex_1 (
    .Reg_Data_1(reg_file_1_readdata1), .Reg_Data_2(reg_file_1_readdata2), .IMM(id_1_addr___immd),
    .DEST_REG(id_1_src_2), .CLK(CLK), .CLR(RESET), .Reg_Data_1_2(id_ex_1_reg_data_1_2),
    .Reg_Data_2_2(id_ex_1_reg_data_2_2), .IMM_2(ID_EX_IMM), .DEST_REG_2(id_ex_1_dest_reg_2),
    .SRC_2(id_1_dest), .SRC_2_2(id_ex_1_src_2_2), .PC(if_id_1_pc_2), .PC_2(id_ex_1_pc_2), .SRC_1(id_1_src_1),
    .SRC_1_2(id_ex_1_src_1_2), .MEM_READ(cntrl_1_memread), .MEM_READ_2(ID_EX_MEM_READ),
    .MEM_WRITE(cntrl_1_memwrite), .MEM_WRITE_2(id_ex_1_mem_write_2), .BNEQ(cntrl_1_bneq),
    .BNEQ_2(id_ex_1_bneq_2), .BEQ(cntrl_1_beq), .BEQ_2(id_ex_1_beq_2), .JUMP(JUMP_PC_Src),
    .JUMP_2(id_ex_1_jump_2), .MEM_TO_REG(cntrl_1_memtoreg), .MEM_TO_REG_2(id_ex_1_mem_to_reg_2),
    .REG_WRITE(cntrl_1_regwrite), .REG_WRITE_2(id_ex_1_reg_write_2), .out_20(ALU_OP), .in_1(cntrl_1_aluop),
    .in_2(cntrl_1_alusrc), .out_21(ALU_SRC), .in_3(cntrl_1_regdst), .out_22(REG_DEST));
  Multiplexer #(.select(2), .width(8), .enable("false")) multiplexer_3 (
    .in0(id_ex_1_reg_data_1_2), .in1(MEM_WB_RegData), .in2(EX_MEM_RegData), .out(multiplexer_3_out),
    .sel(forwarding_unit_1_forward_a));  // open: in3
  Multiplexer #(.select(2), .width(8), .enable("false")) multiplexer_4 (
    .in0(id_ex_1_reg_data_2_2), .in1(MEM_WB_RegData), .in2(EX_MEM_RegData), .out(multiplexer_4_out),
    .sel(forwarding_unit_1_forward_b));  // open: in3
  FORWARDING_UNIT forwarding_unit_1 (
    .ID_EX_RegisterRs(id_ex_1_src_1_2), .ID_EX_RegisterRt(id_ex_1_dest_reg_2),
    .EX_MEM_RegisterRd(ex_mem_1_write_reg_2), .EX_MEM_RegWrite(EX_MEM_REG_WRITE),
    .MEM_WB_RegisterRd(mem_wb_1_write_reg_2), .MEM_WB_RegWrite(MEM_WB_REG_WRITE),
    .Forward_A(forwarding_unit_1_forward_a), .Forward_B(forwarding_unit_1_forward_b));
  // ALU_8_by_ART alu_8_by_art_1: pin names not known; wires that end beside it: multiplexer_3_out, alu_8_by_art_1_p2, ALU_OP, alu_8_by_art_1_p4, alu_8_by_art_1_p5, alu_8_by_art_1_p6
  Multiplexer #(.width(8), .enable("false")) multiplexer_5 (
    .in0(multiplexer_4_out), .in1(ID_EX_IMM), .out(alu_8_by_art_1_p2), .sel(ALU_SRC));
  Adder adder_1 (.a(id_ex_1_pc_2), .b(ID_EX_IMM), .out(adder_1_out));  // open: cin, cout
  Multiplexer #(.width(4), .enable("false")) multiplexer_6 (
    .in0(id_ex_1_dest_reg_2), .in1(id_ex_1_src_2_2), .out(multiplexer_6_out), .sel(REG_DEST));
  EX_MEM ex_mem_1 (
    .REG_WRITE(id_ex_1_reg_write_2), .ALU_RESULT(alu_8_by_art_1_p5), .WRITE_REG(multiplexer_6_out),
    .CLK(CLK), .CLR(RESET), .ALU_RESULT_2(EX_MEM_RegData), .WRITE_REG_2(ex_mem_1_write_reg_2),
    .Reg_Data_2(multiplexer_4_out), .Reg_Data_2_2(ex_mem_1_reg_data_2_2), .MEM_TO_REG(id_ex_1_mem_to_reg_2),
    .JUMP(id_ex_1_jump_2), .BNEQ(id_ex_1_bneq_2), .BEQ(id_ex_1_beq_2), .MEM_WRITE(id_ex_1_mem_write_2),
    .MEM_READ(ID_EX_MEM_READ), .ZERO(alu_8_by_art_1_p4), .MEM_READ_2(MEM_READ), .MEM_WRITE_2(MEM_WRITE),
    .BNEQ_2(ex_mem_1_bneq_2), .BEQ_2(ex_mem_1_beq_2), .JUMP_2(alu_8_by_art_1_p6),
    .MEM_TO_REG_2(ex_mem_1_mem_to_reg_2), .REG_WRITE_2(EX_MEM_REG_WRITE), .ZERO_2(ex_mem_1_zero_2),
    .PC(adder_1_out), .PC_2(Branch_PC));
  Multiplexer #(.enable("false")) multiplexer_7 (
    .in0(ex_mem_1_bneq_2), .in1(ex_mem_1_beq_2), .out(Branch_PC_Src), .sel(ex_mem_1_zero_2));
  MEM mem_1 (
    .Address(EX_MEM_RegData), .WriteData(ex_mem_1_reg_data_2_2), .Data_Read(mem_1_data_read),
    .MemWrite(MEM_WRITE), .CLK(CLK), .MemRead(MEM_READ), .CLR(RESET));
  MEM_WB mem_wb_1 (
    .ALU_RESULT(EX_MEM_RegData), .Reg_Data_2(mem_1_data_read), .CLK(CLK), .CLR(RESET),
    .ALU_RESULT_2(mem_wb_1_alu_result_2), .Reg_Data_2_2(mem_wb_1_reg_data_2_2),
    .MEM_TO_REG(ex_mem_1_mem_to_reg_2), .MEM_TO_REG_2(MEM_TO_REG), .REG_WRITE(EX_MEM_REG_WRITE),
    .REG_WRITE_2(MEM_WB_REG_WRITE), .WRITE_REG(ex_mem_1_write_reg_2), .WRITE_REG_2(mem_wb_1_write_reg_2));
  Multiplexer #(.width(8), .enable("false")) multiplexer_8 (
    .in0(mem_wb_1_alu_result_2), .in1(mem_wb_1_reg_data_2_2), .out(MEM_WB_RegData), .sel(MEM_TO_REG));

  // Other names for the same wires on the sheet: CLR = RESET
endmodule

module IF (
  input  [7:0] PC_Write,
  input  Stall,
  input  CLK,
  input  RESET,
  output [7:0] PC_Read,
  output [7:0] PC___1,
  output [19:0] Instruction
);

  wire not_1_out;

  Register register_1 (.D(PC_Write), .en(not_1_out), .Q(PC_Read), .clk(CLK), .clr(RESET));
  not not_1 (not_1_out, Stall);
  Adder adder_1 (.a(PC_Read), .b(8'h1), .out(PC___1), .cin(1'b0));  // open: cout
  ROM #(.dataWidth(20)) rom_1 (.addr(PC_Read), .data(Instruction), .sel(1'b1));

  // Notes on the sheet:
  //   contents of rom_1 (hex, n*v repeats v):
  //   a0fa0 a069f f7400 f4d00 f0500 8fd00 8fe01 8f002 a5100 f6b00 8f003 a0300 df304 23307 d4100 d4201
  //   a0703 a0804 7732a 7832d 79330 7a333 77b26 78b29 79b2c 7ab2f a4402 344c0 2111f 2220f 84100 84201
  //   a5300 f2600 7d10e a5502 355c0 f0500 d3700 d3801 77104 a3302 333c0 543fa f2200 78201 f2900 fd600
  //   f4d00 5e2f1 acc01 8fc0d dfd0f dfe0f 2dd1f 2ee0f 9c31a 23380 503ea feb00 f4d00 79b07 a22ff c07b0
  //   f1a00 7ab07 a1101 c08b0 f1a00 77bf7 a2201 c09b0 f1a00 78bf7 a11ff c0ab0 f1a00 dfd0f dfe0f 2dd1f
  //   2ee0f a0b04 a0c00 8fc0d a05c0 a5406 a0107 a0207 85100 85201 a0108 a0207 85102 85203 a0109 a0207
  //   85104 85205 a010a a0207 85106 85207 a0703 a0804 a0907 a0a01 f0400 d1200 d1301 8f200 8f301 8f002
  //   74199 a1102 311c0 f6b00 a0153 8f105 a016e 8f105 a0161 8f105 a016b 8f105 a0165 8f105 a0120 8f105
  //   a0147 8f105 a0161 8f105 a016d 8f105 a0165 8f105 a012e 8f105 a010a 8f105 a0155 8f105 a0173 8f105
  //   a0165 8f105 a0120 8f105 a0127 8f105 a0150 8f105 a016f 8f105 a016b 8f105 a0165 8f105 a0120 8f105
  //   a0154 8f105 a016f 8f105 a016f 8f105 a016c 8f105 a0127 8f105 a0120 8f105 a016f 8f105 a016e 8f105
  //   a0120 8f105 a016b 8f105 a0165 8f105 a0179 8f105 a0162 8f105 a016f 8f105 a0161 8f105 a0172 8f105
  //   a0164 8f105 a0120 8f105 a0174 8f105 a016f 8f105 a010a 8f105 a0170 8f105 a016c 8f105 a0161 8f105
  //   a0179 8f105 a012e 8f105 a010a f0300 a0159 8f105 a016f 8f105 a0175 8f105 a0120 8f105 a014c 8f105
  //   a016f 8f105 a0173 8f105 a0174 8f105 a012e 8f105 a010a 8f105 f3000 a0159 8f105 a016f 8f105 a0175
  //   8f105 a0120 8f105 a0157 8f105 a016f 8f105 a016e 8f105 a012e 8f105 a010a 8f105 f3c00
endmodule

module ID (
  input  [19:0] Instruction,
  output [3:0] Opcode,
  output [3:0] Src_1,
  output [3:0] Src_2,
  output [3:0] Dest,
  output [7:0] Addr___Immd,
  output [7:0] Jump_Addr
);


  assign Addr___Immd = Instruction[7:0];
  assign Dest = Instruction[7:4];
  assign Jump_Addr = Instruction[15:8];
  assign Opcode = Instruction[19:16];
  assign Src_1 = Instruction[15:12];
  assign Src_2 = Instruction[11:8];

  // Notes on the sheet:
  //   Shift Amt
endmodule

module REG_FILE (
  input  RegWrite,
  input  [3:0] Dest_1,
  input  [3:0] Src_1,
  input  [3:0] Src_2,
  input  [7:0] WriteData,
  input  CLK,
  input  CLR,
  output [23:0] t4__t3__t2,
  output [23:0] t1__t0__sp,
  output [7:0] ReadData1,
  output [7:0] ReadData2
);

  wire and_1_out, and_2_out, comparator_1_eq, comparator_2_eq, comparator_3_eq, comparator_4_eq,
       demultiplexer_1_out1, demultiplexer_1_out2, demultiplexer_1_out3, demultiplexer_1_out4,
       demultiplexer_1_out5, demultiplexer_1_out6, not_1_out, not_2_out;
  wire [2:0] bit_extender_1_out, bit_extender_2_out, bit_extender_3_out;
  wire [7:0] multiplexer_1_out, multiplexer_3_out;

  Comparator #(.width(4), .mode("unsigned")) comparator_1 (
    .a(Dest_1), .b(Src_1), .eq(comparator_1_eq));  // open: gt, lt
  Comparator #(.width(4), .mode("unsigned")) comparator_2 (
    .a(Dest_1), .b(4'b0000), .eq(comparator_2_eq));  // open: gt, lt
  Register t1 (.D(WriteData), .en(demultiplexer_1_out1), .Q(t1__t0__sp[23:16]), .clk(CLK), .clr(CLR));
  Bit_Extender #(.in_width(4), .out_width(3)) bit_extender_1 (.in(Src_1), .out(bit_extender_1_out));
  and and_1 (and_1_out, comparator_1_eq, RegWrite, not_1_out);
  not not_1 (not_1_out, comparator_2_eq);
  Bit_Extender #(.in_width(4), .out_width(3)) bit_extender_2 (.in(Dest_1), .out(bit_extender_2_out));
  Register t2 (.D(WriteData), .en(demultiplexer_1_out2), .Q(t4__t3__t2[7:0]), .clk(CLK), .clr(CLR));
  Multiplexer #(.select(3), .width(8), .enable("false")) multiplexer_1 (
    .in0({8{1'b0}}), .in1(t1__t0__sp[23:16]), .in2(t4__t3__t2[7:0]), .in3(t4__t3__t2[15:8]),
    .in4(t4__t3__t2[23:16]), .in5(t1__t0__sp[15:8]), .in6(t1__t0__sp[7:0]), .out(multiplexer_1_out),
    .sel(bit_extender_1_out));  // open: in7
  Multiplexer #(.width(8), .enable("false")) multiplexer_2 (
    .in0(multiplexer_1_out), .in1(WriteData), .out(ReadData1), .sel(and_1_out));
  Demultiplexer #(.select(3), .enable("false")) demultiplexer_1 (
    .out1(demultiplexer_1_out1), .out2(demultiplexer_1_out2), .out3(demultiplexer_1_out3),
    .out4(demultiplexer_1_out4), .out5(demultiplexer_1_out5), .out6(demultiplexer_1_out6), .in(RegWrite),
    .sel(bit_extender_2_out));  // open: out0, out7
  Register t3 (.D(WriteData), .en(demultiplexer_1_out3), .Q(t4__t3__t2[15:8]), .clk(CLK), .clr(CLR));
  Register t4 (.D(WriteData), .en(demultiplexer_1_out4), .Q(t4__t3__t2[23:16]), .clk(CLK), .clr(CLR));
  Bit_Extender #(.in_width(4), .out_width(3)) bit_extender_3 (.in(Src_2), .out(bit_extender_3_out));
  Comparator #(.width(4), .mode("unsigned")) comparator_3 (
    .a(Dest_1), .b(Src_2), .eq(comparator_3_eq));  // open: gt, lt
  Comparator #(.width(4), .mode("unsigned")) comparator_4 (
    .a(Dest_1), .b(4'b0000), .eq(comparator_4_eq));  // open: gt, lt
  not not_2 (not_2_out, comparator_4_eq);
  Register t0 (.D(WriteData), .en(demultiplexer_1_out5), .Q(t1__t0__sp[15:8]), .clk(CLK), .clr(CLR));
  Multiplexer #(.select(3), .width(8), .enable("false")) multiplexer_3 (
    .in0({8{1'b0}}), .in1(t1__t0__sp[23:16]), .in2(t4__t3__t2[7:0]), .in3(t4__t3__t2[15:8]),
    .in4(t4__t3__t2[23:16]), .in5(t1__t0__sp[15:8]), .in6(t1__t0__sp[7:0]), .out(multiplexer_3_out),
    .sel(bit_extender_3_out));  // open: in7
  and and_2 (and_2_out, comparator_3_eq, RegWrite, not_2_out);
  Multiplexer #(.width(8), .enable("false")) multiplexer_4 (
    .in0(multiplexer_3_out), .in1(WriteData), .out(ReadData2), .sel(and_2_out));
  Register sp (.D(WriteData), .en(demultiplexer_1_out6), .Q(t1__t0__sp[7:0]), .clk(CLK), .clr(CLR));

  // Other names for the same wires on the sheet: D1[3:0] = Dest_1; READ_DATA_1[7:0] = ReadData1;
  //   READ_DATA_2[7:0] = ReadData2; S1[3:0] = Src_1; S2[3:0] = Src_2; WD[7:0] = WriteData

  // Notes on the sheet:
  //   Registers typically write on rising edge and reads on falling edge. But in logsim we have no way (at least IDK) to control when to read.
  //   So what we are doing here is we are checking if the register we are trying to read is also getting updated if so we just pass the new value of it using MUX.
  //   But we must be careful to not pass it when reading or writing to zero register. Also the write register flag should be checked.
endmodule

module MEM (
  input  [7:0] Address,
  input  [7:0] WriteData,
  input  CLK,
  input  CLR,
  input  MemWrite,
  input  MemRead,
  output [7:0] Data_Read
);

  RAM #(.bus("separate")) ram_1 (
    .addr(Address), .din(WriteData), .data(Data_Read), .str(MemWrite), .sel(1'b1), .clk(CLK), .ld(MemRead),
    .clr(CLR));
endmodule

module CNTRL (
  input  [3:0] OP_Code,
  input  NOP,
  output RegDst,
  output ALUSrc,
  output MemToReg,
  output RegWrite,
  output MemRead,
  output MemWrite,
  output beq,
  output bneq,
  output Jump,
  output [2:0] ALUOp
);

  wire [11:0] rom_1_data;

  ROM #(.addrWidth(4), .dataWidth(12)) rom_1 (.addr(OP_Code), .data(rom_1_data), .sel(1'b1));
  Multiplexer #(.width(12), .enable("false")) multiplexer_1 (
    .in0(rom_1_data), .in1({12{1'b0}}),
    .out({RegDst, ALUSrc, MemToReg, RegWrite, MemRead, MemWrite, beq, bneq, Jump, ALUOp}), .sel(NOP));

  // Notes on the sheet:
  //   contents of rom_1 (hex, n*v repeats v):
  //   901 506 503 502 904 11 903 21 c40 501 500 505 900 780 902 8
endmodule

module IF_ID (
  input  Stall,
  input  [7:0] PC,
  input  [19:0] Instruction,
  input  CLK,
  input  CLR,
  output [7:0] PC_2,
  output [19:0] Instruction_2
);

  wire EnableWrite;

  not not_1 (EnableWrite, Stall);
  Register u_PC (.D(PC), .en(EnableWrite), .Q(PC_2), .clk(CLK), .clr(CLR));
  Register #(.width(20)) IF_ID_REG (.D(Instruction), .en(EnableWrite), .Q(Instruction_2), .clk(CLK), .clr(CLR));
endmodule

module ID_EX (
  input  [2:0] in_1,
  input  in_2,
  input  in_3,
  input  MEM_READ,
  input  MEM_WRITE,
  input  BNEQ,
  input  BEQ,
  input  JUMP,
  input  MEM_TO_REG,
  input  REG_WRITE,
  input  [7:0] PC,
  input  [7:0] Reg_Data_1,
  input  [7:0] Reg_Data_2,
  input  [7:0] IMM,
  input  [3:0] SRC_1,
  input  [3:0] SRC_2,
  input  [3:0] DEST_REG,
  input  CLK,
  input  CLR,
  output [2:0] out_20,
  output out_21,
  output out_22,
  output MEM_READ_2,
  output MEM_WRITE_2,
  output BNEQ_2,
  output BEQ_2,
  output JUMP_2,
  output MEM_TO_REG_2,
  output REG_WRITE_2,
  output [7:0] PC_2,
  output [7:0] Reg_Data_1_2,
  output [7:0] Reg_Data_2_2,
  output [7:0] IMM_2,
  output [3:0] SRC_1_2,
  output [3:0] SRC_2_2,
  output [3:0] DEST_REG_2
);

  Register #(.width(3)) ALUOp (.D(in_1), .en(1'b1), .Q(out_20), .clk(CLK), .clr(CLR));
  Register #(.width(1)) ALUSrc (.D(in_2), .en(1'b1), .Q(out_21), .clk(CLK), .clr(CLR));
  Register #(.width(1)) RegDest (.D(in_3), .en(1'b1), .Q(out_22), .clk(CLK), .clr(CLR));
  Register #(.width(1)) u_MEM_READ (.D(MEM_READ), .en(1'b1), .Q(MEM_READ_2), .clk(CLK), .clr(CLR));
  Register #(.width(1)) u_MEM_WRITE (.D(MEM_WRITE), .en(1'b1), .Q(MEM_WRITE_2), .clk(CLK), .clr(CLR));
  Register #(.width(1)) u_BNEQ (.D(BNEQ), .en(1'b1), .Q(BNEQ_2), .clk(CLK), .clr(CLR));
  Register #(.width(1)) u_BEQ (.D(BEQ), .en(1'b1), .Q(BEQ_2), .clk(CLK), .clr(CLR));
  Register #(.width(1)) u_JUMP (.D(JUMP), .en(1'b1), .Q(JUMP_2), .clk(CLK), .clr(CLR));
  Register #(.width(1)) u_MEM_TO_REG (.D(MEM_TO_REG), .en(1'b1), .Q(MEM_TO_REG_2), .clk(CLK), .clr(CLR));
  Register #(.width(1)) u_REG_WRITE (.D(REG_WRITE), .en(1'b1), .Q(REG_WRITE_2), .clk(CLK), .clr(CLR));
  Register u_PC (.D(PC), .en(1'b1), .Q(PC_2), .clk(CLK), .clr(CLR));
  Register u_Reg_Data_1 (.D(Reg_Data_1), .en(1'b1), .Q(Reg_Data_1_2), .clk(CLK), .clr(CLR));
  Register u_Reg_Data_2 (.D(Reg_Data_2), .en(1'b1), .Q(Reg_Data_2_2), .clk(CLK), .clr(CLR));
  Register u_IMM (.D(IMM), .en(1'b1), .Q(IMM_2), .clk(CLK), .clr(CLR));
  Register #(.width(4)) u_SRC_1 (.D(SRC_1), .en(1'b1), .Q(SRC_1_2), .clk(CLK), .clr(CLR));
  Register #(.width(4)) u_SRC_2 (.D(SRC_2), .en(1'b1), .Q(SRC_2_2), .clk(CLK), .clr(CLR));
  Register #(.width(4)) u_DEST_REG (.D(DEST_REG), .en(1'b1), .Q(DEST_REG_2), .clk(CLK), .clr(CLR));
endmodule

module EX_MEM (
  input  MEM_READ,
  input  MEM_WRITE,
  input  BNEQ,
  input  BEQ,
  input  JUMP,
  input  MEM_TO_REG,
  input  REG_WRITE,
  input  [7:0] PC,
  input  ZERO,
  input  [7:0] ALU_RESULT,
  input  [7:0] Reg_Data_2,
  input  [3:0] WRITE_REG,
  input  CLK,
  input  CLR,
  output MEM_READ_2,
  output MEM_WRITE_2,
  output BNEQ_2,
  output BEQ_2,
  output JUMP_2,
  output MEM_TO_REG_2,
  output REG_WRITE_2,
  output [7:0] PC_2,
  output ZERO_2,
  output [7:0] ALU_RESULT_2,
  output [7:0] Reg_Data_2_2,
  output [3:0] WRITE_REG_2
);

  Register #(.width(1)) u_MEM_READ (.D(MEM_READ), .en(1'b1), .Q(MEM_READ_2), .clk(CLK), .clr(CLR));
  Register #(.width(1)) u_MEM_WRITE (.D(MEM_WRITE), .en(1'b1), .Q(MEM_WRITE_2), .clk(CLK), .clr(CLR));
  Register #(.width(1)) u_BNEQ (.D(BNEQ), .en(1'b1), .Q(BNEQ_2), .clk(CLK), .clr(CLR));
  Register #(.width(1)) u_BEQ (.D(BEQ), .en(1'b1), .Q(BEQ_2), .clk(CLK), .clr(CLR));
  Register #(.width(1)) u_JUMP (.D(JUMP), .en(1'b1), .Q(JUMP_2), .clk(CLK), .clr(CLR));
  Register #(.width(1)) u_MEM_TO_REG (.D(MEM_TO_REG), .en(1'b1), .Q(MEM_TO_REG_2), .clk(CLK), .clr(CLR));
  Register #(.width(1)) u_REG_WRITE (.D(REG_WRITE), .en(1'b1), .Q(REG_WRITE_2), .clk(CLK), .clr(CLR));
  Register u_PC (.D(PC), .en(1'b1), .Q(PC_2), .clk(CLK), .clr(CLR));
  Register #(.width(1)) u_ZERO (.D(ZERO), .en(1'b1), .Q(ZERO_2), .clk(CLK), .clr(CLR));
  Register u_ALU_RESULT (.D(ALU_RESULT), .en(1'b1), .Q(ALU_RESULT_2), .clk(CLK), .clr(CLR));
  Register u_Reg_Data_2 (.D(Reg_Data_2), .en(1'b1), .Q(Reg_Data_2_2), .clk(CLK), .clr(CLR));
  Register #(.width(4)) u_WRITE_REG (.D(WRITE_REG), .en(1'b1), .Q(WRITE_REG_2), .clk(CLK), .clr(CLR));
endmodule

module MEM_WB (
  input  MEM_TO_REG,
  input  REG_WRITE,
  input  [7:0] ALU_RESULT,
  input  [7:0] Reg_Data_2,
  input  [3:0] WRITE_REG,
  input  CLK,
  input  CLR,
  output MEM_TO_REG_2,
  output REG_WRITE_2,
  output [7:0] ALU_RESULT_2,
  output [7:0] Reg_Data_2_2,
  output [3:0] WRITE_REG_2
);

  Register #(.width(1)) u_MEM_TO_REG (.D(MEM_TO_REG), .en(1'b1), .Q(MEM_TO_REG_2), .clk(CLK), .clr(CLR));
  Register #(.width(1)) u_REG_WRITE (.D(REG_WRITE), .en(1'b1), .Q(REG_WRITE_2), .clk(CLK), .clr(CLR));
  Register u_ALU_RESULT (.D(ALU_RESULT), .en(1'b1), .Q(ALU_RESULT_2), .clk(CLK), .clr(CLR));
  Register u_Reg_Data_2 (.D(Reg_Data_2), .en(1'b1), .Q(Reg_Data_2_2), .clk(CLK), .clr(CLR));
  Register #(.width(4)) u_WRITE_REG (.D(WRITE_REG), .en(1'b1), .Q(WRITE_REG_2), .clk(CLK), .clr(CLR));
endmodule

module FORWARDING_UNIT (
  input  [3:0] ID_EX_RegisterRs,
  input  [3:0] ID_EX_RegisterRt,
  input  [3:0] EX_MEM_RegisterRd,
  input  EX_MEM_RegWrite,
  input  [3:0] MEM_WB_RegisterRd,
  input  MEM_WB_RegWrite,
  output [1:0] Forward_A,
  output [1:0] Forward_B
);

  wire comparator_1_eq, comparator_2_eq, comparator_3_eq, comparator_4_eq, comparator_5_eq, comparator_6_eq,
       EX_Hazard_A, EX_Hazard_B, MEM_Hazard_A, MEM_Hazard_B, not_1_out, not_2_out;
  wire [1:0] bit_extender_1_out, bit_extender_2_out;

  Comparator #(.width(4), .mode("unsigned")) comparator_1 (
    .a(EX_MEM_RegisterRd), .b(4'b0000), .eq(comparator_1_eq));  // open: gt, lt
  Comparator #(.width(4), .mode("unsigned")) comparator_2 (
    .a(EX_MEM_RegisterRd), .b(ID_EX_RegisterRs), .eq(comparator_2_eq));  // open: gt, lt
  Comparator #(.width(4), .mode("unsigned")) comparator_3 (
    .a(EX_MEM_RegisterRd), .b(ID_EX_RegisterRt), .eq(comparator_3_eq));  // open: gt, lt
  Comparator #(.width(4), .mode("unsigned")) comparator_4 (
    .a(MEM_WB_RegisterRd), .b(4'b0000), .eq(comparator_4_eq));  // open: gt, lt
  Comparator #(.width(4), .mode("unsigned")) comparator_5 (
    .a(MEM_WB_RegisterRd), .b(ID_EX_RegisterRs), .eq(comparator_5_eq));  // open: gt, lt
  Comparator #(.width(4), .mode("unsigned")) comparator_6 (
    .a(MEM_WB_RegisterRd), .b(ID_EX_RegisterRt), .eq(comparator_6_eq));  // open: gt, lt
  not not_1 (not_1_out, comparator_1_eq);
  not not_2 (not_2_out, comparator_4_eq);
  assign bit_extender_1_out = {{1{1'b0}}, MEM_Hazard_A};  // Bit_Extender bit_extender_1
  assign bit_extender_2_out = {{1{1'b0}}, MEM_Hazard_B};  // Bit_Extender bit_extender_2
  and and_1 (EX_Hazard_A, EX_MEM_RegWrite, not_1_out, comparator_2_eq);
  and and_2 (EX_Hazard_B, EX_MEM_RegWrite, not_1_out, comparator_3_eq);
  and and_3 (MEM_Hazard_A, MEM_WB_RegWrite, not_2_out, comparator_5_eq);
  and and_4 (MEM_Hazard_B, MEM_WB_RegWrite, not_2_out, comparator_6_eq);
  Multiplexer #(.width(2), .enable("false")) multiplexer_1 (
    .in0(bit_extender_1_out), .in1(2'b10), .out(Forward_A), .sel(EX_Hazard_A));
  Multiplexer #(.width(2), .enable("false")) multiplexer_2 (
    .in0(bit_extender_2_out), .in1(2'b10), .out(Forward_B), .sel(EX_Hazard_B));

  // Notes on the sheet:
  //   EX HAZARD
  //   MEM HAZARD
endmodule

module HAZARD_DETECTION (
  input  ID_EX_MemRead,
  input  [3:0] ID_EX_RegisterRt,
  input  [3:0] IF_ID_RegisterRs,
  input  [3:0] IF_ID_RegisterRt,
  output Hazard
);

  wire comparator_1_eq, comparator_2_eq, or_1_out;

  Comparator #(.width(4), .mode("unsigned")) comparator_1 (
    .a(ID_EX_RegisterRt), .b(IF_ID_RegisterRs), .eq(comparator_1_eq));  // open: gt, lt
  Comparator #(.width(4), .mode("unsigned")) comparator_2 (
    .a(ID_EX_RegisterRt), .b(IF_ID_RegisterRt), .eq(comparator_2_eq));  // open: gt, lt
  or or_1 (or_1_out, comparator_1_eq, comparator_2_eq);
  and and_1 (Hazard, ID_EX_MemRead, or_1_out);

  // Notes on the sheet:
  //   We always write to Rt register in case of lw. So no need to consider ID/EX.RegisterRd
endmodule

module COMPUTER_SETUP (
  input  RESET
);

  wire A, B, C, CLK, D, E, E4, E13, F, G, H, I, J, K, L, M, mips_extended_io_1_io_0, mips_extended_io_1_io_1,
       mips_extended_io_1_io_2, mips_extended_io_1_io_3, mips_extended_io_1_io_5, mips_extended_io_1_io_14,
       mips_extended_io_1_io_15, N, O, or_1_out, P, Q, R, S, Sign, T, U;
  wire [3:0] binary_to_bcd_1_hundreds, binary_to_bcd_1_ones, binary_to_bcd_1_tens, mips_extended_io_1_io_addr;
  wire [6:0] bit_extender_1_out, keyboard_1_data;
  wire [7:0] Input_00, Input_01, Input_02, Input_03, Input_04, Input_05, Input_06, Input_07, Input_08,
       Input_09, Input_10, Input_11, Input_12, Input_13, Input_14, Input_15, mips_extended_io_1_current_pc,
       READ, register_1_q, register_2_q, WRITE;
  wire [15:0] n16_x_32_display_adapter_1_out_9, n16_x_32_display_adapter_1_out_10,
       n16_x_32_display_adapter_1_out_11, n16_x_32_display_adapter_1_out_12,
       n16_x_32_display_adapter_1_out_13, n16_x_32_display_adapter_1_out_14,
       n16_x_32_display_adapter_1_out_15, n16_x_32_display_adapter_1_out_16,
       n16_x_32_display_adapter_1_out_17, n16_x_32_display_adapter_1_out_18,
       n16_x_32_display_adapter_1_out_19, n16_x_32_display_adapter_1_out_20,
       n16_x_32_display_adapter_1_out_21, n16_x_32_display_adapter_1_out_22,
       n16_x_32_display_adapter_1_out_23, n16_x_32_display_adapter_1_out_24,
       n16_x_32_display_adapter_1_out_25, n16_x_32_display_adapter_1_out_26,
       n16_x_32_display_adapter_1_out_27, n16_x_32_display_adapter_1_out_28,
       n16_x_32_display_adapter_1_out_29, n16_x_32_display_adapter_1_out_30,
       n16_x_32_display_adapter_1_out_31, n16_x_32_display_adapter_1_out_32,
       n16_x_32_display_adapter_1_out_33, n16_x_32_display_adapter_1_out_34,
       n16_x_32_display_adapter_1_out_35, n16_x_32_display_adapter_1_out_36,
       n16_x_32_display_adapter_1_out_37, n16_x_32_display_adapter_1_out_38,
       n16_x_32_display_adapter_1_out_39, n16_x_32_display_adapter_1_out_40;

  // Probe on mips_extended_io_1_current_pc
  Multiplexer #(.select(4), .width(8), .enable("false")) multiplexer_1 (
    .in0(Input_00), .in1(Input_01), .in2(Input_02), .in3(Input_03), .in4(Input_04), .in5(Input_05),
    .in6(Input_06), .in7(Input_07), .in8(Input_08), .in9(Input_09), .in10(Input_10), .in11(Input_11),
    .in12(Input_12), .in13(Input_13), .in14(Input_14), .in15(Input_15), .out(READ),
    .sel(mips_extended_io_1_io_addr));
  Binary_to_BCD binary_to_bcd_1 (
    .Binary(WRITE), .WRITE(E13), .Signed(1'b1), .Ones(binary_to_bcd_1_ones), .Tens(binary_to_bcd_1_tens),
    .Hundreds(binary_to_bcd_1_hundreds), .Sign_Bit(Sign), .CLK(CLK), .CLR(RESET));
  MIPS_EXTENDED_IO mips_extended_io_1 (
    .RESET(RESET), .CLK(CLK), .OUTPUT(WRITE), .INPUT(READ), .Current_PC(mips_extended_io_1_current_pc),
    .IO_0(mips_extended_io_1_io_0), .IO_1(mips_extended_io_1_io_1), .IO_2(mips_extended_io_1_io_2),
    .IO_3(mips_extended_io_1_io_3), .IO_4(E4), .IO_5(mips_extended_io_1_io_5), .IO_13(E13),
    .IO_14(mips_extended_io_1_io_14), .IO_15(mips_extended_io_1_io_15), .IO_ADDR(mips_extended_io_1_io_addr));  // open: IO_6, IO_7, IO_8, IO_9, IO_10, IO_11, IO_12
  Bit_Extender #(.out_width(7)) bit_extender_1 (.in(WRITE), .out(bit_extender_1_out));
  TTY tty_1 (.data(bit_extender_1_out), .clk(CLK), .we(mips_extended_io_1_io_5), .clr(or_1_out));
  BCD_to_7_Segment_Display bcd_to_7_segment_display_1 (
    .BCD(binary_to_bcd_1_ones), .LD(E), .M(A), .RU(D), .LU(B), .UU(C), .DD(F), .RD(G));
  BCD_to_7_Segment_Display bcd_to_7_segment_display_2 (
    .BCD(binary_to_bcd_1_tens), .LD(L), .M(H), .RU(K), .LU(I), .UU(J), .DD(M), .RD(N));
  BCD_to_7_Segment_Display bcd_to_7_segment_display_3 (
    .BCD(binary_to_bcd_1_hundreds), .LD(S), .M(O), .RU(R), .LU(P), .UU(Q), .DD(T), .RD(U));
  buf or_1 (or_1_out, RESET);  // OR_Gate
  _16_x_32_Display_Adapter u_16_x_32_display_adapter_1 (
    .CLR(RESET), .UPDATE(mips_extended_io_1_io_2), .FLUSH_BUFFER(mips_extended_io_1_io_3), .X(WRITE),
    .Y(WRITE), .out_9(n16_x_32_display_adapter_1_out_9), .out_10(n16_x_32_display_adapter_1_out_10),
    .out_11(n16_x_32_display_adapter_1_out_11), .out_12(n16_x_32_display_adapter_1_out_12),
    .out_13(n16_x_32_display_adapter_1_out_13), .out_14(n16_x_32_display_adapter_1_out_14),
    .out_15(n16_x_32_display_adapter_1_out_15), .out_16(n16_x_32_display_adapter_1_out_16),
    .out_17(n16_x_32_display_adapter_1_out_17), .out_18(n16_x_32_display_adapter_1_out_18),
    .out_19(n16_x_32_display_adapter_1_out_19), .out_20(n16_x_32_display_adapter_1_out_20),
    .out_21(n16_x_32_display_adapter_1_out_21), .out_22(n16_x_32_display_adapter_1_out_22),
    .out_23(n16_x_32_display_adapter_1_out_23), .out_24(n16_x_32_display_adapter_1_out_24),
    .out_25(n16_x_32_display_adapter_1_out_25), .out_26(n16_x_32_display_adapter_1_out_26),
    .out_27(n16_x_32_display_adapter_1_out_27), .out_28(n16_x_32_display_adapter_1_out_28),
    .out_29(n16_x_32_display_adapter_1_out_29), .out_30(n16_x_32_display_adapter_1_out_30),
    .out_31(n16_x_32_display_adapter_1_out_31), .out_32(n16_x_32_display_adapter_1_out_32),
    .out_33(n16_x_32_display_adapter_1_out_33), .out_34(n16_x_32_display_adapter_1_out_34),
    .out_35(n16_x_32_display_adapter_1_out_35), .out_36(n16_x_32_display_adapter_1_out_36),
    .out_37(n16_x_32_display_adapter_1_out_37), .out_38(n16_x_32_display_adapter_1_out_38),
    .out_39(n16_x_32_display_adapter_1_out_39), .out_40(n16_x_32_display_adapter_1_out_40),
    .X_Enable(mips_extended_io_1_io_0), .Y_Enable(mips_extended_io_1_io_1), .CLK(CLK));
  Random_Number_Generator random_number_generator_1 (.CLK(CLK), .Enable(mips_extended_io_1_io_15), .Random(Input_15));
  DotMatrix #(.matrixcols(32), .matrixrows(16)) dotmatrix_1 (
    .col0(n16_x_32_display_adapter_1_out_9), .col1(n16_x_32_display_adapter_1_out_10),
    .col2(n16_x_32_display_adapter_1_out_11), .col3(n16_x_32_display_adapter_1_out_12),
    .col4(n16_x_32_display_adapter_1_out_13), .col5(n16_x_32_display_adapter_1_out_14),
    .col6(n16_x_32_display_adapter_1_out_15), .col7(n16_x_32_display_adapter_1_out_16),
    .col8(n16_x_32_display_adapter_1_out_17), .col9(n16_x_32_display_adapter_1_out_18),
    .col10(n16_x_32_display_adapter_1_out_19), .col11(n16_x_32_display_adapter_1_out_20),
    .col12(n16_x_32_display_adapter_1_out_21), .col13(n16_x_32_display_adapter_1_out_22),
    .col14(n16_x_32_display_adapter_1_out_23), .col15(n16_x_32_display_adapter_1_out_24),
    .col16(n16_x_32_display_adapter_1_out_25), .col17(n16_x_32_display_adapter_1_out_26),
    .col18(n16_x_32_display_adapter_1_out_27), .col19(n16_x_32_display_adapter_1_out_28),
    .col20(n16_x_32_display_adapter_1_out_29), .col21(n16_x_32_display_adapter_1_out_30),
    .col22(n16_x_32_display_adapter_1_out_31), .col23(n16_x_32_display_adapter_1_out_32),
    .col24(n16_x_32_display_adapter_1_out_33), .col25(n16_x_32_display_adapter_1_out_34),
    .col26(n16_x_32_display_adapter_1_out_35), .col27(n16_x_32_display_adapter_1_out_36),
    .col28(n16_x_32_display_adapter_1_out_37), .col29(n16_x_32_display_adapter_1_out_38),
    .col30(n16_x_32_display_adapter_1_out_39), .col31(n16_x_32_display_adapter_1_out_40));
  Register register_1 (.D(WRITE), .en(mips_extended_io_1_io_14), .Q(register_1_q), .clk(CLK), .clr(RESET));
  Register register_2 (.D(register_1_q), .en(mips_extended_io_1_io_14), .Q(register_2_q), .clk(CLK), .clr(RESET));
  Keyboard #(.buflen(5)) keyboard_1 (.clk(CLK), .re(E4), .clr(RESET), .data(keyboard_1_data));  // open: avail
  // Probe on register_1_q
  // Probe on register_2_q
  _7_Segment_Display u_7_segment_display_1 (.g(Sign), .dp(1'b0));  // open: f, a, b, e, d, c
  _7_Segment_Display u_7_segment_display_2 (.g(O), .f(P), .a(Q), .b(R), .e(S), .d(T), .c(U), .dp(1'b0));
  // Probe on register_1_q
  // Probe on register_1_q
  // Probe on register_2_q
  // Probe on register_2_q
  _7_Segment_Display u_7_segment_display_3 (.g(H), .f(I), .a(J), .b(K), .e(L), .d(M), .c(N), .dp(1'b0));
  _7_Segment_Display u_7_segment_display_4 (.g(A), .f(B), .a(C), .b(D), .e(E), .d(F), .c(G), .dp(1'b0));
  assign Input_04 = {{1{1'b0}}, keyboard_1_data};  // Bit_Extender bit_extender_2

  // Other names for the same wires on the sheet: CLR = RESET

  // Notes on the sheet:
  //   ONES
  //   HUNDREDS
  //   TENS
  //   SCORE:
  //   KEYBOARD
  //   DEBUG VALUES
  //   Latest
  //   History
endmodule

module MIPS_EXTENDED_IO (
  input  RESET,
  input  [7:0] INPUT,
  output CLK,
  output [7:0] Current_PC,
  output [7:0] OUTPUT,
  output IO_0,
  output IO_1,
  output IO_2,
  output IO_3,
  output IO_4,
  output IO_5,
  output IO_6,
  output IO_7,
  output IO_8,
  output IO_9,
  output IO_10,
  output IO_11,
  output IO_12,
  output IO_13,
  output IO_14,
  output IO_15,
  output [3:0] IO_ADDR
);

  wire ALU_SRC, and_1_out, BRANCH, control_1_beq, control_1_bneq, IO, JUMP, MEM_READ, MEM_TO_REG, MEM_WRITE,
       or_1_out, REG_DEST, REG_WRITE, ZERO;
  wire [2:0] ALU_OP;
  wire [3:0] instruction_1_dest, instruction_1_src_1, instruction_1_src_2, multiplexer_1_out, OP_CODE;
  wire [7:0] adder_1_out, adder_2_out, alu_8_by_art_1_p5, demultiplexer_1_out0, demultiplexer_1_out1,
       extended_registers_1_readdata1, extended_registers_1_readdata2, IMM, JUMP_ADDR, memory_1_data_read,
       multiplexer_3_out, multiplexer_4_out, multiplexer_7_out, multiplexer_8_out, UPDATED_PC;

  // Probe on Current_PC
  Clock u_CLK (.out(CLK));
  // Probe on OP_CODE
  Instruction instruction_1 (
    .PC_Write(UPDATED_PC), .CLK(CLK), .RESET(RESET), .PC_Read(Current_PC), .Opcode(OP_CODE),
    .Src_1(instruction_1_src_1), .Src_2(instruction_1_src_2), .Dest(instruction_1_dest), .Addr___Immd(IMM),
    .Jump_Addr(JUMP_ADDR));
  Control control_1 (
    .OP_Code(OP_CODE), .RegDst(REG_DEST), .ALUSrc(ALU_SRC), .MemToReg(MEM_TO_REG), .RegWrite(REG_WRITE),
    .MemRead(MEM_READ), .MemWrite(MEM_WRITE), .beq(control_1_beq), .bneq(control_1_bneq), .Jump(JUMP),
    .ALUOp(ALU_OP));
  Adder adder_1 (.a(Current_PC), .b(8'h1), .out(adder_1_out), .cin(1'b0));  // open: cout
  Multiplexer #(.width(4), .enable("false")) multiplexer_1 (
    .in0(instruction_1_src_2), .in1(instruction_1_dest), .out(multiplexer_1_out), .sel(REG_DEST));
  Multiplexer #(.enable("false")) multiplexer_2 (.in0(control_1_bneq), .in1(control_1_beq), .out(BRANCH), .sel(ZERO));
  Adder adder_2 (.a(adder_1_out), .b(IMM), .out(adder_2_out), .cin(1'b0));  // open: cout
  Multiplexer #(.width(8), .enable("false")) multiplexer_3 (
    .in0(adder_1_out), .in1(adder_2_out), .out(multiplexer_3_out), .sel(BRANCH));
  Extended_Registers extended_registers_1 (
    .RegWrite(REG_WRITE), .Dest_1(multiplexer_1_out), .Src_1(instruction_1_src_1),
    .Src_2(instruction_1_src_2), .WriteData(multiplexer_8_out), .CLK(CLK), .CLR(RESET),
    .ReadData1(extended_registers_1_readdata1), .ReadData2(extended_registers_1_readdata2));
  Multiplexer #(.width(8), .enable("false")) multiplexer_4 (
    .in0(extended_registers_1_readdata2), .in1(IMM), .out(multiplexer_4_out), .sel(ALU_SRC));
  Multiplexer #(.width(8), .enable("false")) multiplexer_5 (
    .in0(multiplexer_3_out), .in1(JUMP_ADDR), .out(UPDATED_PC), .sel(JUMP));
  // ALU_8_by_ART alu_8_by_art_1: pin names not known; wires that end beside it: extended_registers_1_readdata1, multiplexer_4_out, ALU_OP, ZERO, alu_8_by_art_1_p5
  Address_Decoder address_decoder_1 (
    .Address(alu_8_by_art_1_p5), .Output_Peripheral_Address(IO_ADDR), .Output_Peripheral(IO));  // open: Data_And_Stack
  Demultiplexer #(.width(8), .enable("false")) demultiplexer_1 (
    .out0(demultiplexer_1_out0), .out1(demultiplexer_1_out1), .in(extended_registers_1_readdata2), .sel(IO));
  Multiplexer #(.width(8), .enable("false")) multiplexer_6 (
    .in0({8{1'b0}}), .in1(demultiplexer_1_out1), .out(OUTPUT), .sel(MEM_WRITE));
  or or_1 (or_1_out, MEM_READ, MEM_WRITE);
  Memory memory_1 (
    .Address(alu_8_by_art_1_p5), .WriteData(demultiplexer_1_out0), .CLK(CLK), .CLR(RESET),
    .Data_Read(memory_1_data_read), .MemRead(MEM_READ), .MemWrite(MEM_WRITE));
  Demultiplexer #(.select(4), .enable("false")) demultiplexer_2 (
    .out0(IO_0), .out1(IO_1), .out2(IO_2), .out3(IO_3), .out4(IO_4), .out5(IO_5), .out6(IO_6), .out7(IO_7),
    .out8(IO_8), .out9(IO_9), .out10(IO_10), .out11(IO_11), .out12(IO_12), .out13(IO_13), .out14(IO_14),
    .out15(IO_15), .in(and_1_out), .sel(IO_ADDR));
  and and_1 (and_1_out, IO, or_1_out);
  Multiplexer #(.width(8), .enable("false")) multiplexer_7 (
    .in0(memory_1_data_read), .in1(INPUT), .out(multiplexer_7_out), .sel(IO));
  Multiplexer #(.width(8), .enable("false")) multiplexer_8 (
    .in0(alu_8_by_art_1_p5), .in1(multiplexer_7_out), .out(multiplexer_8_out), .sel(MEM_TO_REG));
endmodule

module Instruction (
  input  [7:0] PC_Write,
  input  CLK,
  input  RESET,
  output [7:0] PC_Read,
  output [3:0] Opcode,
  output [3:0] Src_1,
  output [3:0] Src_2,
  output [3:0] Dest,
  output [7:0] Addr___Immd,
  output [7:0] Jump_Addr
);

  Register register_1 (.D(PC_Write), .en(1'b1), .Q(PC_Read), .clk(CLK), .clr(RESET));
  ROM #(.dataWidth(20)) rom_1 (.addr(PC_Read), .data({Opcode, Jump_Addr, Addr___Immd}), .sel(1'b1));

  assign Dest = Addr___Immd[7:4];
  assign Src_1 = Jump_Addr[7:4];
  assign Src_2 = Jump_Addr[3:0];

  // Notes on the sheet:
  //   contents of rom_1 (hex, n*v repeats v):
  //   a0fa0 a069f f7400 f4d00 f0500 8fd00 8fe01 8f002 a5100 f6b00 8f003 a0300 df304 23307 d4100 d4201
  //   a0703 a0804 7732a 7832d 79330 7a333 77b26 78b29 79b2c 7ab2f a4402 344c0 2111f 2220f 84100 84201
  //   a5300 f2600 7d10e a5502 355c0 f0500 d3700 d3801 77104 a3302 333c0 543fa f2200 78201 f2900 fd700
  //   f4d00 5e2f1 acc01 8fc0d dfd0f dfe0f 2dd1f 2ee0f 9c31a 23380 503ea fec00 f4d00 79b07 a22ff c07b0
  //   f1a00 7ab07 a1101 c08b0 f1a00 77bf7 a2201 c09b0 f1a00 78bf7 a11ff c0ab0 f1a00 dfd0f dfe0f 2dd1f
  //   2ee0f a0b04 a0c00 8fc0d a05c0 a5406 a0107 a0207 85100 85201 a0108 a0207 85102 85203 a0109 a0207
  //   85104 85205 a010a a0207 85106 85207 a0703 a0804 a0907 a0a01 f0400 d1200 d1301 8f200 8f301 8f002
  //   74199 a1102 311c0 f6b00 a0153 8f105 a016e 8f105 a0161 8f105 a016b 8f105 a0165 8f105 a0120 8f105
  //   a0147 8f105 a0161 8f105 a016d 8f105 a0165 8f105 a012e 8f105 a010a 8f105 a0155 8f105 a0173 8f105
  //   a0165 8f105 a0120 8f105 a0127 8f105 a0150 8f105 a016f 8f105 a016b 8f105 a0165 8f105 a0120 8f105
  //   a0154 8f105 a016f 8f105 a016f 8f105 a016c 8f105 a0127 8f105 a0120 8f105 a016f 8f105 a016e 8f105
  //   a0120 8f105 a016b 8f105 a0165 8f105 a0179 8f105 a0162 8f105 a016f 8f105 a0161 8f105 a0172 8f105
  //   a0164 8f105 a0120 8f105 a0174 8f105 a016f 8f105 a010a 8f105 a0170 8f105 a016c 8f105 a0161 8f105
  //   a0179 8f105 a012e 8f105 a010a 8f105 f0300 a0159 8f105 a016f 8f105 a0175 8f105 a0120 8f105 a014c
  //   8f105 a016f 8f105 a0173 8f105 a0174 8f105 a012e 8f105 a010a 8f105 f3000 a0159 8f105 a016f 8f105
  //   a0175 8f105 a0120 8f105 a0157 8f105 a016f 8f105 a016e 8f105 a012e 8f105 a010a 8f105 f3c00
  //   Shift Amt
endmodule

module Control (
  input  [3:0] OP_Code,
  output RegDst,
  output ALUSrc,
  output MemToReg,
  output RegWrite,
  output MemRead,
  output MemWrite,
  output beq,
  output bneq,
  output Jump,
  output [2:0] ALUOp
);

  ROM #(.addrWidth(4), .dataWidth(12)) rom_1 (
    .addr(OP_Code), .data({RegDst, ALUSrc, MemToReg, RegWrite, MemRead, MemWrite, beq, bneq, Jump, ALUOp}),
    .sel(1'b1));

  // Notes on the sheet:
  //   contents of rom_1 (hex, n*v repeats v):
  //   901 506 503 502 904 11 903 21 c40 501 500 505 900 780 902 8
endmodule

module Registers (
  input  RegWrite,
  input  [3:0] Src_1,
  input  [3:0] Src_2,
  input  [3:0] Dest_1,
  input  [7:0] WriteData,
  input  CLK,
  input  CLR,
  output [23:0] t4__t3__t2,
  output [23:0] t1__t0__sp,
  output [7:0] ReadData1,
  output [7:0] ReadData2
);

  wire demultiplexer_1_out1, demultiplexer_1_out2, demultiplexer_1_out3, demultiplexer_1_out4,
       demultiplexer_1_out5, demultiplexer_1_out6;
  wire [2:0] bit_extender_1_out, bit_extender_2_out, bit_extender_3_out;

  Register t1 (.D(WriteData), .en(demultiplexer_1_out1), .Q(t1__t0__sp[23:16]), .clk(CLK), .clr(CLR));
  Bit_Extender #(.in_width(4), .out_width(3)) bit_extender_1 (.in(Src_1), .out(bit_extender_1_out));
  Bit_Extender #(.in_width(4), .out_width(3)) bit_extender_2 (.in(Dest_1), .out(bit_extender_2_out));
  Register t2 (.D(WriteData), .en(demultiplexer_1_out2), .Q(t4__t3__t2[7:0]), .clk(CLK), .clr(CLR));
  Multiplexer #(.select(3), .width(8), .enable("false")) multiplexer_1 (
    .in0({8{1'b0}}), .in1(t1__t0__sp[23:16]), .in2(t4__t3__t2[7:0]), .in3(t4__t3__t2[15:8]),
    .in4(t4__t3__t2[23:16]), .in5(t1__t0__sp[15:8]), .in6(t1__t0__sp[7:0]), .out(ReadData1),
    .sel(bit_extender_1_out));  // open: in7
  Demultiplexer #(.select(3), .enable("false")) demultiplexer_1 (
    .out1(demultiplexer_1_out1), .out2(demultiplexer_1_out2), .out3(demultiplexer_1_out3),
    .out4(demultiplexer_1_out4), .out5(demultiplexer_1_out5), .out6(demultiplexer_1_out6), .in(RegWrite),
    .sel(bit_extender_2_out));  // open: out0, out7
  Register t3 (.D(WriteData), .en(demultiplexer_1_out3), .Q(t4__t3__t2[15:8]), .clk(CLK), .clr(CLR));
  Register t4 (.D(WriteData), .en(demultiplexer_1_out4), .Q(t4__t3__t2[23:16]), .clk(CLK), .clr(CLR));
  Bit_Extender #(.in_width(4), .out_width(3)) bit_extender_3 (.in(Src_2), .out(bit_extender_3_out));
  Register t0 (.D(WriteData), .en(demultiplexer_1_out5), .Q(t1__t0__sp[15:8]), .clk(CLK), .clr(CLR));
  Multiplexer #(.select(3), .width(8), .enable("false")) multiplexer_2 (
    .in0({8{1'b0}}), .in1(t1__t0__sp[23:16]), .in2(t4__t3__t2[7:0]), .in3(t4__t3__t2[15:8]),
    .in4(t4__t3__t2[23:16]), .in5(t1__t0__sp[15:8]), .in6(t1__t0__sp[7:0]), .out(ReadData2),
    .sel(bit_extender_3_out));  // open: in7
  Register sp (.D(WriteData), .en(demultiplexer_1_out6), .Q(t1__t0__sp[7:0]), .clk(CLK), .clr(CLR));

  // Other names for the same wires on the sheet: S1[3:0] = Src_1; S2[3:0] = Src_2; WD[7:0] = WriteData
endmodule

module Extended_Registers (
  input  RegWrite,
  input  [3:0] Dest_1,
  input  [3:0] Src_1,
  input  [3:0] Src_2,
  input  [7:0] WriteData,
  input  CLK,
  input  CLR,
  output [7:0] ReadData1,
  output [7:0] ReadData2
);

  wire demultiplexer_1_out1, demultiplexer_1_out2, demultiplexer_1_out3, demultiplexer_1_out4,
       demultiplexer_1_out5, demultiplexer_1_out6, demultiplexer_1_out7, demultiplexer_1_out8,
       demultiplexer_1_out9, demultiplexer_1_out10, demultiplexer_1_out11, demultiplexer_1_out12,
       demultiplexer_1_out13, demultiplexer_1_out14, demultiplexer_1_out15;
  wire [7:0] io_q, s0_q, s1_q, s2_q, s3_q, sp_q, t0_q, t1_q, t2_q, t3_q, t4_q, v0_q, v1_q, v2_q, v3_q;

  Demultiplexer #(.select(4), .enable("false")) demultiplexer_1 (
    .out1(demultiplexer_1_out1), .out2(demultiplexer_1_out2), .out3(demultiplexer_1_out3),
    .out4(demultiplexer_1_out4), .out5(demultiplexer_1_out5), .out6(demultiplexer_1_out6),
    .out7(demultiplexer_1_out7), .out8(demultiplexer_1_out8), .out9(demultiplexer_1_out9),
    .out10(demultiplexer_1_out10), .out11(demultiplexer_1_out11), .out12(demultiplexer_1_out12),
    .out13(demultiplexer_1_out13), .out14(demultiplexer_1_out14), .out15(demultiplexer_1_out15),
    .in(RegWrite), .sel(Dest_1));  // open: out0
  Register t0 (.D(WriteData), .en(demultiplexer_1_out1), .Q(t0_q), .clk(CLK), .clr(CLR));
  Register t1 (.D(WriteData), .en(demultiplexer_1_out2), .Q(t1_q), .clk(CLK), .clr(CLR));
  Register t2 (.D(WriteData), .en(demultiplexer_1_out3), .Q(t2_q), .clk(CLK), .clr(CLR));
  Register t3 (.D(WriteData), .en(demultiplexer_1_out4), .Q(t3_q), .clk(CLK), .clr(CLR));
  Register t4 (.D(WriteData), .en(demultiplexer_1_out5), .Q(t4_q), .clk(CLK), .clr(CLR));
  Register sp (.D(WriteData), .en(demultiplexer_1_out6), .Q(sp_q), .clk(CLK), .clr(CLR));
  Register v0 (.D(WriteData), .en(demultiplexer_1_out7), .Q(v0_q), .clk(CLK), .clr(CLR));
  Register v1 (.D(WriteData), .en(demultiplexer_1_out8), .Q(v1_q), .clk(CLK), .clr(CLR));
  Register v2 (.D(WriteData), .en(demultiplexer_1_out9), .Q(v2_q), .clk(CLK), .clr(CLR));
  Register v3 (.D(WriteData), .en(demultiplexer_1_out10), .Q(v3_q), .clk(CLK), .clr(CLR));
  Register s0 (.D(WriteData), .en(demultiplexer_1_out11), .Q(s0_q), .clk(CLK), .clr(CLR));
  Register s1 (.D(WriteData), .en(demultiplexer_1_out12), .Q(s1_q), .clk(CLK), .clr(CLR));
  Register s2 (.D(WriteData), .en(demultiplexer_1_out13), .Q(s2_q), .clk(CLK), .clr(CLR));
  Register s3 (.D(WriteData), .en(demultiplexer_1_out14), .Q(s3_q), .clk(CLK), .clr(CLR));
  Register io (.D(WriteData), .en(demultiplexer_1_out15), .Q(io_q), .clk(CLK), .clr(CLR));
  Multiplexer #(.select(4), .width(8), .enable("false")) multiplexer_1 (
    .in0({8{1'b0}}), .in1(t0_q), .in2(t1_q), .in3(t2_q), .in4(t3_q), .in5(t4_q), .in6(sp_q), .in7(v0_q),
    .in8(v1_q), .in9(v2_q), .in10(v3_q), .in11(s0_q), .in12(s1_q), .in13(s2_q), .in14(s3_q), .in15(io_q),
    .out(ReadData1), .sel(Src_1));
  Multiplexer #(.select(4), .width(8), .enable("false")) multiplexer_2 (
    .in0({8{1'b0}}), .in1(t0_q), .in2(t1_q), .in3(t2_q), .in4(t3_q), .in5(t4_q), .in6(sp_q), .in7(v0_q),
    .in8(v1_q), .in9(v2_q), .in10(v3_q), .in11(s0_q), .in12(s1_q), .in13(s2_q), .in14(s3_q), .in15(io_q),
    .out(ReadData2), .sel(Src_2));

  // Other names for the same wires on the sheet: D1[3:0] = Dest_1; READ_DATA_1[7:0] = ReadData1;
  //   READ_DATA_2[7:0] = ReadData2; S1[3:0] = Src_1; S2[3:0] = Src_2; WD[7:0] = WriteData
endmodule

module Memory (
  input  [7:0] Address,
  input  [7:0] WriteData,
  input  CLK,
  input  CLR,
  input  MemWrite,
  input  MemRead,
  output [7:0] Data_Read
);

  RAM #(.bus("separate")) ram_1 (
    .addr(Address), .din(WriteData), .data(Data_Read), .str(MemWrite), .sel(1'b1), .clk(CLK), .ld(MemRead),
    .clr(CLR));
endmodule

module Address_Decoder (
  input  [7:0] Address,
  output Data_And_Stack,
  output [3:0] Output_Peripheral_Address,
  output Output_Peripheral
);

  wire not_1_out, not_2_out;

  not not_1 (not_1_out, Address[4]);
  not not_2 (not_2_out, Address[6]);
  and and_1 (Output_Peripheral, not_1_out, Address[5], not_2_out, Address[7]);
  Multiplexer #(.width(4), .enable("false")) multiplexer_1 (
    .in0(4'b0000), .in1(Address[3:0]), .out(Output_Peripheral_Address), .sel(Output_Peripheral));
  not not_3 (Data_And_Stack, Output_Peripheral);

  // Notes on the sheet:
  //   1010 XXXX
  //   This format of 16 addresses are reserved for I/O
  //   1010 XXXX
  //   Last 4 bits (XXXX) is I/O address
endmodule

module _16_x_32_Display_Adapter (
  input  CLK,
  input  CLR,
  input  UPDATE,
  input  FLUSH_BUFFER,
  input  [7:0] X,
  input  X_Enable,
  input  [7:0] Y,
  input  Y_Enable,
  output [15:0] out_9,
  output [15:0] out_10,
  output [15:0] out_11,
  output [15:0] out_12,
  output [15:0] out_13,
  output [15:0] out_14,
  output [15:0] out_15,
  output [15:0] out_16,
  output [15:0] out_17,
  output [15:0] out_18,
  output [15:0] out_19,
  output [15:0] out_20,
  output [15:0] out_21,
  output [15:0] out_22,
  output [15:0] out_23,
  output [15:0] out_24,
  output [15:0] out_25,
  output [15:0] out_26,
  output [15:0] out_27,
  output [15:0] out_28,
  output [15:0] out_29,
  output [15:0] out_30,
  output [15:0] out_31,
  output [15:0] out_32,
  output [15:0] out_33,
  output [15:0] out_34,
  output [15:0] out_35,
  output [15:0] out_36,
  output [15:0] out_37,
  output [15:0] out_38,
  output [15:0] out_39,
  output [15:0] out_40
);

  wire or_1_out, register_3_q, register_4_q;
  wire [3:0] bit_extender_2_out;
  wire [4:0] bit_extender_1_out;
  wire [7:0] register_1_q, register_2_q;
  wire [15:0] n32_x_16b_sticky_reg_1_r0, n32_x_16b_sticky_reg_1_r0_2, n32_x_16b_sticky_reg_1_r1,
       n32_x_16b_sticky_reg_1_r1_2, n32_x_16b_sticky_reg_1_r2, n32_x_16b_sticky_reg_1_r2_2,
       n32_x_16b_sticky_reg_1_r3, n32_x_16b_sticky_reg_1_r3_2, n32_x_16b_sticky_reg_1_r4,
       n32_x_16b_sticky_reg_1_r4_2, n32_x_16b_sticky_reg_1_r5, n32_x_16b_sticky_reg_1_r5_2,
       n32_x_16b_sticky_reg_1_r6, n32_x_16b_sticky_reg_1_r6_2, n32_x_16b_sticky_reg_1_r7,
       n32_x_16b_sticky_reg_1_r7_2, n32_x_16b_sticky_reg_1_r8, n32_x_16b_sticky_reg_1_r8_2,
       n32_x_16b_sticky_reg_1_r9, n32_x_16b_sticky_reg_1_r9_2, n32_x_16b_sticky_reg_1_r10,
       n32_x_16b_sticky_reg_1_r10_2, n32_x_16b_sticky_reg_1_r11, n32_x_16b_sticky_reg_1_r11_2,
       n32_x_16b_sticky_reg_1_r12, n32_x_16b_sticky_reg_1_r12_2, n32_x_16b_sticky_reg_1_r13,
       n32_x_16b_sticky_reg_1_r13_2, n32_x_16b_sticky_reg_1_r14, n32_x_16b_sticky_reg_1_r14_2,
       n32_x_16b_sticky_reg_1_r15, n32_x_16b_sticky_reg_1_r15_2, shifter_1_out, undriven, undriven_2,
       undriven_3, undriven_4, undriven_5, undriven_6, undriven_7, undriven_8, undriven_9, undriven_10,
       undriven_11, undriven_12, undriven_13, undriven_14, undriven_15, undriven_16, undriven_17,
       undriven_18, undriven_19, undriven_20, undriven_21, undriven_22, undriven_23, undriven_24,
       undriven_25, undriven_26, undriven_27, undriven_28, undriven_29, undriven_30, undriven_31, undriven_32;

  Register register_1 (.D(X), .en(X_Enable), .Q(register_1_q), .clk(CLK));  // open: clr
  Register register_2 (.D(Y), .en(Y_Enable), .Q(register_2_q), .clk(CLK));  // open: clr
  Bit_Extender #(.out_width(5)) bit_extender_1 (.in(register_1_q), .out(bit_extender_1_out));
  Bit_Extender #(.out_width(4)) bit_extender_2 (.in(register_2_q), .out(bit_extender_2_out));
  Shifter #(.width(16)) shifter_1 (.in(16'h1), .\dist (bit_extender_2_out), .out(shifter_1_out));
  // Probe on shifter_1_out
  or or_1 (or_1_out, CLR, register_4_q);
  Register #(.width(1), .trigger("falling")) register_3 (
    .D(FLUSH_BUFFER), .en(1'b1), .Q(register_3_q), .clk(CLK));  // open: clr
  Register #(.width(1), .trigger("falling")) register_4 (
    .D(register_3_q), .en(1'b1), .Q(register_4_q), .clk(CLK));  // open: clr
  _32_x_16b_STICKY_REG u_32_x_16b_sticky_reg_1 (
    .CLK(CLK), .CLR(or_1_out), .FLUSH(UPDATE), .ADDR(bit_extender_1_out), .WRITE_DATA(shifter_1_out),
    .R0(n32_x_16b_sticky_reg_1_r0), .R1(n32_x_16b_sticky_reg_1_r1), .R2(n32_x_16b_sticky_reg_1_r2),
    .R3(n32_x_16b_sticky_reg_1_r3), .R4(n32_x_16b_sticky_reg_1_r4), .R5(n32_x_16b_sticky_reg_1_r5),
    .R6(n32_x_16b_sticky_reg_1_r6), .R7(n32_x_16b_sticky_reg_1_r7), .R8(n32_x_16b_sticky_reg_1_r8),
    .R9(n32_x_16b_sticky_reg_1_r9), .R10(n32_x_16b_sticky_reg_1_r10), .R11(n32_x_16b_sticky_reg_1_r11),
    .R12(n32_x_16b_sticky_reg_1_r12), .R13(n32_x_16b_sticky_reg_1_r13), .R14(n32_x_16b_sticky_reg_1_r14),
    .R15(n32_x_16b_sticky_reg_1_r15), .R0_2(n32_x_16b_sticky_reg_1_r0_2), .R1_2(n32_x_16b_sticky_reg_1_r1_2),
    .R2_2(n32_x_16b_sticky_reg_1_r2_2), .R3_2(n32_x_16b_sticky_reg_1_r3_2),
    .R4_2(n32_x_16b_sticky_reg_1_r4_2), .R5_2(n32_x_16b_sticky_reg_1_r5_2),
    .R6_2(n32_x_16b_sticky_reg_1_r6_2), .R7_2(n32_x_16b_sticky_reg_1_r7_2),
    .R8_2(n32_x_16b_sticky_reg_1_r8_2), .R9_2(n32_x_16b_sticky_reg_1_r9_2),
    .R10_2(n32_x_16b_sticky_reg_1_r10_2), .R11_2(n32_x_16b_sticky_reg_1_r11_2),
    .R12_2(n32_x_16b_sticky_reg_1_r12_2), .R13_2(n32_x_16b_sticky_reg_1_r13_2),
    .R14_2(n32_x_16b_sticky_reg_1_r14_2), .R15_2(n32_x_16b_sticky_reg_1_r15_2));
  _32_x_16b_BUFFER u_32_x_16b_buffer_1 (
    .CLK(CLK), .CLR(CLR), .FLUSH(FLUSH_BUFFER), .R0(n32_x_16b_sticky_reg_1_r0),
    .R1(n32_x_16b_sticky_reg_1_r1), .R2(n32_x_16b_sticky_reg_1_r2), .R3(n32_x_16b_sticky_reg_1_r3),
    .R4(n32_x_16b_sticky_reg_1_r4), .R5(n32_x_16b_sticky_reg_1_r5), .R6(n32_x_16b_sticky_reg_1_r6),
    .R7(n32_x_16b_sticky_reg_1_r7), .R8(n32_x_16b_sticky_reg_1_r8), .R9(n32_x_16b_sticky_reg_1_r9),
    .R10(n32_x_16b_sticky_reg_1_r10), .R11(n32_x_16b_sticky_reg_1_r11), .R12(n32_x_16b_sticky_reg_1_r12),
    .R13(n32_x_16b_sticky_reg_1_r13), .R14(n32_x_16b_sticky_reg_1_r14), .R15(n32_x_16b_sticky_reg_1_r15),
    .R0_2(n32_x_16b_sticky_reg_1_r0_2), .R1_2(n32_x_16b_sticky_reg_1_r1_2),
    .R2_2(n32_x_16b_sticky_reg_1_r2_2), .R3_2(n32_x_16b_sticky_reg_1_r3_2),
    .R4_2(n32_x_16b_sticky_reg_1_r4_2), .R5_2(n32_x_16b_sticky_reg_1_r5_2),
    .R6_2(n32_x_16b_sticky_reg_1_r6_2), .R7_2(n32_x_16b_sticky_reg_1_r7_2),
    .R8_2(n32_x_16b_sticky_reg_1_r8_2), .R9_2(n32_x_16b_sticky_reg_1_r9_2),
    .R10_2(n32_x_16b_sticky_reg_1_r10_2), .R11_2(n32_x_16b_sticky_reg_1_r11_2),
    .R12_2(n32_x_16b_sticky_reg_1_r12_2), .R13_2(n32_x_16b_sticky_reg_1_r13_2),
    .R14_2(n32_x_16b_sticky_reg_1_r14_2), .R15_2(n32_x_16b_sticky_reg_1_r15_2), .R0_3(out_9), .R1_3(out_10),
    .R2_3(out_11), .R3_3(out_12), .R4_3(out_13), .R5_3(out_14), .R6_3(out_15), .R7_3(out_16), .R8_3(out_17),
    .R9_3(out_18), .R10_3(out_19), .R11_3(out_20), .R12_3(out_21), .R13_3(out_22), .R14_3(out_23),
    .R15_3(out_24), .R0_4(out_25), .R1_4(out_26), .R2_4(out_27), .R3_4(out_28), .R4_4(out_29), .R5_4(out_30),
    .R6_4(out_31), .R7_4(out_32), .R8_4(out_33), .R9_4(out_34), .R10_4(out_35), .R11_4(out_36),
    .R12_4(out_37), .R13_4(out_38), .R14_4(out_39), .R15_4(out_40));
  DotMatrix #(.matrixcols(32), .matrixrows(16)) dotmatrix_1 (
    .col0(undriven_16), .col1(undriven), .col2(undriven_2), .col3(undriven_3), .col4(undriven_17),
    .col5(undriven_18), .col6(undriven_4), .col7(undriven_19), .col8(undriven_5), .col9(undriven_20),
    .col10(undriven_21), .col11(undriven_6), .col12(undriven_22), .col13(undriven_7), .col14(undriven_8),
    .col15(undriven_23), .col16(undriven_24), .col17(undriven_25), .col18(undriven_9), .col19(undriven_10),
    .col20(undriven_26), .col21(undriven_27), .col22(undriven_28), .col23(undriven_11), .col24(undriven_12),
    .col25(undriven_29), .col26(undriven_13), .col27(undriven_30), .col28(undriven_14), .col29(undriven_31),
    .col30(undriven_32), .col31(undriven_15));

  // Notes on the sheet:
  //   After flushing the screen values to display clear the sticky register.
  //   Give a one full clock delay before clearing the registers to give time to read them.
  //   MSB
  //   LSB
endmodule

module _32_x_8b_REGISTER (
  input  CLK,
  input  CLR,
  input  FLUSH,
  input  [4:0] ADDR,
  input  [7:0] WRITE_DATA,
  output [7:0] R0,
  output [7:0] R1,
  output [7:0] R2,
  output [7:0] R3,
  output [7:0] R4,
  output [7:0] R5,
  output [7:0] R6,
  output [7:0] R7,
  output [7:0] R8,
  output [7:0] R9,
  output [7:0] R10,
  output [7:0] R11,
  output [7:0] R12,
  output [7:0] R13,
  output [7:0] R14,
  output [7:0] R15,
  output [7:0] R0_2,
  output [7:0] R1_2,
  output [7:0] R2_2,
  output [7:0] R3_2,
  output [7:0] R4_2,
  output [7:0] R5_2,
  output [7:0] R6_2,
  output [7:0] R7_2,
  output [7:0] R8_2,
  output [7:0] R9_2,
  output [7:0] R10_2,
  output [7:0] R11_2,
  output [7:0] R12_2,
  output [7:0] R13_2,
  output [7:0] R14_2,
  output [7:0] R15_2
);

  wire demultiplexer_1_out0, demultiplexer_1_out1, demultiplexer_1_out2, demultiplexer_1_out3,
       demultiplexer_1_out4, demultiplexer_1_out5, demultiplexer_1_out6, demultiplexer_1_out7,
       demultiplexer_1_out8, demultiplexer_1_out9, demultiplexer_1_out10, demultiplexer_1_out11,
       demultiplexer_1_out12, demultiplexer_1_out13, demultiplexer_1_out14, demultiplexer_1_out15,
       demultiplexer_1_out16, demultiplexer_1_out17, demultiplexer_1_out18, demultiplexer_1_out19,
       demultiplexer_1_out20, demultiplexer_1_out21, demultiplexer_1_out22, demultiplexer_1_out23,
       demultiplexer_1_out24, demultiplexer_1_out25, demultiplexer_1_out26, demultiplexer_1_out27,
       demultiplexer_1_out28, demultiplexer_1_out29, demultiplexer_1_out30, demultiplexer_1_out31;

  Demultiplexer #(.select(5), .enable("false")) demultiplexer_1 (
    .out0(demultiplexer_1_out0), .out1(demultiplexer_1_out1), .out2(demultiplexer_1_out2),
    .out3(demultiplexer_1_out3), .out4(demultiplexer_1_out4), .out5(demultiplexer_1_out5),
    .out6(demultiplexer_1_out6), .out7(demultiplexer_1_out7), .out8(demultiplexer_1_out8),
    .out9(demultiplexer_1_out9), .out10(demultiplexer_1_out10), .out11(demultiplexer_1_out11),
    .out12(demultiplexer_1_out12), .out13(demultiplexer_1_out13), .out14(demultiplexer_1_out14),
    .out15(demultiplexer_1_out15), .out16(demultiplexer_1_out16), .out17(demultiplexer_1_out17),
    .out18(demultiplexer_1_out18), .out19(demultiplexer_1_out19), .out20(demultiplexer_1_out20),
    .out21(demultiplexer_1_out21), .out22(demultiplexer_1_out22), .out23(demultiplexer_1_out23),
    .out24(demultiplexer_1_out24), .out25(demultiplexer_1_out25), .out26(demultiplexer_1_out26),
    .out27(demultiplexer_1_out27), .out28(demultiplexer_1_out28), .out29(demultiplexer_1_out29),
    .out30(demultiplexer_1_out30), .out31(demultiplexer_1_out31), .in(FLUSH), .sel(ADDR));
  Register register_1 (.D(WRITE_DATA), .en(demultiplexer_1_out1), .Q(R1), .clk(CLK), .clr(CLR));
  Register register_2 (.D(WRITE_DATA), .en(demultiplexer_1_out3), .Q(R3), .clk(CLK), .clr(CLR));
  Register register_3 (.D(WRITE_DATA), .en(demultiplexer_1_out5), .Q(R5), .clk(CLK), .clr(CLR));
  Register register_4 (.D(WRITE_DATA), .en(demultiplexer_1_out7), .Q(R7), .clk(CLK), .clr(CLR));
  Register register_5 (.D(WRITE_DATA), .en(demultiplexer_1_out9), .Q(R9), .clk(CLK), .clr(CLR));
  Register register_6 (.D(WRITE_DATA), .en(demultiplexer_1_out11), .Q(R11), .clk(CLK), .clr(CLR));
  Register register_7 (.D(WRITE_DATA), .en(demultiplexer_1_out13), .Q(R13), .clk(CLK), .clr(CLR));
  Register register_8 (.D(WRITE_DATA), .en(demultiplexer_1_out15), .Q(R15), .clk(CLK), .clr(CLR));
  Register register_9 (.D(WRITE_DATA), .en(demultiplexer_1_out17), .Q(R1_2), .clk(CLK), .clr(CLR));
  Register register_10 (.D(WRITE_DATA), .en(demultiplexer_1_out19), .Q(R3_2), .clk(CLK), .clr(CLR));
  Register register_11 (.D(WRITE_DATA), .en(demultiplexer_1_out21), .Q(R5_2), .clk(CLK), .clr(CLR));
  Register register_12 (.D(WRITE_DATA), .en(demultiplexer_1_out23), .Q(R7_2), .clk(CLK), .clr(CLR));
  Register register_13 (.D(WRITE_DATA), .en(demultiplexer_1_out25), .Q(R9_2), .clk(CLK), .clr(CLR));
  Register register_14 (.D(WRITE_DATA), .en(demultiplexer_1_out27), .Q(R11_2), .clk(CLK), .clr(CLR));
  Register register_15 (.D(WRITE_DATA), .en(demultiplexer_1_out29), .Q(R13_2), .clk(CLK), .clr(CLR));
  Register register_16 (.D(WRITE_DATA), .en(demultiplexer_1_out31), .Q(R15_2), .clk(CLK), .clr(CLR));
  Register register_17 (.D(WRITE_DATA), .en(demultiplexer_1_out0), .Q(R0), .clk(CLK), .clr(CLR));
  Register register_18 (.D(WRITE_DATA), .en(demultiplexer_1_out2), .Q(R2), .clk(CLK), .clr(CLR));
  Register register_19 (.D(WRITE_DATA), .en(demultiplexer_1_out4), .Q(R4), .clk(CLK), .clr(CLR));
  Register register_20 (.D(WRITE_DATA), .en(demultiplexer_1_out6), .Q(R6), .clk(CLK), .clr(CLR));
  Register register_21 (.D(WRITE_DATA), .en(demultiplexer_1_out8), .Q(R8), .clk(CLK), .clr(CLR));
  Register register_22 (.D(WRITE_DATA), .en(demultiplexer_1_out10), .Q(R10), .clk(CLK), .clr(CLR));
  Register register_23 (.D(WRITE_DATA), .en(demultiplexer_1_out12), .Q(R12), .clk(CLK), .clr(CLR));
  Register register_24 (.D(WRITE_DATA), .en(demultiplexer_1_out14), .Q(R14), .clk(CLK), .clr(CLR));
  Register register_25 (.D(WRITE_DATA), .en(demultiplexer_1_out16), .Q(R0_2), .clk(CLK), .clr(CLR));
  Register register_26 (.D(WRITE_DATA), .en(demultiplexer_1_out18), .Q(R2_2), .clk(CLK), .clr(CLR));
  Register register_27 (.D(WRITE_DATA), .en(demultiplexer_1_out20), .Q(R4_2), .clk(CLK), .clr(CLR));
  Register register_28 (.D(WRITE_DATA), .en(demultiplexer_1_out22), .Q(R6_2), .clk(CLK), .clr(CLR));
  Register register_29 (.D(WRITE_DATA), .en(demultiplexer_1_out24), .Q(R8_2), .clk(CLK), .clr(CLR));
  Register register_30 (.D(WRITE_DATA), .en(demultiplexer_1_out26), .Q(R10_2), .clk(CLK), .clr(CLR));
  Register register_31 (.D(WRITE_DATA), .en(demultiplexer_1_out28), .Q(R12_2), .clk(CLK), .clr(CLR));
  Register register_32 (.D(WRITE_DATA), .en(demultiplexer_1_out30), .Q(R14_2), .clk(CLK), .clr(CLR));

  // Other names for the same wires on the sheet: WD[7:0] = WRITE_DATA; WRITE = FLUSH
endmodule

module _32_x_16b_STICKY_REG (
  input  CLK,
  input  CLR,
  input  FLUSH,
  input  [4:0] ADDR,
  input  [15:0] WRITE_DATA,
  output [15:0] R0,
  output [15:0] R1,
  output [15:0] R2,
  output [15:0] R3,
  output [15:0] R4,
  output [15:0] R5,
  output [15:0] R6,
  output [15:0] R7,
  output [15:0] R8,
  output [15:0] R9,
  output [15:0] R10,
  output [15:0] R11,
  output [15:0] R12,
  output [15:0] R13,
  output [15:0] R14,
  output [15:0] R15,
  output [15:0] R0_2,
  output [15:0] R1_2,
  output [15:0] R2_2,
  output [15:0] R3_2,
  output [15:0] R4_2,
  output [15:0] R5_2,
  output [15:0] R6_2,
  output [15:0] R7_2,
  output [15:0] R8_2,
  output [15:0] R9_2,
  output [15:0] R10_2,
  output [15:0] R11_2,
  output [15:0] R12_2,
  output [15:0] R13_2,
  output [15:0] R14_2,
  output [15:0] R15_2
);

  wire demultiplexer_1_out0, demultiplexer_1_out1, demultiplexer_1_out2, demultiplexer_1_out3,
       demultiplexer_1_out4, demultiplexer_1_out5, demultiplexer_1_out6, demultiplexer_1_out7,
       demultiplexer_1_out8, demultiplexer_1_out9, demultiplexer_1_out10, demultiplexer_1_out11,
       demultiplexer_1_out12, demultiplexer_1_out13, demultiplexer_1_out14, demultiplexer_1_out15,
       demultiplexer_1_out16, demultiplexer_1_out17, demultiplexer_1_out18, demultiplexer_1_out19,
       demultiplexer_1_out20, demultiplexer_1_out21, demultiplexer_1_out22, demultiplexer_1_out23,
       demultiplexer_1_out24, demultiplexer_1_out25, demultiplexer_1_out26, demultiplexer_1_out27,
       demultiplexer_1_out28, demultiplexer_1_out29, demultiplexer_1_out30, demultiplexer_1_out31;
  wire [15:0] or_1_out, or_2_out, or_3_out, or_4_out, or_5_out, or_6_out, or_7_out, or_8_out, or_9_out,
       or_10_out, or_11_out, or_12_out, or_13_out, or_14_out, or_15_out, or_16_out, or_17_out, or_18_out,
       or_19_out, or_20_out, or_21_out, or_22_out, or_23_out, or_24_out, or_25_out, or_26_out, or_27_out,
       or_28_out, or_29_out, or_30_out, or_31_out, or_32_out;

  Demultiplexer #(.select(5), .enable("false")) demultiplexer_1 (
    .out0(demultiplexer_1_out0), .out1(demultiplexer_1_out1), .out2(demultiplexer_1_out2),
    .out3(demultiplexer_1_out3), .out4(demultiplexer_1_out4), .out5(demultiplexer_1_out5),
    .out6(demultiplexer_1_out6), .out7(demultiplexer_1_out7), .out8(demultiplexer_1_out8),
    .out9(demultiplexer_1_out9), .out10(demultiplexer_1_out10), .out11(demultiplexer_1_out11),
    .out12(demultiplexer_1_out12), .out13(demultiplexer_1_out13), .out14(demultiplexer_1_out14),
    .out15(demultiplexer_1_out15), .out16(demultiplexer_1_out16), .out17(demultiplexer_1_out17),
    .out18(demultiplexer_1_out18), .out19(demultiplexer_1_out19), .out20(demultiplexer_1_out20),
    .out21(demultiplexer_1_out21), .out22(demultiplexer_1_out22), .out23(demultiplexer_1_out23),
    .out24(demultiplexer_1_out24), .out25(demultiplexer_1_out25), .out26(demultiplexer_1_out26),
    .out27(demultiplexer_1_out27), .out28(demultiplexer_1_out28), .out29(demultiplexer_1_out29),
    .out30(demultiplexer_1_out30), .out31(demultiplexer_1_out31), .in(FLUSH), .sel(ADDR));
  assign or_1_out = R1 | WRITE_DATA;  // OR_Gate or_1, 16 bits wide
  assign or_2_out = R3 | WRITE_DATA;  // OR_Gate or_2, 16 bits wide
  assign or_3_out = R5 | WRITE_DATA;  // OR_Gate or_3, 16 bits wide
  assign or_4_out = R7 | WRITE_DATA;  // OR_Gate or_4, 16 bits wide
  assign or_5_out = R9 | WRITE_DATA;  // OR_Gate or_5, 16 bits wide
  assign or_6_out = R11 | WRITE_DATA;  // OR_Gate or_6, 16 bits wide
  assign or_7_out = R13 | WRITE_DATA;  // OR_Gate or_7, 16 bits wide
  assign or_8_out = R15 | WRITE_DATA;  // OR_Gate or_8, 16 bits wide
  assign or_9_out = R1_2 | WRITE_DATA;  // OR_Gate or_9, 16 bits wide
  assign or_10_out = R3_2 | WRITE_DATA;  // OR_Gate or_10, 16 bits wide
  assign or_11_out = R5_2 | WRITE_DATA;  // OR_Gate or_11, 16 bits wide
  assign or_12_out = R7_2 | WRITE_DATA;  // OR_Gate or_12, 16 bits wide
  assign or_13_out = R9_2 | WRITE_DATA;  // OR_Gate or_13, 16 bits wide
  assign or_14_out = R11_2 | WRITE_DATA;  // OR_Gate or_14, 16 bits wide
  assign or_15_out = R13_2 | WRITE_DATA;  // OR_Gate or_15, 16 bits wide
  assign or_16_out = R15_2 | WRITE_DATA;  // OR_Gate or_16, 16 bits wide
  Register #(.width(16)) register_1 (.D(or_1_out), .en(demultiplexer_1_out1), .Q(R1), .clk(CLK), .clr(CLR));
  Register #(.width(16)) register_2 (.D(or_2_out), .en(demultiplexer_1_out3), .Q(R3), .clk(CLK), .clr(CLR));
  Register #(.width(16)) register_3 (.D(or_3_out), .en(demultiplexer_1_out5), .Q(R5), .clk(CLK), .clr(CLR));
  Register #(.width(16)) register_4 (.D(or_4_out), .en(demultiplexer_1_out7), .Q(R7), .clk(CLK), .clr(CLR));
  Register #(.width(16)) register_5 (.D(or_5_out), .en(demultiplexer_1_out9), .Q(R9), .clk(CLK), .clr(CLR));
  Register #(.width(16)) register_6 (.D(or_6_out), .en(demultiplexer_1_out11), .Q(R11), .clk(CLK), .clr(CLR));
  Register #(.width(16)) register_7 (.D(or_7_out), .en(demultiplexer_1_out13), .Q(R13), .clk(CLK), .clr(CLR));
  Register #(.width(16)) register_8 (.D(or_8_out), .en(demultiplexer_1_out15), .Q(R15), .clk(CLK), .clr(CLR));
  Register #(.width(16)) register_9 (.D(or_9_out), .en(demultiplexer_1_out17), .Q(R1_2), .clk(CLK), .clr(CLR));
  Register #(.width(16)) register_10 (.D(or_10_out), .en(demultiplexer_1_out19), .Q(R3_2), .clk(CLK), .clr(CLR));
  Register #(.width(16)) register_11 (.D(or_11_out), .en(demultiplexer_1_out21), .Q(R5_2), .clk(CLK), .clr(CLR));
  Register #(.width(16)) register_12 (.D(or_12_out), .en(demultiplexer_1_out23), .Q(R7_2), .clk(CLK), .clr(CLR));
  Register #(.width(16)) register_13 (.D(or_13_out), .en(demultiplexer_1_out25), .Q(R9_2), .clk(CLK), .clr(CLR));
  Register #(.width(16)) register_14 (.D(or_14_out), .en(demultiplexer_1_out27), .Q(R11_2), .clk(CLK), .clr(CLR));
  Register #(.width(16)) register_15 (.D(or_15_out), .en(demultiplexer_1_out29), .Q(R13_2), .clk(CLK), .clr(CLR));
  Register #(.width(16)) register_16 (.D(or_16_out), .en(demultiplexer_1_out31), .Q(R15_2), .clk(CLK), .clr(CLR));
  assign or_17_out = R0 | WRITE_DATA;  // OR_Gate or_17, 16 bits wide
  Register #(.width(16)) register_17 (.D(or_17_out), .en(demultiplexer_1_out0), .Q(R0), .clk(CLK), .clr(CLR));
  assign or_18_out = R2 | WRITE_DATA;  // OR_Gate or_18, 16 bits wide
  Register #(.width(16)) register_18 (.D(or_18_out), .en(demultiplexer_1_out2), .Q(R2), .clk(CLK), .clr(CLR));
  assign or_19_out = R4 | WRITE_DATA;  // OR_Gate or_19, 16 bits wide
  Register #(.width(16)) register_19 (.D(or_19_out), .en(demultiplexer_1_out4), .Q(R4), .clk(CLK), .clr(CLR));
  assign or_20_out = R6 | WRITE_DATA;  // OR_Gate or_20, 16 bits wide
  Register #(.width(16)) register_20 (.D(or_20_out), .en(demultiplexer_1_out6), .Q(R6), .clk(CLK), .clr(CLR));
  assign or_21_out = R8 | WRITE_DATA;  // OR_Gate or_21, 16 bits wide
  Register #(.width(16)) register_21 (.D(or_21_out), .en(demultiplexer_1_out8), .Q(R8), .clk(CLK), .clr(CLR));
  assign or_22_out = R10 | WRITE_DATA;  // OR_Gate or_22, 16 bits wide
  Register #(.width(16)) register_22 (.D(or_22_out), .en(demultiplexer_1_out10), .Q(R10), .clk(CLK), .clr(CLR));
  assign or_23_out = R12 | WRITE_DATA;  // OR_Gate or_23, 16 bits wide
  Register #(.width(16)) register_23 (.D(or_23_out), .en(demultiplexer_1_out12), .Q(R12), .clk(CLK), .clr(CLR));
  assign or_24_out = R14 | WRITE_DATA;  // OR_Gate or_24, 16 bits wide
  Register #(.width(16)) register_24 (.D(or_24_out), .en(demultiplexer_1_out14), .Q(R14), .clk(CLK), .clr(CLR));
  assign or_25_out = R0_2 | WRITE_DATA;  // OR_Gate or_25, 16 bits wide
  Register #(.width(16)) register_25 (.D(or_25_out), .en(demultiplexer_1_out16), .Q(R0_2), .clk(CLK), .clr(CLR));
  assign or_26_out = R2_2 | WRITE_DATA;  // OR_Gate or_26, 16 bits wide
  Register #(.width(16)) register_26 (.D(or_26_out), .en(demultiplexer_1_out18), .Q(R2_2), .clk(CLK), .clr(CLR));
  assign or_27_out = R4_2 | WRITE_DATA;  // OR_Gate or_27, 16 bits wide
  Register #(.width(16)) register_27 (.D(or_27_out), .en(demultiplexer_1_out20), .Q(R4_2), .clk(CLK), .clr(CLR));
  assign or_28_out = R6_2 | WRITE_DATA;  // OR_Gate or_28, 16 bits wide
  Register #(.width(16)) register_28 (.D(or_28_out), .en(demultiplexer_1_out22), .Q(R6_2), .clk(CLK), .clr(CLR));
  assign or_29_out = R8_2 | WRITE_DATA;  // OR_Gate or_29, 16 bits wide
  Register #(.width(16)) register_29 (.D(or_29_out), .en(demultiplexer_1_out24), .Q(R8_2), .clk(CLK), .clr(CLR));
  assign or_30_out = R10_2 | WRITE_DATA;  // OR_Gate or_30, 16 bits wide
  Register #(.width(16)) register_30 (.D(or_30_out), .en(demultiplexer_1_out26), .Q(R10_2), .clk(CLK), .clr(CLR));
  assign or_31_out = R12_2 | WRITE_DATA;  // OR_Gate or_31, 16 bits wide
  Register #(.width(16)) register_31 (.D(or_31_out), .en(demultiplexer_1_out28), .Q(R12_2), .clk(CLK), .clr(CLR));
  assign or_32_out = R14_2 | WRITE_DATA;  // OR_Gate or_32, 16 bits wide
  Register #(.width(16)) register_32 (.D(or_32_out), .en(demultiplexer_1_out30), .Q(R14_2), .clk(CLK), .clr(CLR));

  // Other names for the same wires on the sheet: WD[15:0] = WRITE_DATA; WRITE = FLUSH
endmodule

module _32_x_16b_OVERWRITE_REGISTER (
  input  CLK,
  input  CLR,
  input  FLUSH,
  input  [4:0] ADDR,
  input  [15:0] WRITE_DATA,
  output [15:0] R0,
  output [15:0] R1,
  output [15:0] R2,
  output [15:0] R3,
  output [15:0] R4,
  output [15:0] R5,
  output [15:0] R6,
  output [15:0] R7,
  output [15:0] R8,
  output [15:0] R9,
  output [15:0] R10,
  output [15:0] R11,
  output [15:0] R12,
  output [15:0] R13,
  output [15:0] R14,
  output [15:0] R15,
  output [15:0] R0_2,
  output [15:0] R1_2,
  output [15:0] R2_2,
  output [15:0] R3_2,
  output [15:0] R4_2,
  output [15:0] R5_2,
  output [15:0] R6_2,
  output [15:0] R7_2,
  output [15:0] R8_2,
  output [15:0] R9_2,
  output [15:0] R10_2,
  output [15:0] R11_2,
  output [15:0] R12_2,
  output [15:0] R13_2,
  output [15:0] R14_2,
  output [15:0] R15_2
);

  wire demultiplexer_1_out0, demultiplexer_1_out1, demultiplexer_1_out2, demultiplexer_1_out3,
       demultiplexer_1_out4, demultiplexer_1_out5, demultiplexer_1_out6, demultiplexer_1_out7,
       demultiplexer_1_out8, demultiplexer_1_out9, demultiplexer_1_out10, demultiplexer_1_out11,
       demultiplexer_1_out12, demultiplexer_1_out13, demultiplexer_1_out14, demultiplexer_1_out15,
       demultiplexer_1_out16, demultiplexer_1_out17, demultiplexer_1_out18, demultiplexer_1_out19,
       demultiplexer_1_out20, demultiplexer_1_out21, demultiplexer_1_out22, demultiplexer_1_out23,
       demultiplexer_1_out24, demultiplexer_1_out25, demultiplexer_1_out26, demultiplexer_1_out27,
       demultiplexer_1_out28, demultiplexer_1_out29, demultiplexer_1_out30, demultiplexer_1_out31;

  Demultiplexer #(.select(5), .enable("false")) demultiplexer_1 (
    .out0(demultiplexer_1_out0), .out1(demultiplexer_1_out1), .out2(demultiplexer_1_out2),
    .out3(demultiplexer_1_out3), .out4(demultiplexer_1_out4), .out5(demultiplexer_1_out5),
    .out6(demultiplexer_1_out6), .out7(demultiplexer_1_out7), .out8(demultiplexer_1_out8),
    .out9(demultiplexer_1_out9), .out10(demultiplexer_1_out10), .out11(demultiplexer_1_out11),
    .out12(demultiplexer_1_out12), .out13(demultiplexer_1_out13), .out14(demultiplexer_1_out14),
    .out15(demultiplexer_1_out15), .out16(demultiplexer_1_out16), .out17(demultiplexer_1_out17),
    .out18(demultiplexer_1_out18), .out19(demultiplexer_1_out19), .out20(demultiplexer_1_out20),
    .out21(demultiplexer_1_out21), .out22(demultiplexer_1_out22), .out23(demultiplexer_1_out23),
    .out24(demultiplexer_1_out24), .out25(demultiplexer_1_out25), .out26(demultiplexer_1_out26),
    .out27(demultiplexer_1_out27), .out28(demultiplexer_1_out28), .out29(demultiplexer_1_out29),
    .out30(demultiplexer_1_out30), .out31(demultiplexer_1_out31), .in(FLUSH), .sel(ADDR));
  Register #(.width(16)) register_1 (.D(WRITE_DATA), .en(demultiplexer_1_out1), .Q(R1), .clk(CLK), .clr(CLR));
  Register #(.width(16)) register_2 (.D(WRITE_DATA), .en(demultiplexer_1_out3), .Q(R3), .clk(CLK), .clr(CLR));
  Register #(.width(16)) register_3 (.D(WRITE_DATA), .en(demultiplexer_1_out5), .Q(R5), .clk(CLK), .clr(CLR));
  Register #(.width(16)) register_4 (.D(WRITE_DATA), .en(demultiplexer_1_out7), .Q(R7), .clk(CLK), .clr(CLR));
  Register #(.width(16)) register_5 (.D(WRITE_DATA), .en(demultiplexer_1_out9), .Q(R9), .clk(CLK), .clr(CLR));
  Register #(.width(16)) register_6 (.D(WRITE_DATA), .en(demultiplexer_1_out11), .Q(R11), .clk(CLK), .clr(CLR));
  Register #(.width(16)) register_7 (.D(WRITE_DATA), .en(demultiplexer_1_out13), .Q(R13), .clk(CLK), .clr(CLR));
  Register #(.width(16)) register_8 (.D(WRITE_DATA), .en(demultiplexer_1_out15), .Q(R15), .clk(CLK), .clr(CLR));
  Register #(.width(16)) register_9 (.D(WRITE_DATA), .en(demultiplexer_1_out17), .Q(R1_2), .clk(CLK), .clr(CLR));
  Register #(.width(16)) register_10 (.D(WRITE_DATA), .en(demultiplexer_1_out19), .Q(R3_2), .clk(CLK), .clr(CLR));
  Register #(.width(16)) register_11 (.D(WRITE_DATA), .en(demultiplexer_1_out21), .Q(R5_2), .clk(CLK), .clr(CLR));
  Register #(.width(16)) register_12 (.D(WRITE_DATA), .en(demultiplexer_1_out23), .Q(R7_2), .clk(CLK), .clr(CLR));
  Register #(.width(16)) register_13 (.D(WRITE_DATA), .en(demultiplexer_1_out25), .Q(R9_2), .clk(CLK), .clr(CLR));
  Register #(.width(16)) register_14 (.D(WRITE_DATA), .en(demultiplexer_1_out27), .Q(R11_2), .clk(CLK), .clr(CLR));
  Register #(.width(16)) register_15 (.D(WRITE_DATA), .en(demultiplexer_1_out29), .Q(R13_2), .clk(CLK), .clr(CLR));
  Register #(.width(16)) register_16 (.D(WRITE_DATA), .en(demultiplexer_1_out31), .Q(R15_2), .clk(CLK), .clr(CLR));
  Register #(.width(16)) register_17 (.D(WRITE_DATA), .en(demultiplexer_1_out0), .Q(R0), .clk(CLK), .clr(CLR));
  Register #(.width(16)) register_18 (.D(WRITE_DATA), .en(demultiplexer_1_out2), .Q(R2), .clk(CLK), .clr(CLR));
  Register #(.width(16)) register_19 (.D(WRITE_DATA), .en(demultiplexer_1_out4), .Q(R4), .clk(CLK), .clr(CLR));
  Register #(.width(16)) register_20 (.D(WRITE_DATA), .en(demultiplexer_1_out6), .Q(R6), .clk(CLK), .clr(CLR));
  Register #(.width(16)) register_21 (.D(WRITE_DATA), .en(demultiplexer_1_out8), .Q(R8), .clk(CLK), .clr(CLR));
  Register #(.width(16)) register_22 (.D(WRITE_DATA), .en(demultiplexer_1_out10), .Q(R10), .clk(CLK), .clr(CLR));
  Register #(.width(16)) register_23 (.D(WRITE_DATA), .en(demultiplexer_1_out12), .Q(R12), .clk(CLK), .clr(CLR));
  Register #(.width(16)) register_24 (.D(WRITE_DATA), .en(demultiplexer_1_out14), .Q(R14), .clk(CLK), .clr(CLR));
  Register #(.width(16)) register_25 (.D(WRITE_DATA), .en(demultiplexer_1_out16), .Q(R0_2), .clk(CLK), .clr(CLR));
  Register #(.width(16)) register_26 (.D(WRITE_DATA), .en(demultiplexer_1_out18), .Q(R2_2), .clk(CLK), .clr(CLR));
  Register #(.width(16)) register_27 (.D(WRITE_DATA), .en(demultiplexer_1_out20), .Q(R4_2), .clk(CLK), .clr(CLR));
  Register #(.width(16)) register_28 (.D(WRITE_DATA), .en(demultiplexer_1_out22), .Q(R6_2), .clk(CLK), .clr(CLR));
  Register #(.width(16)) register_29 (.D(WRITE_DATA), .en(demultiplexer_1_out24), .Q(R8_2), .clk(CLK), .clr(CLR));
  Register #(.width(16)) register_30 (.D(WRITE_DATA), .en(demultiplexer_1_out26), .Q(R10_2), .clk(CLK), .clr(CLR));
  Register #(.width(16)) register_31 (.D(WRITE_DATA), .en(demultiplexer_1_out28), .Q(R12_2), .clk(CLK), .clr(CLR));
  Register #(.width(16)) register_32 (.D(WRITE_DATA), .en(demultiplexer_1_out30), .Q(R14_2), .clk(CLK), .clr(CLR));

  // Other names for the same wires on the sheet: WD[15:0] = WRITE_DATA; WRITE = FLUSH
endmodule

module _32_x_16b_BUFFER (
  input  CLK,
  input  CLR,
  input  FLUSH,
  input  [15:0] R0,
  input  [15:0] R1,
  input  [15:0] R2,
  input  [15:0] R3,
  input  [15:0] R4,
  input  [15:0] R5,
  input  [15:0] R6,
  input  [15:0] R7,
  input  [15:0] R8,
  input  [15:0] R9,
  input  [15:0] R10,
  input  [15:0] R11,
  input  [15:0] R12,
  input  [15:0] R13,
  input  [15:0] R14,
  input  [15:0] R15,
  input  [15:0] R0_2,
  input  [15:0] R1_2,
  input  [15:0] R2_2,
  input  [15:0] R3_2,
  input  [15:0] R4_2,
  input  [15:0] R5_2,
  input  [15:0] R6_2,
  input  [15:0] R7_2,
  input  [15:0] R8_2,
  input  [15:0] R9_2,
  input  [15:0] R10_2,
  input  [15:0] R11_2,
  input  [15:0] R12_2,
  input  [15:0] R13_2,
  input  [15:0] R14_2,
  input  [15:0] R15_2,
  output [15:0] R0_3,
  output [15:0] R1_3,
  output [15:0] R2_3,
  output [15:0] R3_3,
  output [15:0] R4_3,
  output [15:0] R5_3,
  output [15:0] R6_3,
  output [15:0] R7_3,
  output [15:0] R8_3,
  output [15:0] R9_3,
  output [15:0] R10_3,
  output [15:0] R11_3,
  output [15:0] R12_3,
  output [15:0] R13_3,
  output [15:0] R14_3,
  output [15:0] R15_3,
  output [15:0] R0_4,
  output [15:0] R1_4,
  output [15:0] R2_4,
  output [15:0] R3_4,
  output [15:0] R4_4,
  output [15:0] R5_4,
  output [15:0] R6_4,
  output [15:0] R7_4,
  output [15:0] R8_4,
  output [15:0] R9_4,
  output [15:0] R10_4,
  output [15:0] R11_4,
  output [15:0] R12_4,
  output [15:0] R13_4,
  output [15:0] R14_4,
  output [15:0] R15_4
);

  Register #(.width(16)) register_1 (.D(R1), .en(FLUSH), .Q(R1_3), .clk(CLK), .clr(CLR));
  Register #(.width(16)) register_2 (.D(R3), .en(FLUSH), .Q(R3_3), .clk(CLK), .clr(CLR));
  Register #(.width(16)) register_3 (.D(R5), .en(FLUSH), .Q(R5_3), .clk(CLK), .clr(CLR));
  Register #(.width(16)) register_4 (.D(R7), .en(FLUSH), .Q(R7_3), .clk(CLK), .clr(CLR));
  Register #(.width(16)) register_5 (.D(R9), .en(FLUSH), .Q(R9_3), .clk(CLK), .clr(CLR));
  Register #(.width(16)) register_6 (.D(R11), .en(FLUSH), .Q(R11_3), .clk(CLK), .clr(CLR));
  Register #(.width(16)) register_7 (.D(R13), .en(FLUSH), .Q(R13_3), .clk(CLK), .clr(CLR));
  Register #(.width(16)) register_8 (.D(R15), .en(FLUSH), .Q(R15_3), .clk(CLK), .clr(CLR));
  Register #(.width(16)) register_9 (.D(R1_2), .en(FLUSH), .Q(R1_4), .clk(CLK), .clr(CLR));
  Register #(.width(16)) register_10 (.D(R3_2), .en(FLUSH), .Q(R3_4), .clk(CLK), .clr(CLR));
  Register #(.width(16)) register_11 (.D(R5_2), .en(FLUSH), .Q(R5_4), .clk(CLK), .clr(CLR));
  Register #(.width(16)) register_12 (.D(R7_2), .en(FLUSH), .Q(R7_4), .clk(CLK), .clr(CLR));
  Register #(.width(16)) register_13 (.D(R9_2), .en(FLUSH), .Q(R9_4), .clk(CLK), .clr(CLR));
  Register #(.width(16)) register_14 (.D(R11_2), .en(FLUSH), .Q(R11_4), .clk(CLK), .clr(CLR));
  Register #(.width(16)) register_15 (.D(R13_2), .en(FLUSH), .Q(R13_4), .clk(CLK), .clr(CLR));
  Register #(.width(16)) register_16 (.D(R15_2), .en(FLUSH), .Q(R15_4), .clk(CLK), .clr(CLR));
  Register #(.width(16)) register_17 (.D(R0), .en(FLUSH), .Q(R0_3), .clk(CLK), .clr(CLR));
  Register #(.width(16)) register_18 (.D(R2), .en(FLUSH), .Q(R2_3), .clk(CLK), .clr(CLR));
  Register #(.width(16)) register_19 (.D(R4), .en(FLUSH), .Q(R4_3), .clk(CLK), .clr(CLR));
  Register #(.width(16)) register_20 (.D(R6), .en(FLUSH), .Q(R6_3), .clk(CLK), .clr(CLR));
  Register #(.width(16)) register_21 (.D(R8), .en(FLUSH), .Q(R8_3), .clk(CLK), .clr(CLR));
  Register #(.width(16)) register_22 (.D(R10), .en(FLUSH), .Q(R10_3), .clk(CLK), .clr(CLR));
  Register #(.width(16)) register_23 (.D(R12), .en(FLUSH), .Q(R12_3), .clk(CLK), .clr(CLR));
  Register #(.width(16)) register_24 (.D(R14), .en(FLUSH), .Q(R14_3), .clk(CLK), .clr(CLR));
  Register #(.width(16)) register_25 (.D(R0_2), .en(FLUSH), .Q(R0_4), .clk(CLK), .clr(CLR));
  Register #(.width(16)) register_26 (.D(R2_2), .en(FLUSH), .Q(R2_4), .clk(CLK), .clr(CLR));
  Register #(.width(16)) register_27 (.D(R4_2), .en(FLUSH), .Q(R4_4), .clk(CLK), .clr(CLR));
  Register #(.width(16)) register_28 (.D(R6_2), .en(FLUSH), .Q(R6_4), .clk(CLK), .clr(CLR));
  Register #(.width(16)) register_29 (.D(R8_2), .en(FLUSH), .Q(R8_4), .clk(CLK), .clr(CLR));
  Register #(.width(16)) register_30 (.D(R10_2), .en(FLUSH), .Q(R10_4), .clk(CLK), .clr(CLR));
  Register #(.width(16)) register_31 (.D(R12_2), .en(FLUSH), .Q(R12_4), .clk(CLK), .clr(CLR));
  Register #(.width(16)) register_32 (.D(R14_2), .en(FLUSH), .Q(R14_4), .clk(CLK), .clr(CLR));

  // Other names for the same wires on the sheet: WRITE = FLUSH
endmodule

module Random_Number_Generator (
  input  CLK,
  input  Enable,
  output [7:0] Random
);

  wire [7:0] random_1_out;

  Random #(.seed(235423)) random_1 (.clk(CLK), .next(CLK), .out(random_1_out));  // open: clr
  Multiplexer #(.width(8), .enable("false")) multiplexer_1 (
    .in0({8{1'b0}}), .in1(random_1_out), .out(Random), .sel(Enable));
endmodule

module _7_Segment_Adapter (
  input  [7:0] in_1,
  output UU,
  output LU,
  output RU,
  output M,
  output LD,
  output RD,
  output DD,
  output UU_2,
  output LU_2,
  output RU_2,
  output M_2,
  output LD_2,
  output RD_2,
  output DD_2
);

  wire demultiplexer_1_out0, demultiplexer_1_out1, demultiplexer_1_out2, demultiplexer_1_out3,
       demultiplexer_1_out4, demultiplexer_1_out5, demultiplexer_1_out6, demultiplexer_1_out7,
       demultiplexer_1_out8, demultiplexer_1_out9, demultiplexer_1_out10, demultiplexer_1_out11,
       demultiplexer_1_out12, demultiplexer_1_out13, demultiplexer_1_out14, demultiplexer_1_out15,
       demultiplexer_1_out16, demultiplexer_1_out17, demultiplexer_1_out18, demultiplexer_1_out19,
       demultiplexer_1_out20, demultiplexer_1_out21, demultiplexer_1_out22, demultiplexer_1_out23,
       demultiplexer_1_out24, demultiplexer_1_out25, demultiplexer_1_out26, demultiplexer_1_out27,
       demultiplexer_1_out28, demultiplexer_1_out29, demultiplexer_1_out30, demultiplexer_1_out31, T0, T1,
       T2, T3, U0, U1, U2, U3, U4, U5, U6, U7, U8, U9;
  wire [4:0] bit_extender_1_out;

  Demultiplexer #(.select(5), .enable("false")) demultiplexer_1 (
    .out0(demultiplexer_1_out0), .out1(demultiplexer_1_out1), .out2(demultiplexer_1_out2),
    .out3(demultiplexer_1_out3), .out4(demultiplexer_1_out4), .out5(demultiplexer_1_out5),
    .out6(demultiplexer_1_out6), .out7(demultiplexer_1_out7), .out8(demultiplexer_1_out8),
    .out9(demultiplexer_1_out9), .out10(demultiplexer_1_out10), .out11(demultiplexer_1_out11),
    .out12(demultiplexer_1_out12), .out13(demultiplexer_1_out13), .out14(demultiplexer_1_out14),
    .out15(demultiplexer_1_out15), .out16(demultiplexer_1_out16), .out17(demultiplexer_1_out17),
    .out18(demultiplexer_1_out18), .out19(demultiplexer_1_out19), .out20(demultiplexer_1_out20),
    .out21(demultiplexer_1_out21), .out22(demultiplexer_1_out22), .out23(demultiplexer_1_out23),
    .out24(demultiplexer_1_out24), .out25(demultiplexer_1_out25), .out26(demultiplexer_1_out26),
    .out27(demultiplexer_1_out27), .out28(demultiplexer_1_out28), .out29(demultiplexer_1_out29),
    .out30(demultiplexer_1_out30), .out31(demultiplexer_1_out31), .in(1'b1), .sel(bit_extender_1_out));
  Bit_Extender #(.out_width(5)) bit_extender_1 (.in(in_1), .out(bit_extender_1_out));
  or or_1 (T0, demultiplexer_1_out0, demultiplexer_1_out1, demultiplexer_1_out2, demultiplexer_1_out3, demultiplexer_1_out4, demultiplexer_1_out5, demultiplexer_1_out6, demultiplexer_1_out7, demultiplexer_1_out8, demultiplexer_1_out9);
  or or_2 (T1, demultiplexer_1_out10, demultiplexer_1_out11, demultiplexer_1_out12, demultiplexer_1_out13, demultiplexer_1_out14, demultiplexer_1_out15, demultiplexer_1_out16, demultiplexer_1_out17, demultiplexer_1_out18, demultiplexer_1_out19);
  or or_3 (U0, demultiplexer_1_out0, demultiplexer_1_out10, demultiplexer_1_out20, demultiplexer_1_out30);
  or or_4 (T2, demultiplexer_1_out20, demultiplexer_1_out21, demultiplexer_1_out22, demultiplexer_1_out23, demultiplexer_1_out24, demultiplexer_1_out25, demultiplexer_1_out26, demultiplexer_1_out27, demultiplexer_1_out28, demultiplexer_1_out29);
  or or_5 (U1, demultiplexer_1_out1, demultiplexer_1_out11, demultiplexer_1_out21, demultiplexer_1_out31);
  or or_6 (U2, demultiplexer_1_out2, demultiplexer_1_out12, demultiplexer_1_out22);
  or or_7 (U3, demultiplexer_1_out3, demultiplexer_1_out13, demultiplexer_1_out23);
  or or_8 (T3, demultiplexer_1_out30, demultiplexer_1_out31);
  or or_9 (U5, demultiplexer_1_out5, demultiplexer_1_out15, demultiplexer_1_out25);
  or or_10 (U4, demultiplexer_1_out4, demultiplexer_1_out14, demultiplexer_1_out24);
  or or_11 (U6, demultiplexer_1_out6, demultiplexer_1_out16, demultiplexer_1_out26);
  or or_12 (U8, demultiplexer_1_out8, demultiplexer_1_out18, demultiplexer_1_out28);
  or or_13 (U7, demultiplexer_1_out7, demultiplexer_1_out17, demultiplexer_1_out27);
  or or_14 (U9, demultiplexer_1_out9, demultiplexer_1_out19, demultiplexer_1_out29);
  or or_15 (UU, U0, U2, U3, U5, U6, U7, U8, U9);
  or or_16 (LU, U0, U4, U5, U6, U8, U9);
  or or_17 (RU, U0, U1, U2, U3, U4, 1'b0, U7, U8, U9);
  or or_18 (M, U2, U3, U4, U5, U6, U8, U9);
  or or_19 (LD, U2, U0, U6, U8);
  or or_20 (RD, U0, U1, U3, U4, U5, U6, U7, U8, U9);
  or or_21 (DD, U0, U2, U3, U5, U6, U8, U9);
  or or_22 (UU_2, T0, T2, T3, 1'b0, 1'b0, 1'b0, 1'b0, 1'b0);
  or or_23 (LU_2, T0, 1'b0, 1'b0, 1'b0, 1'b0, 1'b0);
  or or_24 (RU_2, T0, T1, T2, T3, 1'b0, 1'b0, 1'b0, 1'b0, 1'b0);
  or or_25 (M_2, T2, T3, 1'b0, 1'b0, 1'b0, 1'b0, 1'b0);
  or or_26 (LD_2, T2, T0, 1'b0, 1'b0);
  or or_27 (RD_2, T0, T1, T3, 1'b0, 1'b0, 1'b0, 1'b0, 1'b0, 1'b0);
  or or_28 (DD_2, T0, T2, T3, 1'b0, 1'b0, 1'b0, 1'b0);
endmodule

module _7_Segment_TEST (
  input  [7:0] in_1
);

  wire A, B, C, D, E, F, G, H, I, J, K, L, M, N;

  _7_Segment_Display u_7_segment_display_1 (.g(D), .f(A), .a(B), .b(C), .e(E), .d(F), .c(G), .dp(1'b0));
  _7_Segment_Display u_7_segment_display_2 (.g(K), .f(H), .a(I), .b(J), .e(L), .d(M), .c(N), .dp(1'b0));
  _7_Segment_Adapter u_7_segment_adapter_1 (
    .in_1(in_1), .UU(I), .UU_2(B), .LU(H), .LU_2(A), .RU(J), .RU_2(C), .M(K), .M_2(D), .LD_2(E), .RD(N),
    .RD_2(G), .DD(M), .DD_2(F), .LD(L));
endmodule

module Binary_to_BCD (
  input  [7:0] Binary,
  input  WRITE,
  input  Signed,
  input  CLK,
  input  CLR,
  output [3:0] Ones,
  output [3:0] Tens,
  output [3:0] Hundreds,
  output Sign_Bit
);

  wire [7:0] double_dabble_unit_8_output, multiplexer_1_out, register_1_q, subtractor_1_out;
  wire [19:0] double_dabble_unit_1_output, double_dabble_unit_2_output, double_dabble_unit_3_output,
       double_dabble_unit_4_output, double_dabble_unit_5_output, double_dabble_unit_6_output,
       double_dabble_unit_7_output;

  Register register_1 (.D(Binary), .en(WRITE), .Q(register_1_q), .clk(CLK), .clr(CLR));
  Multiplexer #(.width(8), .enable("false")) multiplexer_1 (
    .in0(register_1_q), .in1(subtractor_1_out), .out(multiplexer_1_out), .sel(Sign_Bit));
  Subtractor subtractor_1 (.a({8{1'b0}}), .b(register_1_q), .out(subtractor_1_out));  // open: bin, bout
  and and_1 (Sign_Bit, register_1_q[7], Signed);
  Double_Dabble_Unit double_dabble_unit_1 (
    .Input({{12{1'b0}}, multiplexer_1_out}), .Output(double_dabble_unit_1_output));
  Double_Dabble_Unit double_dabble_unit_2 (.Input(double_dabble_unit_1_output), .Output(double_dabble_unit_2_output));
  Double_Dabble_Unit double_dabble_unit_3 (.Input(double_dabble_unit_2_output), .Output(double_dabble_unit_3_output));
  Double_Dabble_Unit double_dabble_unit_4 (.Input(double_dabble_unit_3_output), .Output(double_dabble_unit_4_output));
  Double_Dabble_Unit double_dabble_unit_5 (.Input(double_dabble_unit_4_output), .Output(double_dabble_unit_5_output));
  Double_Dabble_Unit double_dabble_unit_6 (.Input(double_dabble_unit_5_output), .Output(double_dabble_unit_6_output));
  Double_Dabble_Unit double_dabble_unit_7 (.Input(double_dabble_unit_6_output), .Output(double_dabble_unit_7_output));
  Double_Dabble_Unit double_dabble_unit_8 (
    .Input(double_dabble_unit_7_output), .Output({Hundreds, Tens, Ones, double_dabble_unit_8_output}));
  // Probe on Binary
  // Probe on Ones
  // Probe on Tens
  // Probe on Hundreds

  // Other names for the same wires on the sheet: IS_SIGNED = Signed

  // Notes on the sheet:
  //   Convert to twos complement and set sign bit if signed number and a negative number
  //   Scratch Space
  //   DOUBLE DABBLE ALGORITHM TO CONVERT BINARY TO BCD
endmodule

module Double_Dabble_Unit (
  input  [19:0] Input,
  output [19:0] Output
);

  wire adder_1_cout, adder_2_cout, adder_3_cout, comparator_1_eq, comparator_1_gt, comparator_2_eq,
       comparator_2_gt, comparator_3_eq, comparator_3_gt, or_1_out, or_2_out, or_3_out;
  wire [3:0] adder_1_out, adder_2_out, adder_3_out, multiplexer_1_out, multiplexer_2_out, multiplexer_3_out;

  Comparator #(.width(4), .mode("unsigned")) comparator_1 (
    .a(Input[11:8]), .b(4'b0101), .gt(comparator_1_gt), .eq(comparator_1_eq));  // open: lt
  Comparator #(.width(4), .mode("unsigned")) comparator_2 (
    .a(Input[15:12]), .b(4'b0101), .gt(comparator_2_gt), .eq(comparator_2_eq));  // open: lt
  Comparator #(.width(4), .mode("unsigned")) comparator_3 (
    .a(Input[19:16]), .b(4'b0101), .gt(comparator_3_gt), .eq(comparator_3_eq));  // open: lt
  or or_1 (or_1_out, comparator_1_gt, comparator_1_eq);
  or or_2 (or_2_out, comparator_2_gt, comparator_2_eq);
  or or_3 (or_3_out, comparator_3_gt, comparator_3_eq);
  Multiplexer #(.width(4), .enable("false")) multiplexer_1 (
    .in0(4'b0000), .in1(4'b0011), .out(multiplexer_1_out), .sel(or_1_out));
  Multiplexer #(.width(4), .enable("false")) multiplexer_2 (
    .in0(4'b0000), .in1(4'b0011), .out(multiplexer_2_out), .sel(or_2_out));
  Multiplexer #(.width(4), .enable("false")) multiplexer_3 (
    .in0(4'b0000), .in1(4'b0011), .out(multiplexer_3_out), .sel(or_3_out));
  Adder #(.width(4)) adder_1 (
    .a(Input[11:8]), .b(multiplexer_1_out), .out(adder_1_out), .cin(1'b0), .cout(adder_1_cout));
  Adder #(.width(4)) adder_2 (
    .a(Input[15:12]), .b(multiplexer_2_out), .out(adder_2_out), .cin(1'b0), .cout(adder_2_cout));
  Adder #(.width(4)) adder_3 (
    .a(Input[19:16]), .b(multiplexer_3_out), .out(adder_3_out), .cin(1'b0), .cout(adder_3_cout));
  Shifter #(.width(20)) shifter_1 (
    .in({adder_3_out, adder_2_out, adder_1_out, Input[7:0]}), .\dist (5'b00001), .out(Output));
  // also tied to GND on the sheet: {adder_1_cout, adder_2_cout, adder_3_cout}
endmodule

module BCD_to_7_Segment_Display (
  input  [3:0] BCD,
  output M,
  output LU,
  output UU,
  output RU,
  output LD,
  output DD,
  output RD
);

  wire demultiplexer_1_out0, demultiplexer_1_out1, demultiplexer_1_out2, demultiplexer_1_out3,
       demultiplexer_1_out4, demultiplexer_1_out5, demultiplexer_1_out6, demultiplexer_1_out7,
       demultiplexer_1_out8, demultiplexer_1_out9;

  Demultiplexer #(.select(4), .enable("false")) demultiplexer_1 (
    .out0(demultiplexer_1_out0), .out1(demultiplexer_1_out1), .out2(demultiplexer_1_out2),
    .out3(demultiplexer_1_out3), .out4(demultiplexer_1_out4), .out5(demultiplexer_1_out5),
    .out6(demultiplexer_1_out6), .out7(demultiplexer_1_out7), .out8(demultiplexer_1_out8),
    .out9(demultiplexer_1_out9), .in(1'b1), .sel(BCD));  // open: out10, out11, out12, out13, out14, out15
  or or_1 (M, demultiplexer_1_out2, demultiplexer_1_out3, demultiplexer_1_out4, demultiplexer_1_out5, demultiplexer_1_out6, demultiplexer_1_out8, demultiplexer_1_out9);
  or or_2 (LU, demultiplexer_1_out0, demultiplexer_1_out4, demultiplexer_1_out5, demultiplexer_1_out6, demultiplexer_1_out8, demultiplexer_1_out9);
  or or_3 (UU, demultiplexer_1_out0, demultiplexer_1_out2, demultiplexer_1_out3, demultiplexer_1_out5, demultiplexer_1_out6, demultiplexer_1_out7, demultiplexer_1_out8, demultiplexer_1_out9);
  or or_4 (RU, demultiplexer_1_out0, demultiplexer_1_out1, demultiplexer_1_out2, demultiplexer_1_out3, demultiplexer_1_out4, 1'b0, demultiplexer_1_out7, demultiplexer_1_out8, demultiplexer_1_out9);
  or or_5 (LD, demultiplexer_1_out2, demultiplexer_1_out0, demultiplexer_1_out6, demultiplexer_1_out8);
  or or_6 (DD, demultiplexer_1_out0, demultiplexer_1_out2, demultiplexer_1_out3, demultiplexer_1_out5, demultiplexer_1_out6, demultiplexer_1_out8, demultiplexer_1_out9);
  or or_7 (RD, demultiplexer_1_out0, demultiplexer_1_out1, demultiplexer_1_out3, demultiplexer_1_out4, demultiplexer_1_out5, demultiplexer_1_out6, demultiplexer_1_out7, demultiplexer_1_out8, demultiplexer_1_out9);
endmodule
